# Fritzing sketch Arduino単独システム例 (saved by Fritzing 0.9.2b)
perfboards: 12

parts:
  VCC1 = Battery block 9V  # not connected
  Grove4 = Grove 3 Axis Digital Accelerometer 16g  # not connected
  Grove5 = Grove Infrared Emitter  # not connected
  Grove6 = Grove 3 Axis Digital Accelerometer 16g  # not connected
  J146 = male pin header, 3 pins [form="♂ (male)"]
  J147 = male pin header, 3 pins [form="♂ (male)"]
  J148 = male pin header, 3 pins [form="♂ (male)"]
  S10 = Akizuki slide switch IS-2235
  microSD4 = MicroSD Breakout
  Card_detect3 = male pin header, 12 pins [form="♂ (male)"]
  J149 = male pin header, 12 pins [form="♂ (male)"]
  Chip_select3 = male pin header, 12 pins [form="♂ (male)"]
  J150 = male pin header, 12 pins [form="♂ (male)"]
  ICSP1 = Arduino R3 6pin male header [package=THT]
  IOH14 = female pin header, 10 pins [form="♀ (female)"]
  IOL14 = female pin header, 8 pins [form="♀ (female)"]
  POWER3 = female pin header, 8 pins [form="♀ (female)"]
  AD14 = female pin header, 6 pins [form="♀ (female)"]  # not connected
  SCL3 = male pin header, 3 pins [form="♂ (male)"]
  SCL4 = male pin header, 3 pins [form="♂ (male)"]
  SDA3 = male pin header, 3 pins [form="♂ (male)"]
  SDA4 = male pin header, 3 pins [form="♂ (male)"]
  RTC6 = RTC-8564NB [package="Module(DIP 8P)"]
  SW1 = Akizuki slide switch IS-1250
  ICSP2 = Arduino R3 6pin male header [package=THT]  # not connected
  D14 = Schottky Diode [part_number=1N5817 package="300 mil [THT]"]
  D15 = Schottky Diode [part_number=1N5817 package="300 mil [THT]"]
  IOH15 = female pin header, 10 pins [form="♀ (female)"]
  INT8 = male pin header, 15 pins [form="♂ (male)"]
  J151 = male pin header, 15 pins [form="♂ (male)"]
  IOL15 = female pin header, 8 pins [form="♀ (female)"]
  Power12 = female pin header, 8 pins [form="♀ (female)"]
  AD15 = female pin header, 6 pins [form="♀ (female)"]
  BAT6 = Battery Holders [package=battcom_20mm_pth]
  J152 = male pin header, 6 pins [form="♂ (male)"]
  J153 = male pin header, 13 pins [form="♂ (male)"]
  RSSI3 = male pin header, 13 pins [form="♂ (male)"]
  Xbee6 = SSCI-KIT-XBSOCKET
  ICSP3 = Arduino R3 6pin male header [package=THT]  # not connected
  IOH16 = female pin header, 10 pins [form="♀ (female)"]
  J154 = male pin header, 13 pins [form="♂ (male)"]
  J155 = male pin header, 13 pins [form="♂ (male)"]
  J156 = male pin header, 13 pins [form="♂ (male)"]
  J157 = male pin header, 13 pins [form="♂ (male)"]
  ON/Sleep7 = male pin header, 15 pins [form="♂ (male)"]
  Reset4 = male pin header, 13 pins [form="♂ (male)"]
  Associate3 = male pin header, 13 pins [form="♂ (male)"]
  Sleep_RQ3 = male pin header, 13 pins [form="♂ (male)"]
  Rx7 = male pin header, 15 pins [form="♂ (male)"]
  J158 = male pin header, 15 pins [form="♂ (male)"]
  Tx7 = male pin header, 15 pins [form="♂ (male)"]
  J159 = male pin header, 15 pins [form="♂ (male)"]
  IOL16 = female pin header, 8 pins [form="♀ (female)"]
  Power13 = female pin header, 8 pins [form="♀ (female)"]
  AD16 = female pin header, 6 pins [form="♀ (female)"]
  GR-kurumi1 = GR kurumi (Renesas Gadget) no serial
  AE-LXDC55-3_3V1 = AE-LXDC55-3.3V-Down
  R2 = Resistor [tolerance=±5% resistance=10k package=THT]
  D16 = Rectifier Diode [part_number=1N4001 package="300 mil [THT]"]
  Power_plug7 = Power plug
  ICSP4 = Arduino R3 6pin male header [package=THT]  # not connected
  Reset5 = Momentary Switch [package=ksa_sealed_tac_switch]
  IOH17 = female pin header, 10 pins [form="♀ (female)"]
  Power14 = female pin header, 8 pins [form="♀ (female)"]
  IOL17 = female pin header, 8 pins [form="♀ (female)"]
  AD17 = female pin header, 6 pins [form="♀ (female)"]
  Reset1 = Momentary Switch [package=ksa_sealed_tac_switch]
  IOL2 = female pin header, 8 pins [form="♀ (female)"]
  Power2 = female pin header, 8 pins [form="♀ (female)"]
  Power_plug6 = Power plug
  J97 = Arduino R3 6pin male header [package=THT]  # not connected
  AD2 = female pin header, 6 pins [form="♀ (female)"]
  Pro_Mini_3V3_8MHz1 = Arduino Pro Mini v13
  IOH2 = female pin header, 10 pins [form="♀ (female)"]
  S2 = Akizuki slide switch IS-1250
  VCC2 = Battery block 9V  # not connected
  J160 = male pin header, 6 pins [form="♂ (male)"]
  J161 = male pin header, 3 pins [form="♂ (male)"]
  J162 = male pin header, 13 pins [form="♂ (male)"]
  J163 = male pin header, 3 pins [form="♂ (male)"]
  RSSI4 = male pin header, 13 pins [form="♂ (male)"]
  J164 = male pin header, 3 pins [form="♂ (male)"]
  S11 = Akizuki slide switch IS-2235
  microSD5 = MicroSD Breakout
  Card_detect4 = male pin header, 12 pins [form="♂ (male)"]
  J165 = male pin header, 12 pins [form="♂ (male)"]
  Chip_select4 = male pin header, 12 pins [form="♂ (male)"]
  J166 = male pin header, 12 pins [form="♂ (male)"]
  ICSP6 = Arduino R3 6pin male header [package=THT]
  IOH19 = female pin header, 10 pins [form="♀ (female)"]
  IOL19 = female pin header, 8 pins [form="♀ (female)"]
  POWER4 = female pin header, 8 pins [form="♀ (female)"]
  AD19 = female pin header, 6 pins [form="♀ (female)"]  # not connected
  Xbee7 = SSCI-KIT-XBSOCKET
  ICSP7 = Arduino R3 6pin male header [package=THT]  # not connected
  IOH20 = female pin header, 10 pins [form="♀ (female)"]
  J168 = male pin header, 13 pins [form="♂ (male)"]
  J169 = male pin header, 13 pins [form="♂ (male)"]
  J170 = male pin header, 13 pins [form="♂ (male)"]
  J171 = male pin header, 13 pins [form="♂ (male)"]
  ON/Sleep8 = male pin header, 15 pins [form="♂ (male)"]
  Reset6 = male pin header, 13 pins [form="♂ (male)"]
  Associate4 = male pin header, 13 pins [form="♂ (male)"]
  Sleep_RQ4 = male pin header, 13 pins [form="♂ (male)"]
  Rx8 = male pin header, 15 pins [form="♂ (male)"]
  J172 = male pin header, 15 pins [form="♂ (male)"]
  Tx8 = male pin header, 15 pins [form="♂ (male)"]
  J173 = male pin header, 15 pins [form="♂ (male)"]
  IOL20 = female pin header, 8 pins [form="♀ (female)"]
  Power16 = female pin header, 8 pins [form="♀ (female)"]
  AD20 = female pin header, 6 pins [form="♀ (female)"]
  AD21 = female pin header, 6 pins [form="♀ (female)"]  # not connected
  Power17 = female pin header, 8 pins [form="♀ (female)"]
  IOL21 = female pin header, 8 pins [form="♀ (female)"]
  IOH21 = female pin header, 10 pins [form="♀ (female)"]
  R3 = Resistor [tolerance=±5% resistance=10k package=THT]
  J174 = male pin header, 15 pins [form="♂ (male)"]
  J175 = male pin header, 15 pins [form="♂ (male)"]
  DHT1 = DHT11 Humitidy and Temperature Sensor
  SCL5 = male pin header, 3 pins [form="♂ (male)"]
  SCL6 = male pin header, 3 pins [form="♂ (male)"]
  SDA5 = male pin header, 3 pins [form="♂ (male)"]
  SDA6 = male pin header, 3 pins [form="♂ (male)"]
  RTC7 = RTC-8564NB [package="Module(DIP 8P)"]
  SW2 = Akizuki slide switch IS-1250
  ICSP8 = Arduino R3 6pin male header [package=THT]  # not connected
  D17 = Schottky Diode [part_number=1N5817 package="300 mil [THT]"]
  D18 = Schottky Diode [part_number=1N5817 package="300 mil [THT]"]
  IOH22 = female pin header, 10 pins [form="♀ (female)"]
  INT9 = male pin header, 15 pins [form="♂ (male)"]
  J176 = male pin header, 15 pins [form="♂ (male)"]
  IOL22 = female pin header, 8 pins [form="♀ (female)"]
  Power18 = female pin header, 8 pins [form="♀ (female)"]
  AD22 = female pin header, 6 pins [form="♀ (female)"]
  BAT7 = Battery Holders [package=battcom_20mm_pth]
  パーツ1 = Arduino Mega 2560 (Rev3)  # not connected
  IO6 = female pin header, 8 pins [form="♀ (female)"]
  AD23 = female pin header, 8 pins [form="♀ (female)"]  # not connected
  IO7 = female pin header, 18 pins [form="♀ (female)"]  # not connected
  IO8 = female pin header, 18 pins [form="♀ (female)"]  # not connected
  S12 = Akizuki slide switch IS-2235
  microSD6 = MicroSD Breakout
  Card_detect5 = male pin header, 24 pins [form="♂ (male)"]
  J177 = male pin header, 24 pins [form="♂ (male)"]
  Chip_select5 = male pin header, 24 pins [form="♂ (male)"]
  J178 = male pin header, 24 pins [form="♂ (male)"]
  ICSP9 = Arduino R3 6pin male header [package=THT]
  IO9 = female pin header, 10 pins [form="♀ (female)"]
  IO10 = female pin header, 8 pins [form="♀ (female)"]
  POWER5 = female pin header, 8 pins [form="♀ (female)"]
  AD24 = female pin header, 8 pins [form="♀ (female)"]  # not connected
  J179 = male pin header, 22 pins [form="♂ (male)"]
  INT10 = male pin header, 22 pins [form="♂ (male)"]
  AD25 = female pin header, 8 pins [form="♀ (female)"]  # not connected
  S13 = Akizuki slide switch IS-2235
  RTC8 = RTC-8564NB [package="Module(DIP 8P)"]
  SW3 = Akizuki slide switch IS-1250
  ICSP10 = Arduino R3 6pin male header [package=THT]  # not connected
  D19 = Schottky Diode [part_number=1N5817 package="300 mil [THT]"]
  D20 = Schottky Diode [part_number=1N5817 package="300 mil [THT]"]
  IO11 = female pin header, 10 pins [form="♀ (female)"]
  IO12 = female pin header, 8 pins [form="♀ (female)"]
  Power19 = female pin header, 8 pins [form="♀ (female)"]
  BAT8 = Battery Holders [package=battcom_20mm_pth]
  IO13 = female pin header, 8 pins [form="♀ (female)"]
  AD26 = female pin header, 8 pins [form="♀ (female)"]  # not connected
  IO14 = female pin header, 18 pins [form="♀ (female)"]  # not connected
  IO15 = female pin header, 18 pins [form="♀ (female)"]  # not connected
  LC1 = M-04522
  S14 = Akizuki slide switch IS-1250
  IO16 = female pin header, 8 pins [form="♀ (female)"]
  AD27 = female pin header, 8 pins [form="♀ (female)"]  # not connected
  AD28 = female pin header, 8 pins [form="♀ (female)"]  # not connected
  IO17 = female pin header, 18 pins [form="♀ (female)"]  # not connected
  IO18 = female pin header, 18 pins [form="♀ (female)"]  # not connected
  Xbee8 = SSCI-KIT-XBSOCKET
  IO19 = female pin header, 10 pins [form="♀ (female)"]
  J180 = male pin header, 21 pins [form="♂ (male)"]
  J181 = male pin header, 21 pins [form="♂ (male)"]
  J182 = male pin header, 21 pins [form="♂ (male)"]
  J183 = male pin header, 21 pins [form="♂ (male)"]
  ON/Sleep9 = male pin header, 21 pins [form="♂ (male)"]
  Reset7 = male pin header, 21 pins [form="♂ (male)"]
  RSSI5 = male pin header, 21 pins [form="♂ (male)"]
  Associate5 = male pin header, 21 pins [form="♂ (male)"]
  Rx9 = male pin header, 24 pins [form="♂ (male)"]
  DTR/Sleep1 = male pin header, 21 pins [form="♂ (male)"]
  J184 = male pin header, 21 pins [form="♂ (male)"]
  Tx9 = male pin header, 24 pins [form="♂ (male)"]
  J185 = male pin header, 24 pins [form="♂ (male)"]
  J186 = male pin header, 24 pins [form="♂ (male)"]
  IO20 = female pin header, 8 pins [form="♀ (female)"]
  Power20 = female pin header, 8 pins [form="♀ (female)"]
  Grove7 = Grove 3 Axis Digital Accelerometer 16g  # not connected
  Grove8 = Grove Infrared Emitter  # not connected
  Grove9 = Grove 3 Axis Digital Accelerometer 16g  # not connected

nets:
  N1: J146.pin1, IOH14.pin7
  N2: J146.pin2, IOH14.pin6
  N3: J146.pin3, IOH14.pin5
  N4: J147.pin1, microSD4.DI
  N5: J147.pin2, microSD4.DO
  N6: J147.pin3, microSD4.CLK
  N7: J148.pin1, ICSP1.pin5
  N8: J148.pin2, ICSP1.pin1
  N9: J148.pin3, ICSP1.pin2
  N10: S10.pin0, POWER3.pin5
  N11: S10.pin1, microSD4.5V
  N12: S10.pin4, microSD4.3v
  N13: S10.pin5, POWER3.pin4
  N14: microSD4.CD, Card_detect3.pin1, Card_detect3.pin2, Card_detect3.pin3, Card_detect3.pin4, Card_detect3.pin5, Card_detect3.pin6, Card_detect3.pin7, Card_detect3.pin8, Card_detect3.pin9, Card_detect3.pin10, Card_detect3.pin11, Card_detect3.pin12
  N15: microSD4.CS, Chip_select3.pin1, Chip_select3.pin2, Chip_select3.pin3, Chip_select3.pin4, Chip_select3.pin5, Chip_select3.pin6, Chip_select3.pin7, Chip_select3.pin8, Chip_select3.pin9, Chip_select3.pin10, Chip_select3.pin11, Chip_select3.pin12
  N16: microSD4.GND, IOH14.pin4, POWER3.pin6, POWER3.pin7
  N17: J149.pin1, J150.pin1, IOH14.pin8
  N18: J149.pin2, J150.pin2, IOH14.pin9
  N19: J149.pin3, J150.pin3, IOH14.pin10
  N20: J149.pin5, J150.pin5, IOL14.pin1
  N21: J149.pin6, J150.pin6, IOL14.pin2
  N22: J149.pin7, J150.pin7, IOL14.pin3
  N23: J149.pin8, J150.pin8, IOL14.pin4
  N24: J149.pin9, J150.pin9, IOL14.pin5
  N25: J149.pin10, J150.pin10, IOL14.pin6
  N26: J149.pin11, J150.pin11, IOL14.pin7
  N27: J149.pin12, J150.pin12, IOL14.pin8
  N28: SCL3.pin1, IOH15.pin1
  N29: SCL3.pin2, J151.pin8, IOL15.pin1
  N30: SCL3.pin3, AD15.pin6
  N31: SCL4.pin1, SCL4.pin2, SCL4.pin3, RTC6.SCL
  N32: SDA3.pin1, IOH15.pin2
  N33: SDA3.pin2, IOH15.pin10, J151.pin6
  N34: SDA3.pin3, AD15.pin5
  N35: SDA4.pin1, SDA4.pin2, SDA4.pin3, RTC6.SDA
  N36: RTC6.INT, INT8.pin1, INT8.pin2, INT8.pin3, INT8.pin4, INT8.pin5, INT8.pin6, INT8.pin7, INT8.pin8, INT8.pin9, INT8.pin10, INT8.pin11, INT8.pin12, INT8.pin13, INT8.pin14, INT8.pin15
  N37: RTC6.GND, IOH15.pin4, Power12.pin6, Power12.pin7, BAT6.-
  N38: RTC6.VDD, D14.cathode, D15.cathode
  N39: SW1.pin0, SW1.pin3, Power12.pin5
  N40: SW1.pin1, SW1.pin4, D15.anode
  N41: SW1.pin2, SW1.pin5, Power12.pin4
  N42: D14.anode, BAT6.+
  N43: IOH15.pin5, J151.pin1
  N44: IOH15.pin6, J151.pin2
  N45: IOH15.pin7, J151.pin3
  N46: IOH15.pin8, J151.pin4
  N47: IOH15.pin9, J151.pin5
  N48: J151.pin9, IOL15.pin2
  N49: J151.pin10, IOL15.pin3
  N50: J151.pin11, IOL15.pin4
  N51: J151.pin12, IOL15.pin5
  N52: J151.pin13, IOL15.pin6
  N53: J151.pin14, IOL15.pin7
  N54: J151.pin15, IOL15.pin8
  N55: J152.pin1, AD16.pin1
  N56: J152.pin2, AD16.pin2
  N57: J152.pin3, AD16.pin3
  N58: J152.pin4, AD16.pin4
  N59: J152.pin5, AD16.pin5
  N60: J152.pin6, AD16.pin6
  N61: J153.pin1, IOH16.pin5, J154.pin1, J155.pin1, J156.pin1, J157.pin1, J158.pin1, J159.pin1
  N62: J153.pin2, IOH16.pin6, J154.pin2, J155.pin2, J156.pin2, J157.pin2, J158.pin2, J159.pin2
  N63: J153.pin3, IOH16.pin7, J154.pin3, J155.pin3, J156.pin3, J157.pin3, J158.pin3, J159.pin3
  N64: J153.pin4, IOH16.pin8, J154.pin4, J155.pin4, J156.pin4, J157.pin4, J158.pin4, J159.pin4
  N65: J153.pin5, IOH16.pin9, J154.pin5, J155.pin5, J156.pin5, J157.pin5, J158.pin5, J159.pin5
  N66: J153.pin6, IOH16.pin10, J154.pin6, J155.pin6, J156.pin6, J157.pin6, J158.pin6, J159.pin6
  N67: J153.pin8, J154.pin8, J156.pin8, J157.pin8, J158.pin8, J159.pin8, IOL16.pin1
  N68: J153.pin9, J154.pin9, J155.pin9, J156.pin9, J157.pin9, J158.pin9, J159.pin9, IOL16.pin2
  N69: J153.pin10, J154.pin10, J155.pin10, J156.pin10, J157.pin10, J158.pin10, J159.pin10, IOL16.pin3
  N70: J153.pin11, J154.pin11, J155.pin11, J156.pin11, J157.pin11, J158.pin11, J159.pin11, IOL16.pin4
  N71: J153.pin12, J154.pin12, J155.pin12, J156.pin12, J157.pin12, J158.pin12, J159.pin12, IOL16.pin5
  N72: J153.pin13, J154.pin13, J155.pin13, J156.pin13, J157.pin13, J158.pin13, J159.pin13, IOL16.pin6
  N73: RSSI3.pin1, RSSI3.pin2, RSSI3.pin3, RSSI3.pin4, RSSI3.pin5, RSSI3.pin6, RSSI3.pin7, RSSI3.pin8, RSSI3.pin9, RSSI3.pin10, RSSI3.pin11, RSSI3.pin12, RSSI3.pin13, Xbee6.pin6
  N74: Xbee6.VCC, Power13.pin4
  N75: Xbee6.pin2, Tx7.pin1, Tx7.pin2, Tx7.pin3, Tx7.pin4, Tx7.pin5, Tx7.pin6, Tx7.pin7, Tx7.pin8, Tx7.pin9, Tx7.pin10, Tx7.pin11, Tx7.pin12, Tx7.pin13, Tx7.pin14, Tx7.pin15
  N76: Xbee6.pin3, Rx7.pin1, Rx7.pin2, Rx7.pin3, Rx7.pin4, Rx7.pin5, Rx7.pin6, Rx7.pin7, Rx7.pin8, Rx7.pin9, Rx7.pin10, Rx7.pin11, Rx7.pin12, Rx7.pin13, Rx7.pin14, Rx7.pin15
  N77: Xbee6.pin5, Reset4.pin1, Reset4.pin2, Reset4.pin3, Reset4.pin4, Reset4.pin5, Reset4.pin6, Reset4.pin7, Reset4.pin8, Reset4.pin9, Reset4.pin10, Reset4.pin11, Reset4.pin12, Reset4.pin13
  N78: Xbee6.pin9, Sleep_RQ3.pin1, Sleep_RQ3.pin2, Sleep_RQ3.pin3, Sleep_RQ3.pin4, Sleep_RQ3.pin5, Sleep_RQ3.pin6, Sleep_RQ3.pin7, Sleep_RQ3.pin8, Sleep_RQ3.pin9, Sleep_RQ3.pin10, Sleep_RQ3.pin11, Sleep_RQ3.pin12, Sleep_RQ3.pin13
  N79: Xbee6.GND, IOH16.pin4, Power13.pin6, Power13.pin7
  N80: Xbee6.pin13, ON/Sleep7.pin1, ON/Sleep7.pin2, ON/Sleep7.pin3, ON/Sleep7.pin4, ON/Sleep7.pin5, ON/Sleep7.pin6, ON/Sleep7.pin7, ON/Sleep7.pin8, ON/Sleep7.pin9, ON/Sleep7.pin10, ON/Sleep7.pin11, ON/Sleep7.pin12, ON/Sleep7.pin13, ON/Sleep7.pin14, ON/Sleep7.pin15
  N81: Xbee6.pin15, Associate3.pin1, Associate3.pin2, Associate3.pin3, Associate3.pin4, Associate3.pin5, Associate3.pin6, Associate3.pin7, Associate3.pin8, Associate3.pin9, Associate3.pin10, Associate3.pin11, Associate3.pin12, Associate3.pin13
  N82: J158.pin14, J159.pin14, IOL16.pin7
  N83: J158.pin15, J159.pin15, IOL16.pin8
  N84: GR-kurumi1.D1/TX0, IOL17.pin7
  N85: GR-kurumi1.D0/RX0, IOL17.pin8
  N86: GR-kurumi1.RST, Reset5.2, Power14.pin3
  GND: GR-kurumi1.GND, AE-LXDC55-3_3V1.GND, Power_plug7.GND, Reset5.4, IOH17.pin4, Power14.pin6, Power14.pin7
  N87: GR-kurumi1.D2/INT0, GR-kurumi1.RAW, IOL17.pin6
  N88: GR-kurumi1.D3/INT1/PWM, IOL17.pin5
  N89: GR-kurumi1.D4, IOL17.pin4
  N90: GR-kurumi1.D5/PWM, IOL17.pin3
  N91: GR-kurumi1.D6/PWM, IOL17.pin2
  N92: GR-kurumi1.D7/TX1/SCL, IOL17.pin1
  N93: GR-kurumi1.D8/RX1/SDA, IOH17.pin10
  N94: GR-kurumi1.D9/TX2/PWM, IOH17.pin9
  N95: GR-kurumi1.D10/RX2/SS, IOH17.pin8
  N96: GR-kurumi1.D11/Soft_PWM/MOSI, IOH17.pin7
  N97: GR-kurumi1.D12/MISO, IOH17.pin6
  N98: GR-kurumi1.D13/SCLK, IOH17.pin5
  N99: GR-kurumi1.A0, AD17.pin1
  N100: GR-kurumi1.A1, AD17.pin2
  N101: GR-kurumi1.A2, AD17.pin3
  N102: GR-kurumi1.A3, AD17.pin4
  N103: GR-kurumi1.VCC, AE-LXDC55-3_3V1.OUT, R2.Pin_1, D16.cathode, Power14.pin4
  N104: GR-kurumi1.A4, AD17.pin5
  N105: GR-kurumi1.A5, AD17.pin6
  N106: AE-LXDC55-3_3V1.IN, Power_plug7.VCC, Power14.pin8
  N107: R2.Pin_0, D16.anode, Reset5.1
  N108: Reset1.2, Power2.pin3, Pro_Mini_3V3_8MHz1.RESET
  GND_2: Reset1.4, Power2.pin6, Power2.pin7, Power_plug6.GND, Pro_Mini_3V3_8MHz1.GND, IOH2.pin4
  N109: IOL2.pin1, Pro_Mini_3V3_8MHz1.D7
  N110: IOL2.pin2, Pro_Mini_3V3_8MHz1.D6_PWM
  N111: IOL2.pin3, Pro_Mini_3V3_8MHz1.D5_PWM
  N112: IOL2.pin4, Pro_Mini_3V3_8MHz1.D4
  N113: IOL2.pin5, Pro_Mini_3V3_8MHz1.D3_PWM
  N114: IOL2.pin6, Pro_Mini_3V3_8MHz1.D2
  N115: IOL2.pin7, Pro_Mini_3V3_8MHz1.D1/RX
  N116: IOL2.pin8, Pro_Mini_3V3_8MHz1.D0/TX
  N117: Power2.pin4, S2.pin0, S2.pin3
  N118: Power2.pin5, S2.pin2, S2.pin5
  N119: Power2.pin8, Power_plug6.VCC, Pro_Mini_3V3_8MHz1.RAW
  N120: AD2.pin1, Pro_Mini_3V3_8MHz1.A0
  N121: AD2.pin2, Pro_Mini_3V3_8MHz1.A1
  N122: AD2.pin3, Pro_Mini_3V3_8MHz1.A2
  N123: AD2.pin4, Pro_Mini_3V3_8MHz1.A3
  N124: AD2.pin5, Pro_Mini_3V3_8MHz1.A4
  N125: AD2.pin6, Pro_Mini_3V3_8MHz1.A5
  N126: Pro_Mini_3V3_8MHz1.VCC, S2.pin1, S2.pin4
  N127: Pro_Mini_3V3_8MHz1.D13/SCK, IOH2.pin5
  N128: Pro_Mini_3V3_8MHz1.D12/MISO, IOH2.pin6
  N129: Pro_Mini_3V3_8MHz1.D11_PWM/MOSI, IOH2.pin7
  N130: Pro_Mini_3V3_8MHz1.D10_PWM/SS, IOH2.pin8
  N131: Pro_Mini_3V3_8MHz1.D9_PWM, IOH2.pin9
  N132: Pro_Mini_3V3_8MHz1.D8, IOH2.pin10
  N133: J160.pin1, AD20.pin1
  N134: J160.pin2, AD20.pin2
  N135: J160.pin3, AD20.pin3
  N136: J160.pin4, AD20.pin4
  N137: J160.pin5, AD20.pin5
  N138: J160.pin6, AD20.pin6
  N139: J161.pin1, IOH19.pin7
  N140: J161.pin2, IOH19.pin6
  N141: J161.pin3, IOH19.pin5
  N142: J162.pin1, IOH20.pin5, J168.pin1, J169.pin1, J170.pin1, J171.pin1, J172.pin1, J173.pin1
  N143: J162.pin2, IOH20.pin6, J168.pin2, J169.pin2, J170.pin2, J171.pin2, J172.pin2, J173.pin2
  N144: J162.pin3, IOH20.pin7, J168.pin3, J169.pin3, J170.pin3, J171.pin3, J172.pin3, J173.pin3
  N145: J162.pin4, IOH20.pin8, J168.pin4, J169.pin4, J170.pin4, J171.pin4, J172.pin4, J173.pin4
  N146: J162.pin5, IOH20.pin9, J168.pin5, J169.pin5, J170.pin5, J171.pin5, J172.pin5, J173.pin5
  N147: J162.pin6, IOH20.pin10, J168.pin6, J169.pin6, J170.pin6, J171.pin6, J172.pin6, J173.pin6
  N148: J162.pin8, J168.pin8, J170.pin8, J171.pin8, J172.pin8, J173.pin8, IOL20.pin1
  N149: J162.pin9, J168.pin9, J169.pin9, J170.pin9, J171.pin9, J172.pin9, J173.pin9, IOL20.pin2
  N150: J162.pin10, J168.pin10, J169.pin10, J170.pin10, J171.pin10, J172.pin10, J173.pin10, IOL20.pin3
  N151: J162.pin11, J168.pin11, J169.pin11, J170.pin11, J171.pin11, J172.pin11, J173.pin11, IOL20.pin4
  N152: J162.pin12, J168.pin12, J169.pin12, J170.pin12, J171.pin12, J172.pin12, J173.pin12, IOL20.pin5
  N153: J162.pin13, J168.pin13, J169.pin13, J170.pin13, J171.pin13, J172.pin13, J173.pin13, IOL20.pin6
  N154: J163.pin1, microSD5.DI
  N155: J163.pin2, microSD5.DO
  N156: J163.pin3, microSD5.CLK
  N157: RSSI4.pin1, RSSI4.pin2, RSSI4.pin3, RSSI4.pin4, RSSI4.pin5, RSSI4.pin6, RSSI4.pin7, RSSI4.pin8, RSSI4.pin9, RSSI4.pin10, RSSI4.pin11, RSSI4.pin12, RSSI4.pin13, Xbee7.pin6
  N158: J164.pin1, ICSP6.pin5
  N159: J164.pin2, ICSP6.pin1
  N160: J164.pin3, ICSP6.pin2
  N161: S11.pin0, POWER4.pin5
  N162: S11.pin1, microSD5.5V
  N163: S11.pin4, microSD5.3v
  N164: S11.pin5, POWER4.pin4
  N165: microSD5.CD, Card_detect4.pin1, Card_detect4.pin2, Card_detect4.pin3, Card_detect4.pin4, Card_detect4.pin5, Card_detect4.pin6, Card_detect4.pin7, Card_detect4.pin8, Card_detect4.pin9, Card_detect4.pin10, Card_detect4.pin11, Card_detect4.pin12
  N166: microSD5.CS, Chip_select4.pin1, Chip_select4.pin2, Chip_select4.pin3, Chip_select4.pin4, Chip_select4.pin5, Chip_select4.pin6, Chip_select4.pin7, Chip_select4.pin8, Chip_select4.pin9, Chip_select4.pin10, Chip_select4.pin11, Chip_select4.pin12
  N167: microSD5.GND, IOH19.pin4, POWER4.pin6, POWER4.pin7
  N168: J165.pin1, J166.pin1, IOH19.pin8
  N169: J165.pin2, J166.pin2, IOH19.pin9
  N170: J165.pin3, J166.pin3, IOH19.pin10
  N171: J165.pin5, J166.pin5, IOL19.pin1
  N172: J165.pin6, J166.pin6, IOL19.pin2
  N173: J165.pin7, J166.pin7, IOL19.pin3
  N174: J165.pin8, J166.pin8, IOL19.pin4
  N175: J165.pin9, J166.pin9, IOL19.pin5
  N176: J165.pin10, J166.pin10, IOL19.pin6
  N177: J165.pin11, J166.pin11, IOL19.pin7
  N178: J165.pin12, J166.pin12, IOL19.pin8
  N179: Xbee7.VCC, Power16.pin4
  N180: Xbee7.pin2, Tx8.pin1, Tx8.pin2, Tx8.pin3, Tx8.pin4, Tx8.pin5, Tx8.pin6, Tx8.pin7, Tx8.pin8, Tx8.pin9, Tx8.pin10, Tx8.pin11, Tx8.pin12, Tx8.pin13, Tx8.pin14, Tx8.pin15
  N181: Xbee7.pin3, Rx8.pin1, Rx8.pin2, Rx8.pin3, Rx8.pin4, Rx8.pin5, Rx8.pin6, Rx8.pin7, Rx8.pin8, Rx8.pin9, Rx8.pin10, Rx8.pin11, Rx8.pin12, Rx8.pin13, Rx8.pin14, Rx8.pin15
  N182: Xbee7.pin5, Reset6.pin1, Reset6.pin2, Reset6.pin3, Reset6.pin4, Reset6.pin5, Reset6.pin6, Reset6.pin7, Reset6.pin8, Reset6.pin9, Reset6.pin10, Reset6.pin11, Reset6.pin12, Reset6.pin13
  N183: Xbee7.pin9, Sleep_RQ4.pin1, Sleep_RQ4.pin2, Sleep_RQ4.pin3, Sleep_RQ4.pin4, Sleep_RQ4.pin5, Sleep_RQ4.pin6, Sleep_RQ4.pin7, Sleep_RQ4.pin8, Sleep_RQ4.pin9, Sleep_RQ4.pin10, Sleep_RQ4.pin11, Sleep_RQ4.pin12, Sleep_RQ4.pin13
  N184: Xbee7.GND, IOH20.pin4, Power16.pin6, Power16.pin7
  N185: Xbee7.pin13, ON/Sleep8.pin1, ON/Sleep8.pin2, ON/Sleep8.pin3, ON/Sleep8.pin4, ON/Sleep8.pin5, ON/Sleep8.pin6, ON/Sleep8.pin7, ON/Sleep8.pin8, ON/Sleep8.pin9, ON/Sleep8.pin10, ON/Sleep8.pin11, ON/Sleep8.pin12, ON/Sleep8.pin13, ON/Sleep8.pin14, ON/Sleep8.pin15
  N186: Xbee7.pin15, Associate4.pin1, Associate4.pin2, Associate4.pin3, Associate4.pin4, Associate4.pin5, Associate4.pin6, Associate4.pin7, Associate4.pin8, Associate4.pin9, Associate4.pin10, Associate4.pin11, Associate4.pin12, Associate4.pin13
  N187: J172.pin14, J173.pin14, IOL20.pin7
  N188: J172.pin15, J173.pin15, IOL20.pin8
  N189: Power17.pin4, DHT1.VDD
  N190: Power17.pin6, Power17.pin7, IOH21.pin4, DHT1.GND
  N191: IOL21.pin1, J175.pin8
  N192: IOL21.pin2, J175.pin9
  N193: IOL21.pin3, J175.pin10
  N194: IOL21.pin4, J175.pin11
  N195: IOL21.pin5, J175.pin12
  N196: IOL21.pin6, J175.pin13
  N197: IOL21.pin7, J175.pin14
  N198: IOL21.pin8, J175.pin15
  N199: IOH21.pin5, J175.pin1
  N200: IOH21.pin6, J175.pin2
  N201: IOH21.pin7, J175.pin3
  N202: IOH21.pin8, J175.pin4
  N203: IOH21.pin9, J175.pin5
  N204: IOH21.pin10, J175.pin6
  N205: R3.Pin_0, R3.Pin_1, J174.pin1, J174.pin2, J174.pin3, J174.pin4, J174.pin5, J174.pin6, J174.pin7, J174.pin8, J174.pin9, J174.pin10, J174.pin11, J174.pin12, J174.pin13, J174.pin14, J174.pin15, DHT1.DATA
  N206: SCL5.pin1, IOH22.pin1
  N207: SCL5.pin2, J176.pin8, IOL22.pin1
  N208: SCL5.pin3, AD22.pin6
  N209: SCL6.pin1, SCL6.pin2, SCL6.pin3, RTC7.SCL
  N210: SDA5.pin1, IOH22.pin2
  N211: SDA5.pin2, IOH22.pin10, J176.pin6
  N212: SDA5.pin3, AD22.pin5
  N213: SDA6.pin1, SDA6.pin2, SDA6.pin3, RTC7.SDA
  N214: RTC7.INT, INT9.pin1, INT9.pin2, INT9.pin3, INT9.pin4, INT9.pin5, INT9.pin6, INT9.pin7, INT9.pin8, INT9.pin9, INT9.pin10, INT9.pin11, INT9.pin12, INT9.pin13, INT9.pin14, INT9.pin15
  N215: RTC7.GND, IOH22.pin4, Power18.pin6, Power18.pin7, BAT7.-
  N216: RTC7.VDD, D17.cathode, D18.cathode
  N217: SW2.pin0, SW2.pin3, Power18.pin5
  N218: SW2.pin1, SW2.pin4, D18.anode
  N219: SW2.pin2, SW2.pin5, Power18.pin4
  N220: D17.anode, BAT7.+
  N221: IOH22.pin5, J176.pin1
  N222: IOH22.pin6, J176.pin2
  N223: IOH22.pin7, J176.pin3
  N224: IOH22.pin8, J176.pin4
  N225: IOH22.pin9, J176.pin5
  N226: J176.pin9, IOL22.pin2
  N227: J176.pin10, IOL22.pin3
  N228: J176.pin11, IOL22.pin4
  N229: J176.pin12, IOL22.pin5
  N230: J176.pin13, IOL22.pin6
  N231: J176.pin14, IOL22.pin7
  N232: J176.pin15, IOL22.pin8
  N233: IO6.pin1, J177.pin17, J178.pin17
  N234: IO6.pin2, J177.pin18, J178.pin18
  N235: IO6.pin3, J177.pin19, J178.pin19
  N236: IO6.pin4, J177.pin20, J178.pin20
  N237: IO6.pin5, J177.pin21, J178.pin21
  N238: IO6.pin6, J177.pin22, J178.pin22
  N239: IO6.pin7, J177.pin23, J178.pin23
  N240: IO6.pin8, J177.pin24, J178.pin24
  N241: S12.pin0, S12.pin3, POWER5.pin5
  N242: S12.pin1, microSD6.5V
  N243: S12.pin4, microSD6.3v
  N244: S12.pin5, POWER5.pin4
  N245: microSD6.CD, Card_detect5.pin1, Card_detect5.pin2, Card_detect5.pin3, Card_detect5.pin4, Card_detect5.pin5, Card_detect5.pin6, Card_detect5.pin7, Card_detect5.pin8, Card_detect5.pin9, Card_detect5.pin10, Card_detect5.pin11, Card_detect5.pin12, Card_detect5.pin13, Card_detect5.pin14, Card_detect5.pin15, Card_detect5.pin16, Card_detect5.pin17, Card_detect5.pin18, Card_detect5.pin19, Card_detect5.pin20, Card_detect5.pin21, Card_detect5.pin22, Card_detect5.pin23, Card_detect5.pin24
  N246: microSD6.CS, Chip_select5.pin1, Chip_select5.pin2, Chip_select5.pin3, Chip_select5.pin4, Chip_select5.pin5, Chip_select5.pin6, Chip_select5.pin7, Chip_select5.pin8, Chip_select5.pin9, Chip_select5.pin10, Chip_select5.pin11, Chip_select5.pin12, Chip_select5.pin13, Chip_select5.pin14, Chip_select5.pin15, Chip_select5.pin16, Chip_select5.pin17, Chip_select5.pin18, Chip_select5.pin19, Chip_select5.pin20, Chip_select5.pin21, Chip_select5.pin22, Chip_select5.pin23, Chip_select5.pin24
  N247: microSD6.DI, ICSP9.pin5
  N248: microSD6.DO, ICSP9.pin1
  N249: microSD6.CLK, ICSP9.pin2
  N250: microSD6.GND, IO9.pin4, POWER5.pin6, POWER5.pin7
  N251: J177.pin1, J178.pin1, IO9.pin5
  N252: J177.pin2, J178.pin2, IO9.pin6
  N253: J177.pin3, J178.pin3, IO9.pin7
  N254: J177.pin4, J178.pin4, IO9.pin8
  N255: J177.pin5, J178.pin5, IO9.pin9
  N256: J177.pin6, J178.pin6, IO9.pin10
  N257: J177.pin8, J178.pin8, IO10.pin1
  N258: J177.pin9, J178.pin9, IO10.pin2
  N259: J177.pin10, J178.pin10, IO10.pin3
  N260: J177.pin11, J178.pin11, IO10.pin4
  N261: J177.pin12, J178.pin12, IO10.pin5
  N262: J177.pin13, J178.pin13, IO10.pin6
  N263: J177.pin14, J178.pin14, IO10.pin7
  N264: J177.pin15, J178.pin15, IO10.pin8
  N265: J179.pin1, IO11.pin5
  N266: J179.pin2, IO11.pin6
  N267: J179.pin3, IO11.pin7
  N268: J179.pin4, IO11.pin8
  N269: J179.pin5, IO11.pin9
  N270: J179.pin6, IO11.pin10
  N271: J179.pin8, IO12.pin1
  N272: J179.pin9, IO12.pin2
  N273: J179.pin10, IO12.pin3
  N274: J179.pin11, IO12.pin4
  N275: J179.pin12, IO12.pin5
  N276: J179.pin13, IO12.pin6
  N277: J179.pin14, IO12.pin7
  N278: J179.pin15, IO12.pin8
  N279: J179.pin17, IO13.pin1
  N280: J179.pin18, IO13.pin2
  N281: J179.pin19, IO13.pin3
  N282: J179.pin20, IO13.pin4
  N283: J179.pin21, IO13.pin5
  N284: J179.pin22, IO13.pin6
  N285: INT10.pin1, INT10.pin2, INT10.pin3, INT10.pin4, INT10.pin5, INT10.pin6, INT10.pin7, INT10.pin8, INT10.pin9, INT10.pin10, INT10.pin11, INT10.pin12, INT10.pin13, INT10.pin14, INT10.pin15, INT10.pin16, INT10.pin17, INT10.pin18, INT10.pin19, INT10.pin20, INT10.pin21, INT10.pin22, RTC8.INT
  N286: S13.pin0, IO13.pin8
  N287: S13.pin1, RTC8.SCL
  N288: S13.pin2, IO11.pin1
  N289: S13.pin3, IO13.pin7
  N290: S13.pin4, RTC8.SDA
  N291: S13.pin5, IO11.pin2
  N292: RTC8.GND, IO11.pin4, Power19.pin6, Power19.pin7, BAT8.-
  N293: RTC8.VDD, D19.cathode, D20.cathode
  N294: SW3.pin0, SW3.pin3, Power19.pin5
  N295: SW3.pin1, SW3.pin4, D20.anode
  N296: SW3.pin2, SW3.pin5, Power19.pin4
  N297: D19.anode, BAT8.+
  N298: LC1.A0, Xbee8.pin2
  N299: LC1.A1, Xbee8.pin3
  N300: LC1.A2, Xbee8.pin5
  N301: LC1.A3, Xbee8.pin6
  N302: LC1.A4, Xbee8.pin9
  N303: LC1.A5, Xbee8.pin15
  N304: LC1.A6, Xbee8.pin13
  N305: LC1.VCCA, S14.pin0, S14.pin3, Xbee8.VCC, Power20.pin4
  GND_3: LC1.GND, LC1.OE, Xbee8.GND, IO19.pin4, Power20.pin6, Power20.pin7
  N306: LC1.B0, Tx9.pin1, Tx9.pin2, Tx9.pin3, Tx9.pin4, Tx9.pin5, Tx9.pin6, Tx9.pin7, Tx9.pin8, Tx9.pin9, Tx9.pin10, Tx9.pin11, Tx9.pin12, Tx9.pin13, Tx9.pin14, Tx9.pin15, Tx9.pin16, Tx9.pin17, Tx9.pin18, Tx9.pin19, Tx9.pin20, Tx9.pin21, Tx9.pin22, Tx9.pin23, Tx9.pin24
  N307: LC1.B1, Rx9.pin1, Rx9.pin2, Rx9.pin3, Rx9.pin4, Rx9.pin5, Rx9.pin6, Rx9.pin7, Rx9.pin8, Rx9.pin9, Rx9.pin10, Rx9.pin11, Rx9.pin12, Rx9.pin13, Rx9.pin14, Rx9.pin15, Rx9.pin16, Rx9.pin17, Rx9.pin18, Rx9.pin19, Rx9.pin20, Rx9.pin21, Rx9.pin22, Rx9.pin23, Rx9.pin24
  N308: LC1.B2, Reset7.pin1, Reset7.pin2, Reset7.pin3, Reset7.pin4, Reset7.pin5, Reset7.pin6, Reset7.pin7, Reset7.pin8, Reset7.pin9, Reset7.pin10, Reset7.pin11, Reset7.pin12, Reset7.pin13, Reset7.pin14, Reset7.pin15, Reset7.pin16, Reset7.pin17, Reset7.pin18, Reset7.pin19, Reset7.pin20, Reset7.pin21
  N309: LC1.B3, RSSI5.pin1, RSSI5.pin2, RSSI5.pin3, RSSI5.pin4, RSSI5.pin5, RSSI5.pin6, RSSI5.pin7, RSSI5.pin8, RSSI5.pin9, RSSI5.pin10, RSSI5.pin11, RSSI5.pin12, RSSI5.pin13, RSSI5.pin14, RSSI5.pin15, RSSI5.pin16, RSSI5.pin17, RSSI5.pin18, RSSI5.pin19, RSSI5.pin20, RSSI5.pin21
  N310: LC1.B4, DTR/Sleep1.pin1, DTR/Sleep1.pin2, DTR/Sleep1.pin3, DTR/Sleep1.pin4, DTR/Sleep1.pin5, DTR/Sleep1.pin6, DTR/Sleep1.pin7, DTR/Sleep1.pin8, DTR/Sleep1.pin9, DTR/Sleep1.pin10, DTR/Sleep1.pin11, DTR/Sleep1.pin12, DTR/Sleep1.pin13, DTR/Sleep1.pin14, DTR/Sleep1.pin15, DTR/Sleep1.pin16, DTR/Sleep1.pin17, DTR/Sleep1.pin18, DTR/Sleep1.pin19, DTR/Sleep1.pin20, DTR/Sleep1.pin21
  N311: LC1.B5, Associate5.pin1, Associate5.pin2, Associate5.pin3, Associate5.pin4, Associate5.pin5, Associate5.pin6, Associate5.pin7, Associate5.pin8, Associate5.pin9, Associate5.pin10, Associate5.pin11, Associate5.pin12, Associate5.pin13, Associate5.pin14, Associate5.pin15, Associate5.pin16, Associate5.pin17, Associate5.pin18, Associate5.pin19, Associate5.pin20, Associate5.pin21
  N312: LC1.B6, ON/Sleep9.pin1, ON/Sleep9.pin2, ON/Sleep9.pin3, ON/Sleep9.pin4, ON/Sleep9.pin5, ON/Sleep9.pin6, ON/Sleep9.pin7, ON/Sleep9.pin8, ON/Sleep9.pin9, ON/Sleep9.pin10, ON/Sleep9.pin11, ON/Sleep9.pin12, ON/Sleep9.pin13, ON/Sleep9.pin14, ON/Sleep9.pin15, ON/Sleep9.pin16, ON/Sleep9.pin17, ON/Sleep9.pin18, ON/Sleep9.pin19, ON/Sleep9.pin20, ON/Sleep9.pin21
  N313: LC1.VCCB, S14.pin1, S14.pin4
  N314: S14.pin2, S14.pin5, Power20.pin5
  N315: IO16.pin1, J180.pin14, J181.pin14, J182.pin14, J183.pin14, J184.pin14, J185.pin17, J186.pin17
  N316: IO16.pin2, J180.pin15, J181.pin15, J182.pin15, J183.pin15, J184.pin15, J185.pin18, J186.pin18
  N317: IO16.pin3, J180.pin16, J181.pin16, J182.pin16, J183.pin16, J184.pin16, J185.pin19, J186.pin19
  N318: IO16.pin4, J180.pin17, J181.pin17, J182.pin17, J183.pin17, J184.pin17, J185.pin20, J186.pin20
  N319: IO16.pin5, J180.pin18, J181.pin18, J182.pin18, J183.pin18, J184.pin18, J185.pin21, J186.pin21
  N320: IO16.pin6, J180.pin19, J181.pin19, J182.pin19, J183.pin19, J184.pin19, J185.pin22, J186.pin22
  N321: IO16.pin7, J180.pin20, J181.pin20, J182.pin20, J183.pin20, J184.pin20, J185.pin23, J186.pin23
  N322: IO16.pin8, J180.pin21, J181.pin21, J182.pin21, J183.pin21, J184.pin21, J185.pin24, J186.pin24
  N323: IO19.pin5, J185.pin1, J186.pin1
  N324: IO19.pin6, J185.pin2, J186.pin2
  N325: IO19.pin7, J185.pin3, J186.pin3
  N326: IO19.pin8, J180.pin1, J181.pin1, J182.pin1, J183.pin1, J184.pin1, J185.pin4, J186.pin4
  N327: IO19.pin9, J180.pin2, J181.pin2, J182.pin2, J183.pin2, J184.pin2, J185.pin5, J186.pin5
  N328: IO19.pin10, J180.pin3, J181.pin3, J182.pin3, J183.pin3, J184.pin3, J185.pin6, J186.pin6
  N329: J180.pin5, J181.pin5, J182.pin5, J183.pin5, J184.pin5, J185.pin8, J186.pin8, IO20.pin1
  N330: J180.pin6, J181.pin6, J182.pin6, J183.pin6, J184.pin6, J185.pin9, J186.pin9, IO20.pin2
  N331: J180.pin7, J181.pin7, J182.pin7, J183.pin7, J184.pin7, J185.pin10, J186.pin10, IO20.pin3
  N332: J180.pin8, J181.pin8, J182.pin8, J183.pin8, J184.pin8, J185.pin11, J186.pin11, IO20.pin4
  N333: J180.pin9, J181.pin9, J182.pin9, J183.pin9, J184.pin9, J185.pin12, J186.pin12, IO20.pin5
  N334: J180.pin10, J181.pin10, J182.pin10, J183.pin10, J184.pin10, J185.pin13, J186.pin13, IO20.pin6
  N335: J180.pin11, J181.pin11, J182.pin11, J183.pin11, J184.pin11, J185.pin14, J186.pin14, IO20.pin7
  N336: J180.pin12, J181.pin12, J182.pin12, J183.pin12, J184.pin12, J185.pin15, J186.pin15, IO20.pin8

notes:
  Arduino MEGA
  GR-kurumi
  Arduino Pro Mini 3.3V
  利用上の注意
  (1) GR-kurumiはGroveシールドを搭載すると，本体が動作しなくなる．
  (2) grove用のセンサモジュールは動作しない場合が見受けられるため，センサを使ったシールドを別途用意する必要がある．
  利用上の注意
  ○Xbee用のシールドが3.3V専用となっているため，本体もPro miniの中から3.3V動作をものを選択
  XbeeとMegaの接続(シリアル通信)でデータがなくなることが頻発するが，今のところ原因不明．とりあえず，このシステムでは無線でのセンサのデータの送信はおまけ．

custom parts:
  Akizuki slide switch IS-2235: Akizuki slide switch is-2235 (P-02627)
  MicroSD Breakout: 5V-ready microSD Breakout with Level Shifter
  Arduino R3 6pin male header: Pin header for arduino R3
  RTC-8564NB: Real Time Clock Module and I2C-BUS interface method. This product is a module of the SON 8-pin DIP package. Supply voltage 1.8-5.5V original version by KimuShige
  Akizuki slide switch IS-1250: Akizuki slide switch is-1250 (P-01665)
  SSCI-KIT-XBSOCKET: Xbee pin conversion
  GR kurumi (Renesas Gadget) no serial: RL78/G13
  AE-LXDC55-3.3V-Down: AE-LXDC55-3.3V upside down
  Power plug: 秋月電子通商 AE-DCJACK-DIPKIT-2.1mm-10A(通販コードK-06998)とその互換品(K06999,K-08415,K-08416)
  Arduino Pro Mini v13: It's blue! It's thin! It's the Arduino Pro Mini! SparkFun's minimal design approach to Arduino. This is a 5V Arduino running the 16MHz bootloader. Arduino Pro Mini does not come with connectors populated so that you can solder in any connector or wire with any orientation you need. We recommend first time Arduino users start with the Uno R3. It's a great board that will get you up and running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
  DHT11 Humitidy and Temperature Sensor: DHT11 Humidity and Temperature Sensor
  M-04522: Akizuki 8bit bi-directional logic level converter M-04522
