# Fritzing sketch Arduino連携システム例 (saved by Fritzing 0.9.2b)
perfboards: 10

parts:
  パーツ1 = Arduino Uno (Rev3)  # not connected
  Pro_Mini_3V3_8MHz1 = Arduino Pro Mini v13
  S2 = Akizuki slide switch IS-1250
  Power_plug6 = Power plug
  J97 = Arduino R3 6pin male header [package=THT]  # not connected
  Reset1 = Momentary Switch [package=ksa_sealed_tac_switch]
  IOH2 = female pin header, 10 pins [form="♀ (female)"]
  Power2 = female pin header, 8 pins [form="♀ (female)"]
  IOL2 = female pin header, 8 pins [form="♀ (female)"]
  AD2 = female pin header, 6 pins [form="♀ (female)"]
  Grove1 = Grove 3 Axis Digital Accelerometer 16g  # not connected
  Grove2 = Grove Infrared Emitter  # not connected
  Grove3 = Grove 3 Axis Digital Accelerometer 16g  # not connected
  VCC1 = Battery block 9V  # not connected
  SCL3 = male pin header, 3 pins [form="♂ (male)"]
  SCL4 = male pin header, 3 pins [form="♂ (male)"]
  SDA3 = male pin header, 3 pins [form="♂ (male)"]
  SDA4 = male pin header, 3 pins [form="♂ (male)"]
  RTC5 = RTC-8564NB [package="Module(DIP 8P)"]
  SW1 = Akizuki slide switch IS-1250
  ICSP1 = Arduino R3 6pin male header [package=THT]  # not connected
  D11 = Schottky Diode [part_number=1N5817 package="300 mil [THT]"]
  D12 = Schottky Diode [part_number=1N5817 package="300 mil [THT]"]
  IOH8 = female pin header, 10 pins [form="♀ (female)"]
  INT5 = male pin header, 15 pins [form="♂ (male)"]
  J117 = male pin header, 15 pins [form="♂ (male)"]
  IOL8 = female pin header, 8 pins [form="♀ (female)"]
  Power8 = female pin header, 8 pins [form="♀ (female)"]
  AD8 = female pin header, 6 pins [form="♀ (female)"]
  BAT5 = Battery Holders [package=battcom_20mm_pth]
  ICSP2 = Arduino R3 6pin male header [package=THT]  # not connected
  Power_IN2 = Grove Header 4pin 90 degree direct mount [package="90 degree"]
  Signal_IN2 = Grove Header 4pin 90 degree direct mount [package="90 degree"]
  LevelConverter2 = Bi-Directional Logic Level Converter [part_number=BOB-12009]
  IOH9 = female pin header, 10 pins [form="♀ (female)"]
  Shutdown3 = male pin header, 15 pins [form="♂ (male)"]
  J118 = male pin header, 15 pins [form="♂ (male)"]
  Rx5 = male pin header, 15 pins [form="♂ (male)"]
  J119 = male pin header, 15 pins [form="♂ (male)"]
  Tx5 = male pin header, 15 pins [form="♂ (male)"]
  J120 = male pin header, 15 pins [form="♂ (male)"]
  IOL9 = female pin header, 8 pins [form="♀ (female)"]
  Power9 = female pin header, 8 pins [form="♀ (female)"]
  AD9 = female pin header, 6 pins [form="♀ (female)"]  # not connected
  ICSP3 = Arduino R3 6pin male header [package=THT]  # not connected
  Signal_OUT2 = Grove Header 4pin 90 degree direct mount [package="90 degree"]
  Power_OUT2 = Grove Header 4pin 90 degree direct mount [package="90 degree"]
  IOH10 = female pin header, 10 pins [form="♀ (female)"]
  Rx6 = male pin header, 15 pins [form="♂ (male)"]
  Reset3 = male pin header, 13 pins [form="♂ (male)"]
  J121 = male pin header, 13 pins [form="♂ (male)"]
  Shutdown4 = male pin header, 13 pins [form="♂ (male)"]
  J122 = male pin header, 13 pins [form="♂ (male)"]
  J123 = male pin header, 13 pins [form="♂ (male)"]
  RelayControl2 = male pin header, 13 pins [form="♂ (male)"]
  J124 = male pin header, 15 pins [form="♂ (male)"]
  Tx6 = male pin header, 15 pins [form="♂ (male)"]
  J125 = male pin header, 15 pins [form="♂ (male)"]
  IOL10 = female pin header, 8 pins [form="♀ (female)"]
  Power10 = female pin header, 8 pins [form="♀ (female)"]
  AD10 = female pin header, 6 pins [form="♀ (female)"]  # not connected
  SCL5 = male pin header, 3 pins [form="♂ (male)"]
  SCL6 = male pin header, 3 pins [form="♂ (male)"]
  SDA5 = male pin header, 3 pins [form="♂ (male)"]
  SDA6 = male pin header, 3 pins [form="♂ (male)"]
  RTC6 = RTC-8564NB [package="Module(DIP 8P)"]
  SW2 = Akizuki slide switch IS-1250
  ICSP4 = Arduino R3 6pin male header [package=THT]  # not connected
  D13 = Schottky Diode [part_number=1N5817 package="300 mil [THT]"]
  D14 = Schottky Diode [part_number=1N5817 package="300 mil [THT]"]
  IOH11 = female pin header, 10 pins [form="♀ (female)"]
  INT6 = male pin header, 15 pins [form="♂ (male)"]
  J126 = male pin header, 15 pins [form="♂ (male)"]
  IOL11 = female pin header, 8 pins [form="♀ (female)"]
  Power11 = female pin header, 8 pins [form="♀ (female)"]
  AD11 = female pin header, 6 pins [form="♀ (female)"]
  BAT6 = Battery Holders [package=battcom_20mm_pth]
  J127 = male pin header, 6 pins [form="♂ (male)"]
  J128 = male pin header, 13 pins [form="♂ (male)"]
  RSSI1 = male pin header, 13 pins [form="♂ (male)"]
  Xbee4 = SSCI-KIT-XBSOCKET
  ICSP5 = Arduino R3 6pin male header [package=THT]  # not connected
  IOH12 = female pin header, 10 pins [form="♀ (female)"]
  J129 = male pin header, 13 pins [form="♂ (male)"]
  J130 = male pin header, 13 pins [form="♂ (male)"]
  J131 = male pin header, 13 pins [form="♂ (male)"]
  J132 = male pin header, 13 pins [form="♂ (male)"]
  ON/Sleep1 = male pin header, 15 pins [form="♂ (male)"]
  Reset4 = male pin header, 13 pins [form="♂ (male)"]
  Associate1 = male pin header, 13 pins [form="♂ (male)"]
  Sleep_RQ1 = male pin header, 13 pins [form="♂ (male)"]
  Rx7 = male pin header, 15 pins [form="♂ (male)"]
  J133 = male pin header, 15 pins [form="♂ (male)"]
  Tx7 = male pin header, 15 pins [form="♂ (male)"]
  J134 = male pin header, 15 pins [form="♂ (male)"]
  IOL12 = female pin header, 8 pins [form="♀ (female)"]
  Power12 = female pin header, 8 pins [form="♀ (female)"]
  AD12 = female pin header, 6 pins [form="♀ (female)"]
  J135 = male pin header, 3 pins [form="♂ (male)"]
  J136 = male pin header, 3 pins [form="♂ (male)"]
  J137 = male pin header, 3 pins [form="♂ (male)"]
  S3 = Akizuki slide switch IS-2235
  Card_detect1 = male pin header, 12 pins [form="♂ (male)"]
  J138 = male pin header, 12 pins [form="♂ (male)"]
  Chip_select1 = male pin header, 12 pins [form="♂ (male)"]
  J139 = male pin header, 12 pins [form="♂ (male)"]
  ICSP6 = Arduino R3 6pin male header [package=THT]
  IOH13 = female pin header, 10 pins [form="♀ (female)"]
  IOL13 = female pin header, 8 pins [form="♀ (female)"]
  POWER1 = female pin header, 8 pins [form="♀ (female)"]
  AD13 = female pin header, 6 pins [form="♀ (female)"]  # not connected
  microSD1 = MicroSD Breakout
  U1 = RELAY-G6L [package=1P]
  パーツ2 = Arduino Mega 2560 (Rev3)  # not connected
  J140 = male pin header, 22 pins [form="♂ (male)"]
  INT7 = male pin header, 22 pins [form="♂ (male)"]
  AD14 = female pin header, 8 pins [form="♀ (female)"]  # not connected
  S4 = Akizuki slide switch IS-2235
  RTC7 = RTC-8564NB [package="Module(DIP 8P)"]
  SW3 = Akizuki slide switch IS-1250
  ICSP7 = Arduino R3 6pin male header [package=THT]  # not connected
  D15 = Schottky Diode [part_number=1N5817 package="300 mil [THT]"]
  D16 = Schottky Diode [part_number=1N5817 package="300 mil [THT]"]
  IO6 = female pin header, 10 pins [form="♀ (female)"]
  IO7 = female pin header, 8 pins [form="♀ (female)"]
  Power13 = female pin header, 8 pins [form="♀ (female)"]
  BAT7 = Battery Holders [package=battcom_20mm_pth]
  IO8 = female pin header, 8 pins [form="♀ (female)"]
  AD15 = female pin header, 8 pins [form="♀ (female)"]  # not connected
  IO9 = female pin header, 18 pins [form="♀ (female)"]  # not connected
  IO10 = female pin header, 18 pins [form="♀ (female)"]  # not connected
  IO11 = female pin header, 8 pins [form="♀ (female)"]
  AD16 = female pin header, 8 pins [form="♀ (female)"]  # not connected
  IO12 = female pin header, 18 pins [form="♀ (female)"]  # not connected
  IO13 = female pin header, 18 pins [form="♀ (female)"]  # not connected
  S5 = Akizuki slide switch IS-2235
  microSD2 = MicroSD Breakout
  Card_detect2 = male pin header, 24 pins [form="♂ (male)"]
  J141 = male pin header, 24 pins [form="♂ (male)"]
  Chip_select2 = male pin header, 24 pins [form="♂ (male)"]
  J142 = male pin header, 24 pins [form="♂ (male)"]
  ICSP8 = Arduino R3 6pin male header [package=THT]
  IO14 = female pin header, 10 pins [form="♀ (female)"]
  IO15 = female pin header, 8 pins [form="♀ (female)"]
  POWER2 = female pin header, 8 pins [form="♀ (female)"]
  AD17 = female pin header, 8 pins [form="♀ (female)"]  # not connected
  ICSP9 = Arduino R3 6pin male header [package=THT]  # not connected
  Power_IN3 = Grove Header 4pin 90 degree direct mount [package="90 degree"]
  Signal_IN3 = Grove Header 4pin 90 degree direct mount [package="90 degree"]
  LevelConverter3 = Bi-Directional Logic Level Converter [part_number=BOB-12009]
  IO16 = female pin header, 10 pins [form="♀ (female)"]
  Shutdown5 = male pin header, 24 pins [form="♂ (male)"]
  J143 = male pin header, 24 pins [form="♂ (male)"]
  Rx8 = male pin header, 24 pins [form="♂ (male)"]
  J144 = male pin header, 24 pins [form="♂ (male)"]
  Tx8 = male pin header, 24 pins [form="♂ (male)"]
  J145 = male pin header, 24 pins [form="♂ (male)"]
  IO17 = female pin header, 8 pins [form="♀ (female)"]
  Power14 = female pin header, 8 pins [form="♀ (female)"]
  IO18 = female pin header, 18 pins [form="♀ (female)"]  # not connected
  IO19 = female pin header, 18 pins [form="♀ (female)"]  # not connected
  IO20 = female pin header, 8 pins [form="♀ (female)"]
  ADL1 = female pin header, 8 pins [form="♀ (female)"]  # not connected
  ADH1 = female pin header, 8 pins [form="♀ (female)"]  # not connected
  Grove4 = Grove 3 Axis Digital Accelerometer 16g  # not connected
  Grove5 = Grove Infrared Emitter  # not connected
  Grove6 = Grove 3 Axis Digital Accelerometer 16g  # not connected

nets:
  N1: Pro_Mini_3V3_8MHz1.D0/TX, IOL2.pin8
  N2: Pro_Mini_3V3_8MHz1.D1/RX, IOL2.pin7
  N3: Pro_Mini_3V3_8MHz1.VCC, S2.pin1, S2.pin4
  GND: Pro_Mini_3V3_8MHz1.GND, Power_plug6.GND, Reset1.4, IOH2.pin4, Power2.pin6, Power2.pin7
  N4: Pro_Mini_3V3_8MHz1.A4, AD2.pin5
  N5: Pro_Mini_3V3_8MHz1.A5, AD2.pin6
  N6: Pro_Mini_3V3_8MHz1.RAW, Power_plug6.VCC, Power2.pin8
  N7: Pro_Mini_3V3_8MHz1.RESET, Reset1.2, Power2.pin3
  N8: Pro_Mini_3V3_8MHz1.A3, AD2.pin4
  N9: Pro_Mini_3V3_8MHz1.A2, AD2.pin3
  N10: Pro_Mini_3V3_8MHz1.A1, AD2.pin2
  N11: Pro_Mini_3V3_8MHz1.A0, AD2.pin1
  N12: Pro_Mini_3V3_8MHz1.D13/SCK, IOH2.pin5
  N13: Pro_Mini_3V3_8MHz1.D12/MISO, IOH2.pin6
  N14: Pro_Mini_3V3_8MHz1.D11_PWM/MOSI, IOH2.pin7
  N15: Pro_Mini_3V3_8MHz1.D10_PWM/SS, IOH2.pin8
  N16: Pro_Mini_3V3_8MHz1.D9_PWM, IOH2.pin9
  N17: Pro_Mini_3V3_8MHz1.D8, IOH2.pin10
  N18: Pro_Mini_3V3_8MHz1.D7, IOL2.pin1
  N19: Pro_Mini_3V3_8MHz1.D6_PWM, IOL2.pin2
  N20: Pro_Mini_3V3_8MHz1.D5_PWM, IOL2.pin3
  N21: Pro_Mini_3V3_8MHz1.D4, IOL2.pin4
  N22: Pro_Mini_3V3_8MHz1.D3_PWM, IOL2.pin5
  N23: Pro_Mini_3V3_8MHz1.D2, IOL2.pin6
  N24: S2.pin0, S2.pin3, Power2.pin4
  N25: S2.pin2, S2.pin5, Power2.pin5
  N26: SCL3.pin1, IOH8.pin1
  N27: SCL3.pin2, J117.pin8, IOL8.pin1
  N28: SCL3.pin3, AD8.pin6
  N29: SCL4.pin1, SCL4.pin2, SCL4.pin3, RTC5.SCL
  N30: SDA3.pin1, IOH8.pin2
  N31: SDA3.pin2, IOH8.pin10, J117.pin6
  N32: SDA3.pin3, AD8.pin5
  N33: SDA4.pin1, SDA4.pin2, SDA4.pin3, RTC5.SDA
  N34: RTC5.INT, INT5.pin1, INT5.pin2, INT5.pin3, INT5.pin4, INT5.pin5, INT5.pin6, INT5.pin7, INT5.pin8, INT5.pin9, INT5.pin10, INT5.pin11, INT5.pin12, INT5.pin13, INT5.pin14, INT5.pin15
  N35: RTC5.GND, IOH8.pin4, Power8.pin6, Power8.pin7, BAT5.-
  N36: RTC5.VDD, D11.cathode, D12.cathode
  N37: SW1.pin0, SW1.pin3, Power8.pin5
  N38: SW1.pin1, SW1.pin4, D12.anode
  N39: SW1.pin2, SW1.pin5, Power8.pin4
  N40: D11.anode, BAT5.+
  N41: IOH8.pin5, J117.pin1
  N42: IOH8.pin6, J117.pin2
  N43: IOH8.pin7, J117.pin3
  N44: IOH8.pin8, J117.pin4
  N45: IOH8.pin9, J117.pin5
  N46: J117.pin9, IOL8.pin2
  N47: J117.pin10, IOL8.pin3
  N48: J117.pin11, IOL8.pin4
  N49: J117.pin12, IOL8.pin5
  N50: J117.pin13, IOL8.pin6
  N51: J117.pin14, IOL8.pin7
  N52: J117.pin15, IOL8.pin8
  N53: Power_IN2.2, LevelConverter2.LV
  N54: Power_IN2.3, Power9.pin8
  N55: Power_IN2.4, LevelConverter2.GND, IOH9.pin4, Power9.pin6, Power9.pin7
  N56: Signal_IN2.1, LevelConverter2.LV4
  N57: Signal_IN2.2, LevelConverter2.LV3
  N58: Signal_IN2.3, LevelConverter2.LV2
  N59: Signal_IN2.4, LevelConverter2.LV1
  N60: LevelConverter2.HV4, Power9.pin3
  N61: LevelConverter2.HV3, Shutdown3.pin1, Shutdown3.pin2, Shutdown3.pin3, Shutdown3.pin4, Shutdown3.pin5, Shutdown3.pin6, Shutdown3.pin7, Shutdown3.pin8, Shutdown3.pin9, Shutdown3.pin10, Shutdown3.pin11, Shutdown3.pin12, Shutdown3.pin13, Shutdown3.pin14, Shutdown3.pin15
  N62: LevelConverter2.HV, Power9.pin5
  N63: LevelConverter2.HV2, Rx5.pin1, Rx5.pin2, Rx5.pin3, Rx5.pin4, Rx5.pin5, Rx5.pin6, Rx5.pin7, Rx5.pin8, Rx5.pin9, Rx5.pin10, Rx5.pin11, Rx5.pin12, Rx5.pin13, Rx5.pin14, Rx5.pin15
  N64: LevelConverter2.HV1, Tx5.pin1, Tx5.pin2, Tx5.pin3, Tx5.pin4, Tx5.pin5, Tx5.pin6, Tx5.pin7, Tx5.pin8, Tx5.pin9, Tx5.pin10, Tx5.pin11, Tx5.pin12, Tx5.pin13, Tx5.pin14, Tx5.pin15
  N65: IOH9.pin5, J118.pin1, J119.pin1, J120.pin1
  N66: IOH9.pin6, J118.pin2, J119.pin2, J120.pin2
  N67: IOH9.pin7, J118.pin3, J119.pin3, J120.pin3
  N68: IOH9.pin8, J118.pin4, J119.pin4, J120.pin4
  N69: IOH9.pin9, J118.pin5, J119.pin5, J120.pin5
  N70: IOH9.pin10, J118.pin6, J119.pin6, J120.pin6
  N71: J118.pin8, J119.pin8, J120.pin8, IOL9.pin1
  N72: J118.pin9, J119.pin9, J120.pin9, IOL9.pin2
  N73: J118.pin10, J119.pin10, J120.pin10, IOL9.pin3
  N74: J118.pin11, J119.pin11, J120.pin11, IOL9.pin4
  N75: J118.pin12, J119.pin12, J120.pin12, IOL9.pin5
  N76: J118.pin13, J119.pin13, J120.pin13, IOL9.pin6
  N77: J118.pin14, J119.pin14, J120.pin14, IOL9.pin7
  N78: J118.pin15, J119.pin15, J120.pin15, IOL9.pin8
  N79: Signal_OUT2.1, Reset3.pin1, Reset3.pin2, Reset3.pin3, Reset3.pin4, Reset3.pin5, Reset3.pin6, Reset3.pin7, Reset3.pin8, Reset3.pin9, Reset3.pin10, Reset3.pin11, Reset3.pin12, Reset3.pin13
  N80: Signal_OUT2.2, Shutdown4.pin1, Shutdown4.pin2, Shutdown4.pin3, Shutdown4.pin4, Shutdown4.pin5, Shutdown4.pin6, Shutdown4.pin7, Shutdown4.pin8, Shutdown4.pin9, Shutdown4.pin10, Shutdown4.pin11, Shutdown4.pin12, Shutdown4.pin13
  N81: Signal_OUT2.3, Rx6.pin1, Rx6.pin2, Rx6.pin3, Rx6.pin4, Rx6.pin5, Rx6.pin6, Rx6.pin7, Rx6.pin8, Rx6.pin9, Rx6.pin10, Rx6.pin11, Rx6.pin12, Rx6.pin13, Rx6.pin14, Rx6.pin15
  N82: Signal_OUT2.4, Tx6.pin1, Tx6.pin2, Tx6.pin3, Tx6.pin4, Tx6.pin5, Tx6.pin6, Tx6.pin7, Tx6.pin8, Tx6.pin9, Tx6.pin10, Tx6.pin11, Tx6.pin12, Tx6.pin13, Tx6.pin14, Tx6.pin15
  N83: Power_OUT2.2, Power10.pin4
  N84: Power_OUT2.3, U1.SIO#0
  N85: Power_OUT2.4, IOH10.pin4, Power10.pin6, Power10.pin7, U1.CIO#2
  N86: IOH10.pin5, J121.pin1, J122.pin1, J123.pin1, J124.pin1, J125.pin1
  N87: IOH10.pin6, J121.pin2, J122.pin2, J123.pin2, J124.pin2, J125.pin2
  N88: IOH10.pin7, J121.pin3, J122.pin3, J123.pin3, J124.pin3, J125.pin3
  N89: IOH10.pin8, J121.pin4, J122.pin4, J123.pin4, J124.pin4, J125.pin4
  N90: IOH10.pin9, J122.pin5, J124.pin5, J125.pin5
  N91: IOH10.pin10, J121.pin6, J122.pin6, J123.pin6, J124.pin6, J125.pin6
  N92: J121.pin5, J123.pin5
  N93: J121.pin8, J122.pin8, J123.pin8, J124.pin8, J125.pin8, IOL10.pin1
  N94: J121.pin9, J122.pin9, J123.pin9, J124.pin9, J125.pin9, IOL10.pin2
  N95: J121.pin10, J122.pin10, J123.pin10, J124.pin10, J125.pin10, IOL10.pin3
  N96: J121.pin11, J122.pin11, J123.pin11, J124.pin11, J125.pin11, IOL10.pin4
  N97: J121.pin12, J122.pin12, J123.pin12, J124.pin12, J125.pin12, IOL10.pin5
  N98: J121.pin13, J122.pin13, J123.pin13, J124.pin13, J125.pin13, IOL10.pin6
  N99: RelayControl2.pin1, RelayControl2.pin2, RelayControl2.pin3, RelayControl2.pin4, RelayControl2.pin5, RelayControl2.pin6, RelayControl2.pin7, RelayControl2.pin8, RelayControl2.pin9, RelayControl2.pin10, RelayControl2.pin11, RelayControl2.pin12, RelayControl2.pin13, U1.CIO#1
  N100: J124.pin14, J125.pin14, IOL10.pin7
  N101: J124.pin15, J125.pin15, IOL10.pin8
  N102: Power10.pin8, U1.SIO#3
  N103: SCL5.pin1, IOH11.pin1
  N104: SCL5.pin2, J126.pin8, IOL11.pin1
  N105: SCL5.pin3, AD11.pin6
  N106: SCL6.pin1, SCL6.pin2, SCL6.pin3, RTC6.SCL
  N107: SDA5.pin1, IOH11.pin2
  N108: SDA5.pin2, IOH11.pin10, J126.pin6
  N109: SDA5.pin3, AD11.pin5
  N110: SDA6.pin1, SDA6.pin2, SDA6.pin3, RTC6.SDA
  N111: RTC6.INT, INT6.pin1, INT6.pin2, INT6.pin3, INT6.pin4, INT6.pin5, INT6.pin6, INT6.pin7, INT6.pin8, INT6.pin9, INT6.pin10, INT6.pin11, INT6.pin12, INT6.pin13, INT6.pin14, INT6.pin15
  N112: RTC6.GND, IOH11.pin4, Power11.pin6, Power11.pin7, BAT6.-
  N113: RTC6.VDD, D13.cathode, D14.cathode
  N114: SW2.pin0, SW2.pin3, Power11.pin5
  N115: SW2.pin1, SW2.pin4, D14.anode
  N116: SW2.pin2, SW2.pin5, Power11.pin4
  N117: D13.anode, BAT6.+
  N118: IOH11.pin5, J126.pin1
  N119: IOH11.pin6, J126.pin2
  N120: IOH11.pin7, J126.pin3
  N121: IOH11.pin8, J126.pin4
  N122: IOH11.pin9, J126.pin5
  N123: J126.pin9, IOL11.pin2
  N124: J126.pin10, IOL11.pin3
  N125: J126.pin11, IOL11.pin4
  N126: J126.pin12, IOL11.pin5
  N127: J126.pin13, IOL11.pin6
  N128: J126.pin14, IOL11.pin7
  N129: J126.pin15, IOL11.pin8
  N130: J127.pin1, AD12.pin1
  N131: J127.pin2, AD12.pin2
  N132: J127.pin3, AD12.pin3
  N133: J127.pin4, AD12.pin4
  N134: J127.pin5, AD12.pin5
  N135: J127.pin6, AD12.pin6
  N136: J128.pin1, IOH12.pin5, J129.pin1, J130.pin1, J131.pin1, J132.pin1, J133.pin1, J134.pin1
  N137: J128.pin2, IOH12.pin6, J129.pin2, J130.pin2, J131.pin2, J132.pin2, J133.pin2, J134.pin2
  N138: J128.pin3, IOH12.pin7, J129.pin3, J130.pin3, J131.pin3, J132.pin3, J133.pin3, J134.pin3
  N139: J128.pin4, IOH12.pin8, J129.pin4, J130.pin4, J131.pin4, J132.pin4, J133.pin4, J134.pin4
  N140: J128.pin5, IOH12.pin9, J129.pin5, J130.pin5, J131.pin5, J132.pin5, J133.pin5, J134.pin5
  N141: J128.pin6, IOH12.pin10, J129.pin6, J130.pin6, J131.pin6, J132.pin6, J133.pin6, J134.pin6
  N142: J128.pin8, J129.pin8, J131.pin8, J132.pin8, J133.pin8, J134.pin8, IOL12.pin1
  N143: J128.pin9, J129.pin9, J130.pin9, J131.pin9, J132.pin9, J133.pin9, J134.pin9, IOL12.pin2
  N144: J128.pin10, J129.pin10, J130.pin10, J131.pin10, J132.pin10, J133.pin10, J134.pin10, IOL12.pin3
  N145: J128.pin11, J129.pin11, J130.pin11, J131.pin11, J132.pin11, J133.pin11, J134.pin11, IOL12.pin4
  N146: J128.pin12, J129.pin12, J130.pin12, J131.pin12, J132.pin12, J133.pin12, J134.pin12, IOL12.pin5
  N147: J128.pin13, J129.pin13, J130.pin13, J131.pin13, J132.pin13, J133.pin13, J134.pin13, IOL12.pin6
  N148: RSSI1.pin1, RSSI1.pin2, RSSI1.pin3, RSSI1.pin4, RSSI1.pin5, RSSI1.pin6, RSSI1.pin7, RSSI1.pin8, RSSI1.pin9, RSSI1.pin10, RSSI1.pin11, RSSI1.pin12, RSSI1.pin13, Xbee4.pin6
  N149: Xbee4.VCC, Power12.pin4
  N150: Xbee4.pin2, Tx7.pin1, Tx7.pin2, Tx7.pin3, Tx7.pin4, Tx7.pin5, Tx7.pin6, Tx7.pin7, Tx7.pin8, Tx7.pin9, Tx7.pin10, Tx7.pin11, Tx7.pin12, Tx7.pin13, Tx7.pin14, Tx7.pin15
  N151: Xbee4.pin3, Rx7.pin1, Rx7.pin2, Rx7.pin3, Rx7.pin4, Rx7.pin5, Rx7.pin6, Rx7.pin7, Rx7.pin8, Rx7.pin9, Rx7.pin10, Rx7.pin11, Rx7.pin12, Rx7.pin13, Rx7.pin14, Rx7.pin15
  N152: Xbee4.pin5, Reset4.pin1, Reset4.pin2, Reset4.pin3, Reset4.pin4, Reset4.pin5, Reset4.pin6, Reset4.pin7, Reset4.pin8, Reset4.pin9, Reset4.pin10, Reset4.pin11, Reset4.pin12, Reset4.pin13
  N153: Xbee4.pin9, Sleep_RQ1.pin1, Sleep_RQ1.pin2, Sleep_RQ1.pin3, Sleep_RQ1.pin4, Sleep_RQ1.pin5, Sleep_RQ1.pin6, Sleep_RQ1.pin7, Sleep_RQ1.pin8, Sleep_RQ1.pin9, Sleep_RQ1.pin10, Sleep_RQ1.pin11, Sleep_RQ1.pin12, Sleep_RQ1.pin13
  N154: Xbee4.GND, IOH12.pin4, Power12.pin6, Power12.pin7
  N155: Xbee4.pin13, ON/Sleep1.pin1, ON/Sleep1.pin2, ON/Sleep1.pin3, ON/Sleep1.pin4, ON/Sleep1.pin5, ON/Sleep1.pin6, ON/Sleep1.pin7, ON/Sleep1.pin8, ON/Sleep1.pin9, ON/Sleep1.pin10, ON/Sleep1.pin11, ON/Sleep1.pin12, ON/Sleep1.pin13, ON/Sleep1.pin14, ON/Sleep1.pin15
  N156: Xbee4.pin15, Associate1.pin1, Associate1.pin2, Associate1.pin3, Associate1.pin4, Associate1.pin5, Associate1.pin6, Associate1.pin7, Associate1.pin8, Associate1.pin9, Associate1.pin10, Associate1.pin11, Associate1.pin12, Associate1.pin13
  N157: J133.pin14, J134.pin14, IOL12.pin7
  N158: J133.pin15, J134.pin15, IOL12.pin8
  N159: J135.pin1, IOH13.pin7
  N160: J135.pin2, IOH13.pin6
  N161: J135.pin3, IOH13.pin5
  N162: J136.pin1, microSD1.DI
  N163: J136.pin2, microSD1.DO
  N164: J136.pin3, microSD1.CLK
  N165: J137.pin1, ICSP6.pin5
  N166: J137.pin2, ICSP6.pin1
  N167: J137.pin3, ICSP6.pin2
  N168: S3.pin0, POWER1.pin5
  N169: S3.pin1, microSD1.5V
  N170: S3.pin4, microSD1.3v
  N171: S3.pin5, POWER1.pin4
  N172: Card_detect1.pin1, Card_detect1.pin2, Card_detect1.pin3, Card_detect1.pin4, Card_detect1.pin5, Card_detect1.pin6, Card_detect1.pin7, Card_detect1.pin8, Card_detect1.pin9, Card_detect1.pin10, Card_detect1.pin11, Card_detect1.pin12, microSD1.CD
  N173: J138.pin1, J139.pin1, IOH13.pin8
  N174: J138.pin2, J139.pin2, IOH13.pin9
  N175: J138.pin3, J139.pin3, IOH13.pin10
  N176: J138.pin5, J139.pin5, IOL13.pin1
  N177: J138.pin6, J139.pin6, IOL13.pin2
  N178: J138.pin7, J139.pin7, IOL13.pin3
  N179: J138.pin8, J139.pin8, IOL13.pin4
  N180: J138.pin9, J139.pin9, IOL13.pin5
  N181: J138.pin10, J139.pin10, IOL13.pin6
  N182: J138.pin11, J139.pin11, IOL13.pin7
  N183: J138.pin12, J139.pin12, IOL13.pin8
  N184: Chip_select1.pin1, Chip_select1.pin2, Chip_select1.pin3, Chip_select1.pin4, Chip_select1.pin5, Chip_select1.pin6, Chip_select1.pin7, Chip_select1.pin8, Chip_select1.pin9, Chip_select1.pin10, Chip_select1.pin11, Chip_select1.pin12, microSD1.CS
  N185: IOH13.pin4, POWER1.pin6, POWER1.pin7, microSD1.GND
  N186: J140.pin1, IO6.pin5
  N187: J140.pin2, IO6.pin6
  N188: J140.pin3, IO6.pin7
  N189: J140.pin4, IO6.pin8
  N190: J140.pin5, IO6.pin9
  N191: J140.pin6, IO6.pin10
  N192: J140.pin8, IO7.pin1
  N193: J140.pin9, IO7.pin2
  N194: J140.pin10, IO7.pin3
  N195: J140.pin11, IO7.pin4
  N196: J140.pin12, IO7.pin5
  N197: J140.pin13, IO7.pin6
  N198: J140.pin14, IO7.pin7
  N199: J140.pin15, IO7.pin8
  N200: J140.pin17, IO8.pin1
  N201: J140.pin18, IO8.pin2
  N202: J140.pin19, IO8.pin3
  N203: J140.pin20, IO8.pin4
  N204: J140.pin21, IO8.pin5
  N205: J140.pin22, IO8.pin6
  N206: INT7.pin1, INT7.pin2, INT7.pin3, INT7.pin4, INT7.pin5, INT7.pin6, INT7.pin7, INT7.pin8, INT7.pin9, INT7.pin10, INT7.pin11, INT7.pin12, INT7.pin13, INT7.pin14, INT7.pin15, INT7.pin16, INT7.pin17, INT7.pin18, INT7.pin19, INT7.pin20, INT7.pin21, INT7.pin22, RTC7.INT
  N207: S4.pin0, IO8.pin8
  N208: S4.pin1, RTC7.SCL
  N209: S4.pin2, IO6.pin1
  N210: S4.pin3, IO8.pin7
  N211: S4.pin4, RTC7.SDA
  N212: S4.pin5, IO6.pin2
  N213: RTC7.GND, IO6.pin4, Power13.pin6, Power13.pin7, BAT7.-
  N214: RTC7.VDD, D15.cathode, D16.cathode
  N215: SW3.pin0, SW3.pin3, Power13.pin5
  N216: SW3.pin1, SW3.pin4, D16.anode
  N217: SW3.pin2, SW3.pin5, Power13.pin4
  N218: D15.anode, BAT7.+
  N219: IO11.pin1, J141.pin17, J142.pin17
  N220: IO11.pin2, J141.pin18, J142.pin18
  N221: IO11.pin3, J141.pin19, J142.pin19
  N222: IO11.pin4, J141.pin20, J142.pin20
  N223: IO11.pin5, J141.pin21, J142.pin21
  N224: IO11.pin6, J141.pin22, J142.pin22
  N225: IO11.pin7, J141.pin23, J142.pin23
  N226: IO11.pin8, J141.pin24, J142.pin24
  N227: S5.pin0, POWER2.pin5
  N228: S5.pin1, microSD2.5V
  N229: S5.pin3, S5.pin4, microSD2.3v
  N230: S5.pin5, POWER2.pin4
  N231: microSD2.CD, Card_detect2.pin1, Card_detect2.pin2, Card_detect2.pin3, Card_detect2.pin4, Card_detect2.pin5, Card_detect2.pin6, Card_detect2.pin7, Card_detect2.pin8, Card_detect2.pin9, Card_detect2.pin10, Card_detect2.pin11, Card_detect2.pin12, Card_detect2.pin13, Card_detect2.pin14, Card_detect2.pin15, Card_detect2.pin16, Card_detect2.pin17, Card_detect2.pin18, Card_detect2.pin19, Card_detect2.pin20, Card_detect2.pin21, Card_detect2.pin22, Card_detect2.pin23, Card_detect2.pin24
  N232: microSD2.CS, Chip_select2.pin1, Chip_select2.pin2, Chip_select2.pin3, Chip_select2.pin4, Chip_select2.pin5, Chip_select2.pin6, Chip_select2.pin7, Chip_select2.pin8, Chip_select2.pin9, Chip_select2.pin10, Chip_select2.pin11, Chip_select2.pin12, Chip_select2.pin13, Chip_select2.pin14, Chip_select2.pin15, Chip_select2.pin16, Chip_select2.pin17, Chip_select2.pin18, Chip_select2.pin19, Chip_select2.pin20, Chip_select2.pin21, Chip_select2.pin22, Chip_select2.pin23, Chip_select2.pin24
  N233: microSD2.DI, ICSP8.pin5
  N234: microSD2.DO, ICSP8.pin1
  N235: microSD2.CLK, ICSP8.pin2
  N236: microSD2.GND, IO14.pin4, POWER2.pin6, POWER2.pin7
  N237: J141.pin1, J142.pin1, IO14.pin5
  N238: J141.pin2, J142.pin2, IO14.pin6
  N239: J141.pin3, J142.pin3, IO14.pin7
  N240: J141.pin4, J142.pin4, IO14.pin8
  N241: J141.pin5, J142.pin5, IO14.pin9
  N242: J141.pin6, J142.pin6, IO14.pin10
  N243: J141.pin8, J142.pin8, IO15.pin1
  N244: J141.pin9, J142.pin9, IO15.pin2
  N245: J141.pin10, J142.pin10, IO15.pin3
  N246: J141.pin11, J142.pin11, IO15.pin4
  N247: J141.pin12, J142.pin12, IO15.pin5
  N248: J141.pin13, J142.pin13, IO15.pin6
  N249: J141.pin14, J142.pin14, IO15.pin7
  N250: J141.pin15, J142.pin15, IO15.pin8
  N251: Power_IN3.2, LevelConverter3.LV
  N252: Power_IN3.3, Power14.pin8
  N253: Power_IN3.4, LevelConverter3.GND, IO16.pin4, Power14.pin6, Power14.pin7
  N254: Signal_IN3.1, LevelConverter3.LV4
  N255: Signal_IN3.2, LevelConverter3.LV3
  N256: Signal_IN3.3, LevelConverter3.LV2
  N257: Signal_IN3.4, LevelConverter3.LV1
  N258: LevelConverter3.HV4, Power14.pin3
  N259: LevelConverter3.HV3, Shutdown5.pin1, Shutdown5.pin2, Shutdown5.pin3, Shutdown5.pin4, Shutdown5.pin5, Shutdown5.pin6, Shutdown5.pin7, Shutdown5.pin8, Shutdown5.pin9, Shutdown5.pin10, Shutdown5.pin11, Shutdown5.pin12, Shutdown5.pin13, Shutdown5.pin14, Shutdown5.pin15, Shutdown5.pin16, Shutdown5.pin17, Shutdown5.pin18, Shutdown5.pin19, Shutdown5.pin20, Shutdown5.pin21, Shutdown5.pin22, Shutdown5.pin23, Shutdown5.pin24
  N260: LevelConverter3.HV, Power14.pin5
  N261: LevelConverter3.HV2, Rx8.pin1, Rx8.pin2, Rx8.pin3, Rx8.pin4, Rx8.pin5, Rx8.pin6, Rx8.pin7, Rx8.pin8, Rx8.pin9, Rx8.pin10, Rx8.pin11, Rx8.pin12, Rx8.pin13, Rx8.pin14, Rx8.pin15, Rx8.pin16, Rx8.pin17, Rx8.pin18, Rx8.pin19, Rx8.pin20, Rx8.pin21, Rx8.pin22, Rx8.pin23, Rx8.pin24
  N262: LevelConverter3.HV1, Tx8.pin1, Tx8.pin2, Tx8.pin3, Tx8.pin4, Tx8.pin5, Tx8.pin6, Tx8.pin7, Tx8.pin8, Tx8.pin9, Tx8.pin10, Tx8.pin11, Tx8.pin12, Tx8.pin13, Tx8.pin14, Tx8.pin15, Tx8.pin16, Tx8.pin17, Tx8.pin18, Tx8.pin19, Tx8.pin20, Tx8.pin21, Tx8.pin22, Tx8.pin23, Tx8.pin24
  N263: IO16.pin5, J143.pin1, J144.pin1, J145.pin1
  N264: IO16.pin6, J143.pin2, J144.pin2, J145.pin2
  N265: IO16.pin7, J143.pin3, J144.pin3, J145.pin3
  N266: IO16.pin8, J143.pin4, J144.pin4, J145.pin4
  N267: IO16.pin9, J143.pin5, J144.pin5, J145.pin5
  N268: IO16.pin10, J143.pin6, J144.pin6, J145.pin6
  N269: J143.pin8, J144.pin8, J145.pin8, IO17.pin1
  N270: J143.pin9, J144.pin9, J145.pin9, IO17.pin2
  N271: J143.pin10, J144.pin10, J145.pin10, IO17.pin3
  N272: J143.pin11, J144.pin11, J145.pin11, IO17.pin4
  N273: J143.pin12, J144.pin12, J145.pin12, IO17.pin5
  N274: J143.pin13, J144.pin13, J145.pin13, IO17.pin6
  N275: J143.pin14, J144.pin14, J145.pin14, IO17.pin7
  N276: J143.pin15, J144.pin15, J145.pin15, IO17.pin8
  N277: J143.pin17, J144.pin17, J145.pin17, IO20.pin1
  N278: J143.pin18, J144.pin18, J145.pin18, IO20.pin2
  N279: J143.pin19, J144.pin19, J145.pin19, IO20.pin3
  N280: J143.pin20, J144.pin20, J145.pin20, IO20.pin4
  N281: J143.pin21, J144.pin21, J145.pin21, IO20.pin5
  N282: J143.pin22, J144.pin22, J145.pin22, IO20.pin6
  N283: J143.pin23, J144.pin23, J145.pin23, IO20.pin7
  N284: J143.pin24, J144.pin24, J145.pin24, IO20.pin8

notes:
  電源制御回路
  アプリケーションプロセッサ
  UNO版
  MEGA版
  電源制御回路から，電源を供給され，センサ処理を時刻情報付きで，マイクロSDに保存すると共に，電源制御回路に送る．
  通常眠っているMCUがRTCやXbeeからの割り込みで起き，リレーを制御して，アプリケーションプロセッサに電源を供給する．
  シリアルでアプリケーションプロセッサの処理結果を受け取り，Xbeeを経由して外部に送信する．
  後始末として，リレーをOFFして，アプリプロセッサの電源を落とし，Xbeeを眠らせる(RTCで起きる場合)．

custom parts:
  Arduino Pro Mini v13: It's blue! It's thin! It's the Arduino Pro Mini! SparkFun's minimal design approach to Arduino. This is a 5V Arduino running the 16MHz bootloader. Arduino Pro Mini does not come with connectors populated so that you can solder in any connector or wire with any orientation you need. We recommend first time Arduino users start with the Uno R3. It's a great board that will get you up and running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
  Akizuki slide switch IS-1250: Akizuki slide switch is-1250 (P-01665)
  Power plug: 秋月電子通商 AE-DCJACK-DIPKIT-2.1mm-10A(通販コードK-06998)とその互換品(K06999,K-08415,K-08416)
  Arduino R3 6pin male header: Pin header for arduino R3
  RTC-8564NB: Real Time Clock Module and I2C-BUS interface method. This product is a module of the SON 8-pin DIP package. Supply voltage 1.8-5.5V original version by KimuShige
  Grove Header 4pin 90 degree direct mount: Header
  Bi-Directional Logic Level Converter: Description: If you've ever tried to connect a 3.3V device to a 5V system, you know what a challenge it can be. The SparkFun bi-directional logic level converter is a small device that safely steps down 5V signals to 3.3V AND steps up 3.3V to 5V at the same time. This level converter also works with 2.8V and 1.8V devices. What really separates this Logic level converter from our previous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
  SSCI-KIT-XBSOCKET: Xbee pin conversion
  Akizuki slide switch IS-2235: Akizuki slide switch is-2235 (P-02627)
  MicroSD Breakout: 5V-ready microSD Breakout with Level Shifter
  RELAY-G6L: OMRON G6L
