# Fritzing sketch arduino外部電源3V-UART (saved by Fritzing 0.9.2b)
perfboards: 4
breadboards: 5

parts:
  パーツ1 = Arduino Uno (Rev3)  # not connected
  パーツ2 = Arduino Pro Mini v13
  J5 = female pin header, 6 pins [form="♀ (female)"]  # not connected
  J3 = female pin header, 8 pins [form="♀ (female)"]  # not connected
  J6 = male pin header, 3 pins [form="♂ (male)"]  # not connected
  J7 = male pin header, 3 pins [form="♂ (male)"]  # not connected
  J2 = female pin header, 10 pins [form="♀ (female)"]  # not connected
  J8 = male pin header, 15 pins [form="♂ (male)"]  # not connected
  J13 = female pin header, 8 pins [form="♀ (female)"]
  パーツ6 = Bi-Directional Logic Level Converter [part_number=BOB-12009]
  J15 = female pin header, 5 pins [form="♀ (female)"]
  J14 = female pin header, 5 pins [form="♀ (female)"]
  J16 = female pin header, 2 pins [form="♀ (female)"]
  J17 = female pin header, 10 pins [form="♀ (female)"]  # not connected
  J18 = female pin header, 8 pins [form="♀ (female)"]  # not connected
  J19 = female pin header, 6 pins [form="♀ (female)"]
  J20 = female pin header, 8 pins [form="♀ (female)"]
  J21 = male pin header, 3 pins [form="♂ (male)"]  # not connected
  J22 = male pin header, 3 pins [form="♂ (male)"]  # not connected
  BAT2 = Battery Holders [package=battcom_20mm_pth]
  RTC2 = RTC-8564NB [package="Module(DIP 8P)"]
  J23 = male pin header, 15 pins [form="♂ (male)"]  # not connected
  D5 = Schottky Diode [part_number=1N5817 package="300 mil [THT]"]
  D6 = Schottky Diode [part_number=1N5817 package="300 mil [THT]"]
  U3 = XBEE-1 [package=xbee-1]
  J24 = male pin header, 15 pins [form="♂ (male)"]
  J25 = male pin header, 3 pins [form="♂ (male)"]  # not connected
  J26 = male pin header, 3 pins [form="♂ (male)"]  # not connected
  J27 = female pin header, 10 pins [form="♀ (female)"]  # not connected
  J29 = male pin header, 15 pins [form="♂ (male)"]  # not connected
  J30 = female pin header, 8 pins [form="♀ (female)"]  # not connected
  J31 = female pin header, 8 pins [form="♀ (female)"]
  J32 = female pin header, 6 pins [form="♀ (female)"]  # not connected
  J33 = male pin header, 2 pins [form="♂ (male)"]
  J34 = male pin header, 1 pin [form="♂ (male)"]
  J35 = male pin header, 1 pin [form="♂ (male)"]
  IC1 = SC16IS750 [package=qfn-24]  # not connected
  U4 = XBEE-1 [package=xbee-1]  # not connected
  J36 = female pin header, 10 pins [form="♀ (female)"]  # not connected
  J37 = female pin header, 8 pins [form="♀ (female)"]  # not connected
  J38 = female pin header, 6 pins [form="♀ (female)"]  # not connected
  J39 = female pin header, 8 pins [form="♀ (female)"]  # not connected
  J40 = female pin header, 10 pins [form="♀ (female)"]  # not connected
  J41 = female pin header, 8 pins [form="♀ (female)"]
  J42 = female pin header, 8 pins [form="♀ (female)"]
  J43 = female pin header, 6 pins [form="♀ (female)"]
  BAT3 = Battery Holders [package=battcom_20mm_pth]
  RTC3 = RTC-8564NB [package="Module(DIP 8P)"]
  D7 = Schottky Diode [part_number=1N5817 package="300 mil [THT]"]
  D8 = Schottky Diode [part_number=1N5817 package="300 mil [THT]"]
  Power_plug4 = AE-DC-POWER-JACK-DIP [part_number=AE-DC-POWER-JACK-DIP]
  J44 = female pin header, 6 pins [form="♀ (female)"]
  J45 = female pin header, 8 pins [form="♀ (female)"]
  J46 = female pin header, 8 pins [form="♀ (female)"]
  J47 = female pin header, 10 pins [form="♀ (female)"]
  J48 = male pin header, 3 pins [form="♂ (male)"]  # not connected
  J49 = male pin header, 3 pins [form="♂ (male)"]  # not connected
  J50 = female pin header, 10 pins [form="♀ (female)"]  # not connected
  J52 = male pin header, 15 pins [form="♂ (male)"]
  J53 = female pin header, 8 pins [form="♀ (female)"]  # not connected
  J54 = female pin header, 8 pins [form="♀ (female)"]
  J55 = female pin header, 6 pins [form="♀ (female)"]  # not connected
  J56 = female pin header, 10 pins [form="♀ (female)"]
  J57 = female pin header, 8 pins [form="♀ (female)"]
  J58 = female pin header, 6 pins [form="♀ (female)"]
  J59 = female pin header, 8 pins [form="♀ (female)"]
  J60 = male pin header, 15 pins [form="♂ (male)"]
  R1 = Resistor [tolerance=±5% resistance=1M package=THT]
  U7 = RELAY-2 [package=relay-g5v]
  R2 = Resistor [tolerance=±5% resistance=1M package=THT]
  U8 = RELAY-2 [package=relay-g5v]
  U9 = I2C/SPI-to-UART Breakout [package=UART]
  J64 = male pin header, 15 pins [form="♂ (male)"]
  J65 = male pin header, 15 pins [form="♂ (male)"]
  U12 = I2CSerial Breakout [package=UART]
  X1 = DB9 Connector [package=db9]
  J62 = female pin header, 4 pins [form="♀ (female)"]
  U13 = I2CSerial Breakout [package=UART]  # not connected
  X2 = DB9 Connector [package=db9]  # not connected
  J61 = female pin header, 4 pins [form="♀ (female)"]
  U14 = I2CSerial Breakout [package=UART]
  U15 = I2CSerial Breakout [package=UART]  # not connected
  U16 = I2C/SPI-to-UART Breakout [package=UART]  # not connected

nets:
  N1: パーツ2.A4, J44.pin5
  N2: パーツ2.A5, J44.pin6
  N3: パーツ2.RAW, Power_plug4.VCC#7, J46.pin8
  N4: パーツ2.GND, Power_plug4.GND#0, Power_plug4.GND#2, J46.pin6, J46.pin7, J47.pin4
  N5: パーツ2.RESET, J46.pin3
  N6: パーツ2.VCC, J46.pin4
  N7: パーツ2.A3, J44.pin4
  N8: パーツ2.A2, J44.pin3
  N9: パーツ2.A1, J44.pin2
  N10: パーツ2.A0, J44.pin1
  N11: パーツ2.D13/SCK, J47.pin5
  N12: パーツ2.D12/MISO, J47.pin6
  N13: パーツ2.D11_PWM/MOSI, J47.pin7
  N14: パーツ2.D10_PWM/SS, J47.pin8
  N15: パーツ2.D9_PWM, J47.pin9
  N16: パーツ2.D8, J47.pin10
  N17: パーツ2.D7, J45.pin1
  N18: パーツ2.D6_PWM, J45.pin2
  N19: パーツ2.D5_PWM, J45.pin3
  N20: パーツ2.D4, J45.pin4
  N21: パーツ2.D3_PWM, J45.pin5
  N22: パーツ2.D2, J45.pin6
  N23: パーツ2.D1/RX, J45.pin7
  N24: パーツ2.D0/TX, J45.pin8
  N25: J13.pin5, パーツ6.HV
  N26: J13.pin6, J13.pin7, パーツ6.GND, J15.pin5, J14.pin5
  N27: J13.pin8, J15.pin3, J14.pin3
  N28: パーツ6.LV1, J15.pin1, J14.pin1
  N29: パーツ6.LV2, J15.pin2, J14.pin2
  N30: パーツ6.LV, J15.pin4, J14.pin4
  N31: パーツ6.HV2, J16.pin2
  N32: パーツ6.HV1, J16.pin1
  N33: J19.pin5, RTC2.SDA
  N34: J19.pin6, RTC2.SCL
  N35: J20.pin5, D5.anode
  N36: J20.pin6, BAT2.-, RTC2.GND
  N37: BAT2.+, D6.anode
  N38: RTC2.INT, J24.pin1, J24.pin2, J24.pin3, J24.pin4, J24.pin5, J24.pin6, J24.pin7, J24.pin8, J24.pin9, J24.pin10, J24.pin11, J24.pin12, J24.pin13, J24.pin14, J24.pin15
  N39: RTC2.VDD, D5.cathode, D6.cathode
  N40: U3.VDD, J31.pin4
  N41: U3.DOUT, J33.pin2
  N42: U3.DIN, J33.pin1
  N43: U3.DIO12, J34.pin1
  N44: U3.RESET, J35.pin1
  N45: U3.DIO11, J31.pin3
  N46: U3.GND, J31.pin6
  N47: J41.pin6, RTC3.INT
  N48: J42.pin4, D8.anode
  N49: J42.pin6, J42.pin7, BAT3.-, RTC3.GND
  N50: J43.pin5, RTC3.SDA
  N51: J43.pin6, RTC3.SCL
  N52: BAT3.+, D7.anode
  N53: RTC3.VDD, D7.cathode, D8.cathode
  N54: J52.pin15, J64.pin15
  N55: J54.pin6, R2.Pin_0
  N56: J54.pin7, J62.pin1
  N57: J54.pin8, U7.5
  N58: J56.pin4, J59.pin6, J59.pin7, R1.Pin_0, U12.GND, U12.CD, X1.5, X1.9
  N59: J57.pin1, U8.9
  N60: J57.pin2, J61.pin2
  N61: J58.pin5, U12.SDA
  N62: J58.pin6, U12.SCL
  N63: J59.pin4, U12.3V3
  N64: J59.pin8, U8.1
  N65: J60.pin1, J60.pin2, J60.pin3, J60.pin4, J60.pin5, J60.pin6, J60.pin7, J60.pin8, J60.pin9, J60.pin10, J60.pin11, J60.pin12, J60.pin13, J60.pin14, J60.pin15, U7.9
  N66: R1.Pin_1, U8.2
  N67: U7.2, R2.Pin_1
  N68: U7.6, J62.pin2
  N69: U8.6, J61.pin4
  N70: U9.IO0, U9.IO5
  N71: J65.pin1, J65.pin2, J65.pin3, J65.pin4, J65.pin5, J65.pin6, J65.pin7, J65.pin8, J65.pin9, J65.pin10, J65.pin11, J65.pin12, J65.pin13, J65.pin14, J65.pin15, J62.pin4
  N72: U12.CTS, X1.3
  N73: U12.TX, X1.7
  N74: U12.RX, X1.8
  N75: U12.DSR, X1.1
  N76: U12.DTR, X1.6
  N77: U12.RI, X1.4
  N78: U12.RTS, X1.2
  N79: U14.GND, U14.CD

custom parts:
  Arduino Pro Mini v13: It's blue! It's thin! It's the Arduino Pro Mini! SparkFun's minimal design approach to Arduino. This is a 5V Arduino running the 16MHz bootloader. Arduino Pro Mini does not come with connectors populated so that you can solder in any connector or wire with any orientation you need. We recommend first time Arduino users start with the Uno R3. It's a great board that will get you up and running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
  Bi-Directional Logic Level Converter: Description: If you've ever tried to connect a 3.3V device to a 5V system, you know what a challenge it can be. The SparkFun bi-directional logic level converter is a small device that safely steps down 5V signals to 3.3V AND steps up 3.3V to 5V at the same time. This level converter also works with 2.8V and 1.8V devices. What really separates this Logic level converter from our previous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
  RTC-8564NB: Real Time Clock Module and I2C-BUS interface method. This product is a module of the SON 8-pin DIP package. Supply voltage 1.8-5.5V
  AE-DC-POWER-JACK-DIP: 秋月電子通商 K-05148
  I2C/SPI-to-UART Breakout: SparkFun I2C/SPI-to-UART Breakout - SC16IS750 BOB-09981
  I2CSerial Breakout: SC16IS750 Serial-I2C/SPI Breakout
