# Fritzing sketch arduino外部電源3V-シリアル (saved by Fritzing 0.9.2b)
perfboards: 5
breadboards: 5

parts:
  パーツ1 = Arduino Uno (Rev3)  # not connected
  パーツ2 = Arduino Pro Mini v13
  J5 = female pin header, 6 pins [form="♀ (female)"]  # not connected
  J3 = female pin header, 8 pins [form="♀ (female)"]
  J2 = female pin header, 10 pins [form="♀ (female)"]
  J8 = male pin header, 15 pins [form="♂ (male)"]
  J13 = female pin header, 8 pins [form="♀ (female)"]
  J17 = female pin header, 10 pins [form="♀ (female)"]
  J18 = female pin header, 8 pins [form="♀ (female)"]
  J19 = female pin header, 6 pins [form="♀ (female)"]
  J20 = female pin header, 8 pins [form="♀ (female)"]
  J21 = male pin header, 3 pins [form="♂ (male)"]  # not connected
  J22 = male pin header, 3 pins [form="♂ (male)"]  # not connected
  BAT2 = Battery Holders [package=battcom_20mm_pth]
  RTC2 = RTC-8564NB [package="Module(DIP 8P)"]
  J23 = male pin header, 15 pins [form="♂ (male)"]
  D5 = Schottky Diode [part_number=1N5817 package="300 mil [THT]"]
  D6 = Schottky Diode [part_number=1N5817 package="300 mil [THT]"]
  U3 = XBEE-1 [package=xbee-1]
  J24 = male pin header, 15 pins [form="♂ (male)"]
  J27 = female pin header, 10 pins [form="♀ (female)"]
  J29 = male pin header, 15 pins [form="♂ (male)"]
  J30 = female pin header, 8 pins [form="♀ (female)"]
  J31 = female pin header, 8 pins [form="♀ (female)"]
  J32 = female pin header, 6 pins [form="♀ (female)"]  # not connected
  U4 = XBEE-1 [package=xbee-1]
  J36 = female pin header, 10 pins [form="♀ (female)"]  # not connected
  J37 = female pin header, 8 pins [form="♀ (female)"]
  J38 = female pin header, 6 pins [form="♀ (female)"]  # not connected
  J39 = female pin header, 8 pins [form="♀ (female)"]
  J40 = female pin header, 10 pins [form="♀ (female)"]  # not connected
  J41 = female pin header, 8 pins [form="♀ (female)"]
  J42 = female pin header, 8 pins [form="♀ (female)"]
  J43 = female pin header, 6 pins [form="♀ (female)"]
  BAT3 = Battery Holders [package=battcom_20mm_pth]
  RTC3 = RTC-8564NB [package="Module(DIP 8P)"]
  D7 = Schottky Diode [part_number=1N5817 package="300 mil [THT]"]
  D8 = Schottky Diode [part_number=1N5817 package="300 mil [THT]"]
  Power_plug4 = AE-DC-POWER-JACK-DIP [part_number=AE-DC-POWER-JACK-DIP]
  J44 = female pin header, 6 pins [form="♀ (female)"]
  J45 = female pin header, 8 pins [form="♀ (female)"]
  J46 = female pin header, 8 pins [form="♀ (female)"]
  J47 = female pin header, 10 pins [form="♀ (female)"]
  J50 = female pin header, 10 pins [form="♀ (female)"]
  J52 = male pin header, 15 pins [form="♂ (male)"]
  J53 = female pin header, 8 pins [form="♀ (female)"]
  J54 = female pin header, 8 pins [form="♀ (female)"]
  J55 = female pin header, 6 pins [form="♀ (female)"]  # not connected
  J56 = female pin header, 10 pins [form="♀ (female)"]
  J57 = female pin header, 8 pins [form="♀ (female)"]
  J58 = female pin header, 6 pins [form="♀ (female)"]  # not connected
  J59 = female pin header, 8 pins [form="♀ (female)"]
  J60 = male pin header, 15 pins [form="♂ (male)"]
  R1 = Resistor [tolerance=±5% resistance=1M package=THT]
  U7 = RELAY-2 [package=relay-g5v]
  U8 = RELAY-2 [package=relay-g5v]
  J64 = male pin header, 15 pins [form="♂ (male)"]
  J65 = male pin header, 15 pins [form="♂ (male)"]
  パーツ7 = Bi-Directional Logic Level Converter [part_number=BOB-12009]  # not connected
  J70 = female pin header, 10 pins [form="♀ (female)"]  # not connected
  J71 = female pin header, 8 pins [form="♀ (female)"]  # not connected
  J72 = female pin header, 8 pins [form="♀ (female)"]
  J73 = female pin header, 6 pins [form="♀ (female)"]  # not connected
  J75 = female pin header, 4 pins [form="♀ (female)"]
  J76 = female pin header, 4 pins [form="♀ (female)"]
  J77 = male pin header, 15 pins [form="♂ (male)"]
  J78 = male pin header, 15 pins [form="♂ (male)"]
  J61 = female pin header, 8 pins [form="♀ (female)"]
  J74 = female pin header, 8 pins [form="♀ (female)"]
  J79 = male pin header, 15 pins [form="♂ (male)"]
  J14 = female pin header, 4 pins [form="♀ (female)"]
  J15 = female pin header, 4 pins [form="♀ (female)"]
  パーツ8 = Bi-Directional Logic Level Converter [part_number=BOB-12009]
  J84 = male pin header, 15 pins [form="♂ (male)"]
  J89 = female pin header, 10 pins [form="♀ (female)"]
  J90 = female pin header, 8 pins [form="♀ (female)"]
  J91 = female pin header, 6 pins [form="♀ (female)"]
  J92 = female pin header, 8 pins [form="♀ (female)"]
  S1 = Momentary Switch [package=ksa_sealed_tac_switch]  # not connected
  Power_plug5 = AE-DC-POWER-JACK-DIP [part_number=AE-DC-POWER-JACK-DIP]
  パーツ9 = Arduino Pro Mini v13
  J66 = male pin header, 15 pins [form="♂ (male)"]
  J67 = male pin header, 15 pins [form="♂ (male)"]
  J68 = male pin header, 15 pins [form="♂ (male)"]
  J69 = male pin header, 15 pins [form="♂ (male)"]
  J85 = male pin header, 15 pins [form="♂ (male)"]
  J86 = male pin header, 15 pins [form="♂ (male)"]
  J88 = male pin header, 15 pins [form="♂ (male)"]
  J87 = male pin header, 15 pins [form="♂ (male)"]
  J80 = male pin header, 15 pins [form="♂ (male)"]
  J81 = male pin header, 15 pins [form="♂ (male)"]
  J82 = male pin header, 15 pins [form="♂ (male)"]
  J83 = male pin header, 15 pins [form="♂ (male)"]

nets:
  N1: パーツ2.A4, J44.pin5
  N2: パーツ2.A5, J44.pin6
  N3: パーツ2.RAW, Power_plug4.VCC#7, J46.pin8
  N4: パーツ2.GND, Power_plug4.GND#0, Power_plug4.GND#2, J46.pin6, J46.pin7, J47.pin4
  N5: パーツ2.RESET, J46.pin3
  N6: パーツ2.VCC, J46.pin4
  N7: パーツ2.A3, J44.pin4
  N8: パーツ2.A2, J44.pin3
  N9: パーツ2.A1, J44.pin2
  N10: パーツ2.A0, J44.pin1
  N11: パーツ2.D13/SCK, J47.pin5
  N12: パーツ2.D12/MISO, J47.pin6
  N13: パーツ2.D11_PWM/MOSI, J47.pin7
  N14: パーツ2.D10_PWM/SS, J47.pin8
  N15: パーツ2.D9_PWM, J47.pin9
  N16: パーツ2.D8, J47.pin10
  N17: パーツ2.D7, J45.pin1
  N18: パーツ2.D6_PWM, J45.pin2
  N19: パーツ2.D5_PWM, J45.pin3
  N20: パーツ2.D4, J45.pin4
  N21: パーツ2.D3_PWM, J45.pin5
  N22: パーツ2.D2, J45.pin6
  N23: パーツ2.D1/RX, J45.pin7
  N24: パーツ2.D0/TX, J45.pin8
  N25: J3.pin1, J8.pin8, J80.pin8, J82.pin8
  N26: J3.pin2, J8.pin9, J80.pin9, J82.pin9
  N27: J3.pin3, J8.pin10, J80.pin10, J82.pin10
  N28: J3.pin4, J8.pin11, J80.pin11, J82.pin11
  N29: J3.pin5, J8.pin12, J80.pin12, J82.pin12
  N30: J3.pin6, J8.pin13, J80.pin13, J82.pin13
  N31: J3.pin7, J8.pin14, J80.pin14, J82.pin14
  N32: J3.pin8, J8.pin15, J80.pin15, J82.pin15
  N33: J2.pin5, J8.pin1, J80.pin1, J82.pin1
  N34: J2.pin6, J8.pin2, J80.pin2, J82.pin2
  N35: J2.pin7, J8.pin3, J80.pin3, J82.pin3
  N36: J2.pin8, J8.pin4, J80.pin4, J82.pin4
  N37: J2.pin9, J8.pin5, J80.pin5, J82.pin5
  N38: J2.pin10, J8.pin6, J80.pin6, J82.pin6
  N39: J13.pin3, パーツ8.HV4
  N40: J13.pin5, パーツ8.HV
  N41: J13.pin6, J13.pin7, J15.pin1, パーツ8.GND
  N42: J13.pin8, J15.pin2
  N43: J17.pin5, J23.pin1
  N44: J17.pin6, J23.pin2
  N45: J17.pin7, J23.pin3
  N46: J17.pin8, J23.pin4
  N47: J17.pin9, J23.pin5
  N48: J17.pin10, J23.pin6
  N49: J18.pin1, J23.pin8
  N50: J18.pin2, J23.pin9
  N51: J18.pin3, J23.pin10
  N52: J18.pin4, J23.pin11
  N53: J18.pin5, J23.pin12
  N54: J18.pin6, J23.pin13
  N55: J18.pin7, J23.pin14
  N56: J18.pin8, J23.pin15
  N57: J19.pin5, RTC2.SDA
  N58: J19.pin6, RTC2.SCL
  N59: J20.pin5, D5.anode
  N60: J20.pin6, BAT2.-, RTC2.GND
  N61: BAT2.+, D6.anode
  N62: RTC2.INT, J24.pin1, J24.pin2, J24.pin3, J24.pin4, J24.pin5, J24.pin6, J24.pin7, J24.pin8, J24.pin9, J24.pin10, J24.pin11, J24.pin12, J24.pin13, J24.pin14, J24.pin15
  N63: RTC2.VDD, D5.cathode, D6.cathode
  N64: U3.VDD, J31.pin4
  N65: U3.DOUT, J86.pin1, J86.pin2, J86.pin3, J86.pin4, J86.pin5, J86.pin6, J86.pin7, J86.pin8, J86.pin9, J86.pin10, J86.pin11, J86.pin12, J86.pin13, J86.pin14, J86.pin15
  N66: U3.DIN, J87.pin1, J87.pin2, J87.pin3, J87.pin4, J87.pin5, J87.pin6, J87.pin7, J87.pin8, J87.pin9, J87.pin10, J87.pin11, J87.pin12, J87.pin13, J87.pin14, J87.pin15
  N67: U3.DIO12, J84.pin1, J84.pin2, J84.pin3, J84.pin4, J84.pin5, J84.pin6, J84.pin7, J84.pin8, J84.pin9, J84.pin10, J84.pin11, J84.pin12, J84.pin13, J84.pin14, J84.pin15
  N68: U3.DIO11, J31.pin3
  N69: U3.GND, J31.pin6
  N70: J27.pin5, J29.pin1, J85.pin1, J88.pin1
  N71: J27.pin6, J29.pin2, J85.pin2, J88.pin2
  N72: J27.pin7, J29.pin3, J85.pin3, J88.pin3
  N73: J27.pin8, J29.pin4, J85.pin4, J88.pin4
  N74: J27.pin9, J29.pin5, J85.pin5, J88.pin5
  N75: J27.pin10, J29.pin6, J85.pin6, J88.pin6
  N76: J29.pin8, J30.pin1, J85.pin8, J88.pin8
  N77: J29.pin9, J30.pin2, J85.pin9, J88.pin9
  N78: J29.pin10, J30.pin3, J85.pin10, J88.pin10
  N79: J29.pin11, J30.pin4, J85.pin11, J88.pin11
  N80: J29.pin12, J30.pin5, J85.pin12, J88.pin12
  N81: J29.pin13, J30.pin6, J85.pin13, J88.pin13
  N82: J29.pin14, J30.pin7, J85.pin14, J88.pin14
  N83: J29.pin15, J30.pin8, J85.pin15, J88.pin15
  N84: U4.VDD, J39.pin4
  N85: U4.DOUT, J37.pin3
  N86: U4.DIN, J37.pin4
  N87: U4.DIO12, J39.pin3
  N88: U4.DIO11, J37.pin6
  N89: U4.GND, J39.pin6, J39.pin7
  N90: J41.pin6, RTC3.INT
  N91: J42.pin4, D8.anode
  N92: J42.pin6, J42.pin7, BAT3.-, RTC3.GND
  N93: J43.pin5, RTC3.SDA
  N94: J43.pin6, RTC3.SCL
  N95: BAT3.+, D7.anode
  N96: RTC3.VDD, D7.cathode, D8.cathode
  N97: J50.pin5, J52.pin1, J64.pin1, J78.pin1, J66.pin1, J68.pin1
  N98: J50.pin6, J52.pin2, J64.pin2, J78.pin2, J66.pin2, J68.pin2
  N99: J50.pin7, J52.pin3, J64.pin3, J78.pin3, J66.pin3, J68.pin3
  N100: J50.pin8, J52.pin4, J64.pin4, J78.pin4, J66.pin4, J68.pin4
  N101: J50.pin9, J52.pin5, J64.pin5, J78.pin5, J66.pin5, J68.pin5
  N102: J50.pin10, J52.pin6, J64.pin6, J78.pin6, J66.pin6, J68.pin6
  N103: J52.pin8, J53.pin1, J64.pin8, J78.pin8, J66.pin8, J68.pin8
  N104: J52.pin9, J53.pin2, J64.pin9, J78.pin9, J66.pin9, J68.pin9
  N105: J52.pin10, J53.pin3, J64.pin10, J78.pin10, J66.pin10, J68.pin10
  N106: J52.pin11, J53.pin4, J64.pin11, J78.pin11, J66.pin11, J68.pin11
  N107: J52.pin12, J53.pin5, J64.pin12, J78.pin12, J66.pin12, J68.pin12
  N108: J52.pin13, J53.pin6, J64.pin13, J78.pin13, J66.pin13, J68.pin13
  N109: J52.pin14, J53.pin7, J64.pin14, J78.pin14, J66.pin14, J68.pin14
  N110: J52.pin15, J53.pin8, J64.pin15, J78.pin15, J66.pin15, J68.pin15
  N111: J54.pin4, J75.pin3
  N112: J54.pin6, U7.2
  N113: J54.pin7, J75.pin1
  N114: J54.pin8, U7.5
  N115: J56.pin4, J59.pin6, J59.pin7, R1.Pin_0, J61.pin8
  N116: J57.pin1, U8.9
  N117: J57.pin2, J61.pin3
  N118: J57.pin3, J61.pin4
  N119: J57.pin5, J61.pin1
  N120: J57.pin6, J61.pin2
  N121: J59.pin4, J61.pin6
  N122: J59.pin8, U8.1
  N123: J60.pin1, J60.pin2, J60.pin3, J60.pin4, J60.pin5, J60.pin6, J60.pin7, J60.pin8, J60.pin9, J60.pin10, J60.pin11, J60.pin12, J60.pin13, J60.pin14, J60.pin15, J76.pin1
  N124: R1.Pin_1, U8.2
  N125: U7.6, J75.pin2
  N126: U7.9, J77.pin1, J77.pin2, J77.pin3, J77.pin4, J77.pin5, J77.pin6, J77.pin7, J77.pin8, J77.pin9, J77.pin10, J77.pin11, J77.pin12, J77.pin13, J77.pin14, J77.pin15
  N127: U8.6, J61.pin7
  N128: J65.pin1, J65.pin2, J65.pin3, J65.pin4, J65.pin5, J65.pin6, J65.pin7, J65.pin8, J65.pin9, J65.pin10, J65.pin11, J65.pin12, J65.pin13, J65.pin14, J65.pin15, J76.pin2
  N129: J72.pin6, J72.pin7, J74.pin8
  N130: J72.pin8, J74.pin7
  N131: J76.pin3, J67.pin1, J67.pin2, J67.pin3, J67.pin4, J67.pin5, J67.pin6, J67.pin7, J67.pin8, J67.pin9, J67.pin10, J67.pin11, J67.pin12, J67.pin13, J67.pin14, J67.pin15
  N132: J76.pin4, J69.pin1, J69.pin2, J69.pin3, J69.pin4, J69.pin5, J69.pin6, J69.pin7, J69.pin8, J69.pin9, J69.pin10, J69.pin11, J69.pin12, J69.pin13, J69.pin14, J69.pin15
  N133: J79.pin1, J79.pin2, J79.pin3, J79.pin4, J79.pin5, J79.pin6, J79.pin7, J79.pin8, J79.pin9, J79.pin10, J79.pin11, J79.pin12, J79.pin13, J79.pin14, J79.pin15, パーツ8.HV1
  N134: J14.pin1, パーツ8.LV1
  N135: J14.pin2, パーツ8.LV2
  N136: J14.pin3, パーツ8.LV3
  N137: J14.pin4, パーツ8.LV4
  N138: J15.pin3, パーツ8.LV
  N139: パーツ8.HV3, J83.pin1, J83.pin2, J83.pin3, J83.pin4, J83.pin5, J83.pin6, J83.pin7, J83.pin8, J83.pin9, J83.pin10, J83.pin11, J83.pin12, J83.pin13, J83.pin14, J83.pin15
  N140: パーツ8.HV2, J81.pin1, J81.pin2, J81.pin3, J81.pin4, J81.pin5, J81.pin6, J81.pin7, J81.pin8, J81.pin9, J81.pin10, J81.pin11, J81.pin12, J81.pin13, J81.pin14, J81.pin15
  N141: J89.pin4, J92.pin6, パーツ9.GND
  N142: J89.pin5, パーツ9.D13/SCK
  N143: J89.pin6, パーツ9.D12/MISO
  N144: J89.pin7, パーツ9.D11_PWM/MOSI
  N145: J89.pin8, パーツ9.D10_PWM/SS
  N146: J89.pin9, パーツ9.D9_PWM
  N147: J89.pin10, パーツ9.D8
  N148: J90.pin1, パーツ9.D7
  N149: J90.pin2, パーツ9.D6_PWM
  N150: J90.pin3, パーツ9.D5_PWM
  N151: J90.pin4, パーツ9.D4
  N152: J90.pin5, パーツ9.D3_PWM
  N153: J90.pin6, パーツ9.D2
  N154: J90.pin7, パーツ9.D1/RX
  N155: J90.pin8, パーツ9.D0/TX
  N156: J91.pin1, パーツ9.A0
  N157: J91.pin2, パーツ9.A1
  N158: J91.pin3, パーツ9.A2
  N159: J91.pin4, パーツ9.A3
  N160: J91.pin5, パーツ9.A4
  N161: J91.pin6, パーツ9.A5
  N162: J92.pin3, パーツ9.RESET
  N163: J92.pin4, パーツ9.VCC
  N164: J92.pin8, パーツ9.RAW
  N165: Power_plug5.GND#0, Power_plug5.GND#2

custom parts:
  Arduino Pro Mini v13: It's blue! It's thin! It's the Arduino Pro Mini! SparkFun's minimal design approach to Arduino. This is a 5V Arduino running the 16MHz bootloader. Arduino Pro Mini does not come with connectors populated so that you can solder in any connector or wire with any orientation you need. We recommend first time Arduino users start with the Uno R3. It's a great board that will get you up and running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
  RTC-8564NB: Real Time Clock Module and I2C-BUS interface method. This product is a module of the SON 8-pin DIP package. Supply voltage 1.8-5.5V
  AE-DC-POWER-JACK-DIP: 秋月電子通商 K-05148
  Bi-Directional Logic Level Converter: Description: If you've ever tried to connect a 3.3V device to a 5V system, you know what a challenge it can be. The SparkFun bi-directional logic level converter is a small device that safely steps down 5V signals to 3.3V AND steps up 3.3V to 5V at the same time. This level converter also works with 2.8V and 1.8V devices. What really separates this Logic level converter from our previous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
