# Fritzing sketch Kurumiロガー(シールド) (saved by Fritzing 0.9.2b)
perfboards: 1

parts:
  J8 = female pin header, 6 pins [form="♀ (female)"]  # not connected
  J9 = female pin header, 8 pins [form="♀ (female)"]
  J10 = female pin header, 8 pins [form="♀ (female)"]
  J11 = female pin header, 10 pins [form="♀ (female)"]
  DHT4 = DHT11 Humitidy and Temperature Sensor
  R5 = Resistor [tolerance=±5% resistance=10k package=THT]
  BOB-1 = DeadOn RTC - DS3234 Breakout (for upside down) [part_number=BOB-10160]

nets:
  VDD: J9.pin4, DHT4.VDD, R5.Pin_1, BOB-1.VCC
  GND: J9.pin6, J9.pin7, DHT4.GND, BOB-1.GND
  N1: J10.pin4, DHT4.DATA, R5.Pin_0
  N2: J11.pin5, BOB-1.SCLK
  N3: J11.pin6, BOB-1.MISO
  N4: J11.pin7, BOB-1.MOSI
  N5: J11.pin9, BOB-1.SS

custom parts:
  DHT11 Humitidy and Temperature Sensor: DHT11 Humidity and Temperature Sensor
  DeadOn RTC - DS3234 Breakout (for upside down): Description: Here is a real time clock based on the DS3234 Real Time Clock IC. The DS3234 is a low-cost, extremely accurate SPI bus real-time clock with an integrated temperature-compensated crystal oscillator and crystal. The RTC maintains seconds, minutes, hours, day, date, month, and year information. The date at the end of the month is automatically adjusted for months with fewer than 31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
