# Fritzing sketch Kurumiロガー(本体) (saved by Fritzing 0.9.2b)
perfboards: 1

parts:
  J18 = female pin header, 6 pins [form="♀ (female)"]
  J19 = female pin header, 8 pins [form="♀ (female)"]
  J20 = female pin header, 8 pins [form="♀ (female)"]
  Kurumi1 = GR kurumi (Renesas Gadget)
  Power_plug5 = Power plug
  AE-MOD1 = AE-XCL101C331BR-G
  SD1 = AE-MICRO-SD-DIP
  J21 = female pin header, 10 pins [form="♀ (female)"]
  JP1 = Grove Header 4pin 90 degree direct mount [package="90 degree"]

nets:
  N1: J18.pin1, Kurumi1.A0
  N2: J18.pin2, Kurumi1.A1
  N3: J18.pin3, Kurumi1.A2
  N4: J18.pin4, Kurumi1.A3
  N5: J19.pin2, Kurumi1.D6/PWM, SD1.SS
  N6: J19.pin3, Kurumi1.D5/PWM
  N7: J19.pin4, Kurumi1.D4
  N8: J19.pin5, Kurumi1.VCC#17, Kurumi1.D3/INT1/PWM
  N9: J19.pin6, Kurumi1.D2/INT0, Kurumi1.RAW
  N10: J19.pin7, Kurumi1.D1/TX0
  N11: J19.pin8, Kurumi1.D0/RX0
  N12: J20.pin3, Kurumi1.RST#44
  N13: J20.pin4, Kurumi1.VCC#43, AE-MOD1.Vout, SD1.VCC
  GND: J20.pin6, J20.pin7, Kurumi1.GND, Power_plug5.GND, AE-MOD1.VSS, SD1.GND, J21.pin4, JP1.4
  N14: J20.pin8, Power_plug5.VCC, AE-MOD1.Vbat, AE-MOD1.CE
  N15: Kurumi1.D7/TX1/SCL, JP1.1
  N16: Kurumi1.D8/RX1/SDA, J21.pin10, JP1.2
  N17: Kurumi1.D9/TX2/PWM, J21.pin9
  N18: Kurumi1.D10/RX2/SS, J21.pin8
  N19: Kurumi1.D11/Soft_PWM/MOSI, SD1.MOSI, J21.pin7
  N20: Kurumi1.D12/MISO, SD1.MISO, J21.pin6
  N21: Kurumi1.D13/SCLK, SD1.SCK, J21.pin5
  N22: SD1.CDA, SD1.NC0

notes:
  Tx
  RX
  GND
  NC
  2pin空ける
  (ネジ穴のため)

custom parts:
  GR kurumi (Renesas Gadget): RL78/G13
  Power plug: 秋月電子通商 AE-DCJACK-DIPKIT-2.1mm-10A(通販コードK-06998)とその互換品(K06999,K-08415,K-08416)
  AE-MICRO-SD-DIP: 秋月電子通商 K-05488
  Grove Header 4pin 90 degree direct mount: Header
