# Fritzing sketch Kurumiロガー(本体) (saved by Fritzing 0.9.2b)
perfboards: 1

parts:
  AD = female pin header, 6 pins [form="♀ (female)"]
  IOL = female pin header, 8 pins [form="♀ (female)"]
  Power = female pin header, 8 pins [form="♀ (female)"]
  Kurumi = GR kurumi (Renesas Gadget)
  Power_plug = Power plug
  DCDC = AE-XCL101C331BR-G
  SD = AE-MICRO-SD-DIP
  IOH = female pin header, 10 pins [form="♀ (female)"]
  plug = Grove Header 4pin 90 degree direct mount [package="90 degree"]

nets:
  N1: AD.pin1, Kurumi.A0
  N2: AD.pin2, Kurumi.A1
  N3: AD.pin3, Kurumi.A2
  N4: AD.pin4, Kurumi.A3
  Chip select: IOL.pin2, Kurumi.D6/PWM, SD.SS
  N5: IOL.pin3, Kurumi.D5/PWM
  N6: IOL.pin4, Kurumi.D4
  N7: IOL.pin5, Kurumi.VCC#17, Kurumi.D3/INT1/PWM
  N8: IOL.pin6, Kurumi.D2/INT0, Kurumi.RAW
  N9: IOL.pin7, Kurumi.D1/TX0
  N10: IOL.pin8, Kurumi.D0/RX0
  RST: Power.pin3, Kurumi.RST#44
  3.3V: Power.pin4, Kurumi.VCC#43, DCDC.Vout, SD.VCC
  GND: Power.pin6, Power.pin7, Kurumi.GND, Power_plug.GND, DCDC.VSS, SD.GND, IOH.pin4, plug.4
  VDD: Power.pin8, Power_plug.VCC, DCDC.Vbat, DCDC.CE
  Tx1: Kurumi.D7/TX1/SCL, plug.1
  Rx1: Kurumi.D8/RX1/SDA, IOH.pin10, plug.2
  N11: Kurumi.D9/TX2/PWM, IOH.pin9
  SS: Kurumi.D10/RX2/SS, IOH.pin8
  MOSI: Kurumi.D11/Soft_PWM/MOSI, SD.MOSI, IOH.pin7
  MISO: Kurumi.D12/MISO, SD.MISO, IOH.pin6
  N12: Kurumi.D13/SCLK, SD.SCK, IOH.pin5
  N13: SD.CDA, SD.NC0

notes:
  Tx
  RX
  GND
  NC
  2pin空ける
  (ネジ穴のため)

custom parts:
  GR kurumi (Renesas Gadget): RL78/G13
  Power plug: 秋月電子通商 AE-DCJACK-DIPKIT-2.1mm-10A(通販コードK-06998)とその互換品(K06999,K-08415,K-08416)
  AE-MICRO-SD-DIP: 秋月電子通商 K-05488
  Grove Header 4pin 90 degree direct mount: Header
