# Fritzing sketch システム全体 (saved by Fritzing 0.9.2b)
breadboards: 4

parts:
  R4 = Resistor [tolerance=±5% resistance=10k package=THT]
  温度センサー = DHT11 Humitidy and Temperature Sensor
  Power_plug = Power plug
  秋月AE-XCL101C331BR-G3 = XCL101 [package=sc70-6]
  シリアル用外部端子 = female pin header, 4 pins [form="♀ (female)"]
  GR-kurumi本体 = GR-kurumi
  秋月_マイクロSD_DIP = Akizuki MICRO-SD-DIP
  パーツ2 = DeadOn RTC - DS3234 Breakout (for upside down)
  J1 = female pin header, 10 pins [form="♀ (female)"]
  J2 = female pin header, 8 pins [form="♀ (female)"]
  J3 = female pin header, 8 pins [form="♀ (female)"]
  J4 = female pin header, 6 pins [form="♀ (female)"]  # not connected
  J5 = female pin header, 10 pins [form="♀ (female)"]
  J6 = female pin header, 8 pins [form="♀ (female)"]
  J7 = female pin header, 8 pins [form="♀ (female)"]
  J8 = female pin header, 6 pins [form="♀ (female)"]  # not connected

nets:
  3.3V: R4.Pin_0, 温度センサー.VDD, 秋月AE-XCL101C331BR-G3.Vout, GR-kurumi本体.VCC, 秋月_マイクロSD_DIP.VCC, パーツ2.VCC, J3.pin4, J7.pin4
  N1: R4.Pin_1, 温度センサー.DATA, GR-kurumi本体.D4, J2.pin4, J6.pin4
  GND: 温度センサー.GND, Power_plug.GND, 秋月AE-XCL101C331BR-G3.VSS, シリアル用外部端子.pin1, GR-kurumi本体.GND, 秋月_マイクロSD_DIP.GND, パーツ2.GND, J3.pin6, J3.pin7, J7.pin6, J7.pin7
  N2: Power_plug.VCC, 秋月AE-XCL101C331BR-G3.Vbat, 秋月AE-XCL101C331BR-G3.CE
  Serial in: シリアル用外部端子.pin2, GR-kurumi本体.D8
  Serial out: シリアル用外部端子.pin3, GR-kurumi本体.D7
  SCK: GR-kurumi本体.D13/SCK, 秋月_マイクロSD_DIP.SCK, パーツ2.SCLK, J1.pin5, J5.pin5
  MISO: GR-kurumi本体.D12/MISO, 秋月_マイクロSD_DIP.MISO, パーツ2.MISO, J1.pin6, J5.pin6
  MOSI: GR-kurumi本体.D11_PWM/MOSI, 秋月_マイクロSD_DIP.MOSI, パーツ2.MOSI, J1.pin7, J5.pin7
  N3: GR-kurumi本体.D9_PWM, パーツ2.SS, J1.pin9, J5.pin9
  N4: GR-kurumi本体.D6_PWM, 秋月_マイクロSD_DIP.SS

notes:
  シールド基板用回路
  本体基板用回路
  本体基板
  シールド

custom parts:
  DHT11 Humitidy and Temperature Sensor: DHT11 Humidity and Temperature Sensor
  XCL101: AE-XCL101C331BR-G
  Akizuki MICRO-SD-DIP: AE-MICRO-SD-DIP http://akizukidenshi.com/catalog/g/gK-05488/
  DeadOn RTC - DS3234 Breakout (for upside down): Description: Here is a real time clock based on the DS3234 Real Time Clock IC. The DS3234 is a low-cost, extremely accurate SPI bus real-time clock with an integrated temperature-compensated crystal oscillator and crystal. The RTC maintains seconds, minutes, hours, day, date, month, and year information. The date at the end of the month is automatically adjusted for months with fewer than 31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
