# Fritzing sketch シールド (saved by Fritzing 0.9.2b)
circuit board: 6.88566cm x 5.36311cm
breadboards: 2

parts:
  R4 = Resistor [tolerance=±5% resistance=10k package=THT]
  温度センサー = DHT11 Humitidy and Temperature Sensor
  RTC = DeadOn RTC - DS3234 Breakout (for upside down)
  J5 = female pin header, 10 pins [form="♀ (female)"]
  J6 = female pin header, 8 pins [form="♀ (female)"]
  J7 = female pin header, 8 pins [form="♀ (female)"]
  J8 = female pin header, 6 pins [form="♀ (female)"]  # not connected

nets:
  3.3V: R4.Pin_0, 温度センサー.VDD, RTC.VCC, J7.pin4
  N1: R4.Pin_1, 温度センサー.DATA, J6.pin4
  GND: 温度センサー.GND, RTC.GND, J7.pin6, J7.pin7
  N2: RTC.SS, J5.pin9
  N3: RTC.MOSI, J5.pin7
  N4: RTC.MISO, J5.pin6
  N5: RTC.SCLK, J5.pin5

notes:
  シールド基板用回路

custom parts:
  DHT11 Humitidy and Temperature Sensor: DHT11 Humidity and Temperature Sensor
  DeadOn RTC - DS3234 Breakout (for upside down): Description: Here is a real time clock based on the DS3234 Real Time Clock IC. The DS3234 is a low-cost, extremely accurate SPI bus real-time clock with an integrated temperature-compensated crystal oscillator and crystal. The RTC maintains seconds, minutes, hours, day, date, month, and year information. The date at the end of the month is automatically adjusted for months with fewer than 31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
