# Fritzing sketch 本体 (saved by Fritzing 0.9.2b)
circuit board: 10.16cm x 5.36194cm
breadboards: 2

parts:
  シリアル用外部端子 = female pin header, 4 pins [form="♀ (female)"]
  GR-kurumi本体 = GR-kurumi
  秋月_マイクロSD_DIP = Akizuki MICRO-SD-DIP
  J1 = female pin header, 10 pins [form="♀ (female)"]
  J2 = female pin header, 8 pins [form="♀ (female)"]
  J3 = female pin header, 8 pins [form="♀ (female)"]
  J4 = female pin header, 6 pins [form="♀ (female)"]
  AE-XCL101C331BR-G1 = XCL101 [package=sc70-6]
  Power_plug1 = AE-DC-POWER-JACK-DIP [part_number=AE-DC-POWER-JACK-DIP]

nets:
  Serial out: シリアル用外部端子.pin1, GR-kurumi本体.D7, J2.pin1
  Serial in: シリアル用外部端子.pin2, GR-kurumi本体.D8, J1.pin10
  GND: シリアル用外部端子.pin4, GR-kurumi本体.GND, 秋月_マイクロSD_DIP.GND, J1.pin4, J3.pin6, J3.pin7, AE-XCL101C331BR-G1.VSS, Power_plug1.GND
  RST: GR-kurumi本体.RESET, J3.pin3
  3.3V: GR-kurumi本体.VCC, 秋月_マイクロSD_DIP.VCC, J3.pin4, AE-XCL101C331BR-G1.Vout
  A3: GR-kurumi本体.A3, J4.pin4
  A2: GR-kurumi本体.A2, J4.pin3
  A1: GR-kurumi本体.A1, J4.pin2
  A0: GR-kurumi本体.A0, J4.pin1
  SCK: GR-kurumi本体.D13/SCK, 秋月_マイクロSD_DIP.SCK, J1.pin5
  MISO: GR-kurumi本体.D12/MISO, 秋月_マイクロSD_DIP.MISO, J1.pin6
  MOSI: GR-kurumi本体.D11_PWM/MOSI, 秋月_マイクロSD_DIP.MOSI, J1.pin7
  D10: GR-kurumi本体.D10_PWM/SS, J1.pin8
  N1: GR-kurumi本体.D9_PWM, J1.pin9
  D6: GR-kurumi本体.D6_PWM, 秋月_マイクロSD_DIP.SS, J2.pin2
  D5: GR-kurumi本体.D5_PWM, J2.pin3
  N2: GR-kurumi本体.D4, J2.pin4
  D3: GR-kurumi本体.D3_PWM, J2.pin5
  D2: GR-kurumi本体.D2, J2.pin6
  Rx: GR-kurumi本体.D1/RX, J2.pin8
  Tx: GR-kurumi本体.D0/TX, J2.pin7
  N3: J3.pin8, AE-XCL101C331BR-G1.Vbat, AE-XCL101C331BR-G1.CE, Power_plug1.VCC#6, Power_plug1.VCC#7
  N4: Power_plug1.VCC#4, Power_plug1.VCC#5

notes:
  本体基板用回路

custom parts:
  Akizuki MICRO-SD-DIP: AE-MICRO-SD-DIP http://akizukidenshi.com/catalog/g/gK-05488/
  XCL101: AE-XCL101C331BR-G
  AE-DC-POWER-JACK-DIP: 秋月電子通商 K-05148
