# Fritzing sketch Kurumiロガー(ラッピング確認用) (saved by Fritzing 0.9.2b)
perfboards: 2

parts:
  J7 = female pin header, 4 pins [form="♀ (female)"]  # not connected
  J8 = female pin header, 6 pins [form="♀ (female)"]  # not connected
  J9 = female pin header, 8 pins [form="♀ (female)"]  # not connected
  J10 = female pin header, 8 pins [form="♀ (female)"]  # not connected
  J11 = female pin header, 10 pins [form="♀ (female)"]  # not connected
  DHT4 = DHT11 Humitidy and Temperature Sensor  # not connected
  R5 = Resistor [tolerance=±5% resistance=10k package=THT]  # not connected
  J18 = female pin header, 6 pins [form="♀ (female)"]  # not connected
  J19 = female pin header, 8 pins [form="♀ (female)"]  # not connected
  J20 = female pin header, 8 pins [form="♀ (female)"]  # not connected
  J22 = female pin header, 12 pins [form="♀ (female)"]  # not connected
  J23 = female pin header, 12 pins [form="♀ (female)"]  # not connected
  Akizuki_MICRO-SD-DIP3 = Akizuki MICRO-SD-DIP  # not connected
  IC用ピンソケット = female pin header, 7 pins [form="♀ (female)"]  # not connected
  パーツ1 = DeadOn RTC - DS3234 Breakout (for upside down)  # not connected
  Power_plug4 = Power plug [part_number=AE-DC-POWER-JACK-DIP]
  AE-XCL101C331BR-G2 = XCL101 [package=sc70-6]  # not connected
  J21 = female pin header, 8 pins [form="♀ (female)"]  # not connected
  Kurumi1 = GR kurumi (Renesas Gadget)  # not connected

nets:
  N1: Power_plug4.GND#0, Power_plug4.GND#2

notes:
  Tx
  RX
  GND
  NC
  2pin空ける
  (ネジ穴のため)

custom parts:
  DHT11 Humitidy and Temperature Sensor: DHT11 Humidity and Temperature Sensor
  Akizuki MICRO-SD-DIP: AE-MICRO-SD-DIP http://akizukidenshi.com/catalog/g/gK-05488/
  DeadOn RTC - DS3234 Breakout (for upside down): Description: Here is a real time clock based on the DS3234 Real Time Clock IC. The DS3234 is a low-cost, extremely accurate SPI bus real-time clock with an integrated temperature-compensated crystal oscillator and crystal. The RTC maintains seconds, minutes, hours, day, date, month, and year information. The date at the end of the month is automatically adjusted for months with fewer than 31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
  Power plug: 秋月電子通商 ブレッドボード用ＤＣジャックＤＩＰ化キット
  XCL101: AE-XCL101C331BR-G
  GR kurumi (Renesas Gadget): RL78/G13
