# Fritzing sketch Kurumiロガー(本体) (saved by Fritzing 0.9.2b)
perfboards: 1

parts:
  AD = female pin header, 6 pins [form="♀ (female)"]
  IOL = female pin header, 8 pins [form="♀ (female)"]
  Power = female pin header, 8 pins [form="♀ (female)"]
  Power_plug = Power plug
  DCDC = AE-XCL101C331BR-G
  SD = AE-MICRO-SD-DIP
  IOH = female pin header, 10 pins [form="♀ (female)"]
  plug = Grove Header 4pin 90 degree direct mount [package="90 degree"]
  Kurumi = GR kurumi (Renesas Gadget) no serial

nets:
  N1: AD.pin1, Kurumi.A0
  N2: AD.pin2, Kurumi.A1
  N3: AD.pin3, Kurumi.A2
  N4: AD.pin4, Kurumi.A3
  Chip select: IOL.pin2, SD.SS, Kurumi.D6/PWM
  N5: IOL.pin3, Kurumi.D5/PWM
  N6: IOL.pin4, Kurumi.D4
  N7: IOL.pin5, Kurumi.D3/INT1/PWM
  N8: IOL.pin6, Kurumi.D2/INT0, Kurumi.RAW
  N9: IOL.pin7, Kurumi.D1/TX0
  N10: IOL.pin8, Kurumi.D0/RX0
  RST: Power.pin3, Kurumi.RST#44
  3.3V: Power.pin4, DCDC.Vout, SD.VCC, Kurumi.VCC
  GND: Power.pin6, Power.pin7, Power_plug.GND, DCDC.VSS, SD.GND, IOH.pin4, plug.4, Kurumi.GND
  VDD: Power.pin8, Power_plug.VCC, DCDC.Vbat, DCDC.CE
  N11: SD.CDA, SD.NC0
  MISO: SD.MISO, IOH.pin6, Kurumi.D12/MISO
  N12: SD.SCK, IOH.pin5, Kurumi.D13/SCLK
  MOSI: SD.MOSI, IOH.pin7, Kurumi.D11/Soft_PWM/MOSI
  SS: IOH.pin8, Kurumi.D10/RX2/SS
  N13: IOH.pin9, Kurumi.D9/TX2/PWM
  Rx1: IOH.pin10, plug.2, Kurumi.D8/RX1/SDA
  Tx1: plug.1, Kurumi.D7/TX1/SCL

notes:
  Tx
  RX
  GND
  NC
  2pin空ける
  (ネジ穴のため)

custom parts:
  Power plug: 秋月電子通商 AE-DCJACK-DIPKIT-2.1mm-10A(通販コードK-06998)とその互換品(K06999,K-08415,K-08416)
  AE-MICRO-SD-DIP: 秋月電子通商 K-05488
  Grove Header 4pin 90 degree direct mount: Header
  GR kurumi (Renesas Gadget) no serial: RL78/G13
