# Fritzing sketch kurumi単独システム例 (saved by Fritzing 0.9.2b)
perfboards: 4

parts:
  Grove1 = Grove 3 Axis Digital Accelerometer 16g  # not connected
  Grove2 = Grove Infrared Emitter  # not connected
  Grove3 = Grove 3 Axis Digital Accelerometer 16g  # not connected
  VCC1 = Battery block 9V  # not connected
  ON/Sleep3 = male pin header, 5 pins [form="♂ (male)"]
  J115 = male pin header, 5 pins [form="♂ (male)"]
  Xbee4 = SSCI-KIT-XBSOCKET
  J116 = Arduino R3 6pin male header [package=THT]  # not connected
  IOH7 = female pin header, 10 pins [form="♀ (female)"]
  J117 = male pin header, 11 pins [form="♂ (male)"]
  J118 = male pin header, 11 pins [form="♂ (male)"]
  J119 = male pin header, 11 pins [form="♂ (male)"]
  J120 = male pin header, 11 pins [form="♂ (male)"]
  J121 = male pin header, 11 pins [form="♂ (male)"]
  ON/Sleep4 = male pin header, 11 pins [form="♂ (male)"]
  Reset2 = male pin header, 11 pins [form="♂ (male)"]
  RSSI1 = male pin header, 11 pins [form="♂ (male)"]
  Associate1 = male pin header, 11 pins [form="♂ (male)"]
  Sleep_RQ1 = male pin header, 11 pins [form="♂ (male)"]
  Rx5 = male pin header, 15 pins [form="♂ (male)"]
  J122 = male pin header, 15 pins [form="♂ (male)"]
  Tx5 = male pin header, 15 pins [form="♂ (male)"]
  J123 = male pin header, 15 pins [form="♂ (male)"]
  INT4 = male pin header, 15 pins [form="♂ (male)"]
  J124 = male pin header, 15 pins [form="♂ (male)"]
  IOL7 = female pin header, 8 pins [form="♀ (female)"]
  Power7 = female pin header, 8 pins [form="♀ (female)"]
  AD7 = female pin header, 6 pins [form="♀ (female)"]
  S4 = Akizuki slide switch IS-2235
  microSD2 = MicroSD Breakout
  Card_detect1 = male pin header, 12 pins [form="♂ (male)"]
  J125 = male pin header, 12 pins [form="♂ (male)"]
  Chip_select1 = male pin header, 12 pins [form="♂ (male)"]
  J126 = male pin header, 12 pins [form="♂ (male)"]
  J127 = Arduino R3 6pin male header [package=THT]  # not connected
  IOH8 = female pin header, 10 pins [form="♀ (female)"]
  IOL8 = female pin header, 8 pins [form="♀ (female)"]
  POWER1 = female pin header, 8 pins [form="♀ (female)"]
  AD8 = female pin header, 6 pins [form="♀ (female)"]  # not connected
  Pro_Mini_3V_8MHz1 = GR kurumi (Renesas Gadget) no serial
  R2 = Resistor [tolerance=±5% resistance=10k package=THT]
  D9 = Rectifier Diode [part_number=1N4001 package="300 mil [THT]"]
  Power_plug7 = Power plug
  J128 = Arduino R3 6pin male header [package=THT]  # not connected
  Reset3 = Momentary Switch [package=ksa_sealed_tac_switch]
  IOH9 = female pin header, 10 pins [form="♀ (female)"]
  Power8 = female pin header, 8 pins [form="♀ (female)"]
  IOL9 = female pin header, 8 pins [form="♀ (female)"]
  AD9 = female pin header, 6 pins [form="♀ (female)"]
  S5 = Akizuki slide switch IS-2235
  RTC4 = RTC-8564NB [package="Module(DIP 8P)"]
  S6 = Akizuki slide switch IS-1250
  J129 = Arduino R3 6pin male header [package=THT]  # not connected
  D10 = Schottky Diode [part_number=1N5817 package="300 mil [THT]"]
  D11 = Schottky Diode [part_number=1N5817 package="300 mil [THT]"]
  IOH10 = female pin header, 10 pins [form="♀ (female)"]
  INT5 = male pin header, 15 pins [form="♂ (male)"]
  J130 = male pin header, 15 pins [form="♂ (male)"]
  IOL10 = female pin header, 8 pins [form="♀ (female)"]
  Power9 = female pin header, 8 pins [form="♀ (female)"]
  AD10 = female pin header, 6 pins [form="♀ (female)"]
  BAT4 = Battery Holders [package=battcom_20mm_pth]

nets:
  N1: ON/Sleep3.pin1, ON/Sleep3.pin2, ON/Sleep3.pin3, ON/Sleep3.pin4, ON/Sleep3.pin5, Xbee4.pin13, ON/Sleep4.pin1, ON/Sleep4.pin2, ON/Sleep4.pin3, ON/Sleep4.pin4, ON/Sleep4.pin5, ON/Sleep4.pin6, ON/Sleep4.pin7, ON/Sleep4.pin8, ON/Sleep4.pin9, ON/Sleep4.pin10, ON/Sleep4.pin11
  N2: J115.pin1, AD7.pin1
  N3: J115.pin2, AD7.pin2
  N4: J115.pin3, AD7.pin3
  N5: J115.pin4, AD7.pin4
  N6: J115.pin5, AD7.pin5
  N7: Xbee4.VCC, Power7.pin4
  N8: Xbee4.pin2, Tx5.pin1, Tx5.pin2, Tx5.pin3, Tx5.pin4, Tx5.pin5, Tx5.pin6, Tx5.pin7, Tx5.pin8, Tx5.pin9, Tx5.pin10, Tx5.pin11, Tx5.pin12, Tx5.pin13, Tx5.pin14, Tx5.pin15
  N9: Xbee4.pin3, Rx5.pin1, Rx5.pin2, Rx5.pin3, Rx5.pin4, Rx5.pin5, Rx5.pin6, Rx5.pin7, Rx5.pin8, Rx5.pin9, Rx5.pin10, Rx5.pin11, Rx5.pin12, Rx5.pin13, Rx5.pin14, Rx5.pin15
  N10: Xbee4.pin4, INT4.pin1, INT4.pin2, INT4.pin3, INT4.pin4, INT4.pin5, INT4.pin6, INT4.pin7, INT4.pin8, INT4.pin9, INT4.pin10, INT4.pin11, INT4.pin12, INT4.pin13, INT4.pin14, INT4.pin15
  N11: Xbee4.pin5, Reset2.pin1, Reset2.pin2, Reset2.pin3, Reset2.pin4, Reset2.pin5, Reset2.pin6, Reset2.pin7, Reset2.pin8, Reset2.pin9, Reset2.pin10, Reset2.pin11
  N12: Xbee4.pin6, RSSI1.pin1, RSSI1.pin2, RSSI1.pin3, RSSI1.pin4, RSSI1.pin5, RSSI1.pin6, RSSI1.pin7, RSSI1.pin8, RSSI1.pin9, RSSI1.pin10, RSSI1.pin11
  N13: Xbee4.pin9, Sleep_RQ1.pin1, Sleep_RQ1.pin2, Sleep_RQ1.pin3, Sleep_RQ1.pin4, Sleep_RQ1.pin5, Sleep_RQ1.pin6, Sleep_RQ1.pin7, Sleep_RQ1.pin8, Sleep_RQ1.pin9, Sleep_RQ1.pin10, Sleep_RQ1.pin11
  N14: Xbee4.GND, IOH7.pin4, Power7.pin6, Power7.pin7
  N15: Xbee4.pin15, Associate1.pin1, Associate1.pin2, Associate1.pin3, Associate1.pin4, Associate1.pin5, Associate1.pin6, Associate1.pin7, Associate1.pin8, Associate1.pin9, Associate1.pin10, Associate1.pin11
  N16: IOH7.pin5, J122.pin1, J123.pin1, J124.pin1
  N17: IOH7.pin6, J122.pin2, J123.pin2, J124.pin2
  N18: IOH7.pin7, J122.pin3, J123.pin3, J124.pin3
  N19: IOH7.pin8, J117.pin1, J118.pin1, J119.pin1, J120.pin1, J121.pin1, J122.pin4, J123.pin4, J124.pin4
  N20: IOH7.pin9, J117.pin2, J118.pin2, J119.pin2, J120.pin2, J121.pin2, J122.pin5, J123.pin5, J124.pin5
  N21: IOH7.pin10, J117.pin3, J118.pin3, J119.pin3, J120.pin3, J121.pin3, J122.pin6, J123.pin6, J124.pin6
  N22: J117.pin5, J118.pin5, J119.pin5, J120.pin5, J121.pin5, J122.pin8, J123.pin8, J124.pin8, IOL7.pin1
  N23: J117.pin6, J118.pin6, J119.pin6, J120.pin6, J121.pin6, J122.pin9, J123.pin9, J124.pin9, IOL7.pin2
  N24: J117.pin7, J118.pin7, J119.pin7, J120.pin7, J121.pin7, J122.pin10, J123.pin10, J124.pin10, IOL7.pin3
  N25: J117.pin8, J118.pin8, J119.pin8, J120.pin8, J121.pin8, J122.pin11, J123.pin11, J124.pin11, IOL7.pin4
  N26: J117.pin9, J118.pin9, J119.pin9, J120.pin9, J121.pin9, J122.pin12, J123.pin12, J124.pin12, IOL7.pin5
  N27: J117.pin10, J118.pin10, J119.pin10, J120.pin10, J121.pin10, J122.pin13, J123.pin13, J124.pin13, IOL7.pin6
  N28: J117.pin11, J118.pin11, J119.pin11, J120.pin11, J121.pin11, J122.pin14, J123.pin14, J124.pin14, IOL7.pin7
  N29: J122.pin15, J123.pin15, J124.pin15, IOL7.pin8
  N30: S4.pin0, POWER1.pin5
  N31: S4.pin1, microSD2.5V
  N32: S4.pin4, microSD2.3v
  N33: S4.pin5, POWER1.pin4
  N34: microSD2.CD, Card_detect1.pin1, Card_detect1.pin2, Card_detect1.pin3, Card_detect1.pin4, Card_detect1.pin5, Card_detect1.pin6, Card_detect1.pin7, Card_detect1.pin8, Card_detect1.pin9, Card_detect1.pin10, Card_detect1.pin11, Card_detect1.pin12
  N35: microSD2.CS, Chip_select1.pin1, Chip_select1.pin2, Chip_select1.pin3, Chip_select1.pin4, Chip_select1.pin5, Chip_select1.pin6, Chip_select1.pin7, Chip_select1.pin8, Chip_select1.pin9, Chip_select1.pin10, Chip_select1.pin11, Chip_select1.pin12
  N36: microSD2.DI, IOH8.pin7
  N37: microSD2.DO, IOH8.pin6
  N38: microSD2.CLK, IOH8.pin5
  N39: microSD2.GND, IOH8.pin4, POWER1.pin6, POWER1.pin7
  N40: J125.pin1, J126.pin1, IOH8.pin8
  N41: J125.pin2, J126.pin2, IOH8.pin9
  N42: J125.pin3, J126.pin3, IOH8.pin10
  N43: J125.pin5, J126.pin5, IOL8.pin1
  N44: J125.pin6, J126.pin6, IOL8.pin2
  N45: J125.pin7, J126.pin7, IOL8.pin3
  N46: J125.pin8, J126.pin8, IOL8.pin4
  N47: J125.pin9, J126.pin9, IOL8.pin5
  N48: J125.pin10, J126.pin10, IOL8.pin6
  N49: J125.pin11, J126.pin11, IOL8.pin7
  N50: J125.pin12, J126.pin12, IOL8.pin8
  N51: Pro_Mini_3V_8MHz1.D1/TX0, IOL9.pin7
  N52: Pro_Mini_3V_8MHz1.D0/RX0, IOL9.pin8
  N53: Pro_Mini_3V_8MHz1.RST, Reset3.2, Power8.pin3
  GND: Pro_Mini_3V_8MHz1.GND, Power_plug7.GND, Reset3.4, IOH9.pin4, Power8.pin6, Power8.pin7
  N54: Pro_Mini_3V_8MHz1.D2/INT0, Pro_Mini_3V_8MHz1.RAW, Power_plug7.VCC, Power8.pin8, IOL9.pin6
  N55: Pro_Mini_3V_8MHz1.D3/INT1/PWM, IOL9.pin5
  N56: Pro_Mini_3V_8MHz1.D4, IOL9.pin4
  N57: Pro_Mini_3V_8MHz1.D5/PWM, IOL9.pin3
  N58: Pro_Mini_3V_8MHz1.D6/PWM, IOL9.pin2
  N59: Pro_Mini_3V_8MHz1.D7/TX1/SCL, IOL9.pin1
  N60: Pro_Mini_3V_8MHz1.D8/RX1/SDA, IOH9.pin10
  N61: Pro_Mini_3V_8MHz1.D9/TX2/PWM, IOH9.pin9
  N62: Pro_Mini_3V_8MHz1.D10/RX2/SS, IOH9.pin8
  N63: Pro_Mini_3V_8MHz1.D11/Soft_PWM/MOSI, IOH9.pin7
  N64: Pro_Mini_3V_8MHz1.D12/MISO, IOH9.pin6
  N65: Pro_Mini_3V_8MHz1.D13/SCLK, IOH9.pin5
  N66: Pro_Mini_3V_8MHz1.A0, AD9.pin1
  N67: Pro_Mini_3V_8MHz1.A1, AD9.pin2
  N68: Pro_Mini_3V_8MHz1.A2, AD9.pin3
  N69: Pro_Mini_3V_8MHz1.A3, AD9.pin4
  N70: Pro_Mini_3V_8MHz1.VCC, R2.Pin_1, D9.cathode, Power8.pin4
  N71: Pro_Mini_3V_8MHz1.A4, AD9.pin5
  N72: Pro_Mini_3V_8MHz1.A5, AD9.pin6
  N73: R2.Pin_0, D9.anode, Reset3.1
  N74: S5.pin0, IOH10.pin10, J130.pin6
  N75: S5.pin1, RTC4.SDA
  N76: S5.pin2, AD10.pin5
  N77: S5.pin3, J130.pin8, IOL10.pin1
  N78: S5.pin4, RTC4.SCL
  N79: S5.pin5, AD10.pin6
  N80: RTC4.INT, INT5.pin1, INT5.pin2, INT5.pin3, INT5.pin4, INT5.pin5, INT5.pin6, INT5.pin7, INT5.pin8, INT5.pin9, INT5.pin10, INT5.pin11, INT5.pin12, INT5.pin13, INT5.pin14, INT5.pin15
  N81: RTC4.GND, IOH10.pin4, Power9.pin6, Power9.pin7, BAT4.-
  N82: RTC4.VDD, D10.cathode, D11.cathode
  N83: S6.pin0, S6.pin3, Power9.pin5
  N84: S6.pin1, S6.pin4, D11.anode
  N85: S6.pin2, S6.pin5, Power9.pin4
  N86: D10.anode, BAT4.+
  N87: IOH10.pin5, J130.pin1
  N88: IOH10.pin6, J130.pin2
  N89: IOH10.pin7, J130.pin3
  N90: IOH10.pin8, J130.pin4
  N91: IOH10.pin9, J130.pin5
  N92: J130.pin9, IOL10.pin2
  N93: J130.pin10, IOL10.pin3
  N94: J130.pin11, IOL10.pin4
  N95: J130.pin12, IOL10.pin5
  N96: J130.pin13, IOL10.pin6
  N97: J130.pin14, IOL10.pin7
  N98: J130.pin15, IOL10.pin8

custom parts:
  SSCI-KIT-XBSOCKET: Xbee pin conversion
  Arduino R3 6pin male header: Pin header for arduino R3
  Akizuki slide switch IS-2235: Akizuki slide switch is-2235 (P-02627)
  MicroSD Breakout: 5V-ready microSD Breakout with Level Shifter
  GR kurumi (Renesas Gadget) no serial: RL78/G13
  Power plug: 秋月電子通商 AE-DCJACK-DIPKIT-2.1mm-10A(通販コードK-06998)とその互換品(K06999,K-08415,K-08416)
  RTC-8564NB: Real Time Clock Module and I2C-BUS interface method. This product is a module of the SON 8-pin DIP package. Supply voltage 1.8-5.5V original version by KimuShige
  Akizuki slide switch IS-1250: Akizuki slide switch is-1250 (P-01665)
