# Fritzing sketch Xbee,Arduino連携システム例 (saved by Fritzing 0.9.2b)
perfboards: 9

parts:
  U9 = RELAY-SIL05-1A72-71D [package=relay-g5v]
  J98 = Arduino R3 6pin male header [package=THT]  # not connected
  Signal_OUT1 = Grove Header 4pin 90 degree direct mount [package="90 degree"]
  Power_OUT1 = Grove Header 4pin 90 degree direct mount [package="90 degree"]
  IOH3 = female pin header, 10 pins [form="♀ (female)"]
  Rx2 = male pin header, 15 pins [form="♂ (male)"]
  Reset2 = male pin header, 15 pins [form="♂ (male)"]
  J99 = male pin header, 15 pins [form="♂ (male)"]
  Shutdown1 = male pin header, 15 pins [form="♂ (male)"]
  J100 = male pin header, 15 pins [form="♂ (male)"]
  J101 = male pin header, 15 pins [form="♂ (male)"]
  RelayControl1 = male pin header, 15 pins [form="♂ (male)"]
  J102 = male pin header, 15 pins [form="♂ (male)"]
  Tx2 = male pin header, 15 pins [form="♂ (male)"]
  J103 = male pin header, 15 pins [form="♂ (male)"]
  IOL3 = female pin header, 8 pins [form="♀ (female)"]
  Power3 = female pin header, 8 pins [form="♀ (female)"]
  AD3 = female pin header, 6 pins [form="♀ (female)"]  # not connected
  VCC1 = Battery block 9V  # not connected
  Power_plug7 = Power plug
  Xbee3 = SSCI-KIT-XBSOCKET
  J110 = Arduino R3 6pin male header [package=THT]  # not connected
  Vol1 = Trimmer Potentiometer [maximum_resistance=0.1MΩ package=THT]
  Reset3 = Momentary Switch [package=ksa_sealed_tac_switch]
  IOH6 = female pin header, 10 pins [form="♀ (female)"]
  IOL6 = female pin header, 8 pins [form="♀ (female)"]
  Power6 = female pin header, 8 pins [form="♀ (female)"]
  J111 = male pin header, 3 pins [form="♂ (male)"]
  AD6 = female pin header, 6 pins [form="♀ (female)"]
  R2 = Resistor [tolerance=±5% resistance=10k package=THT]
  AE-MOD2 = AE-XCL101C331BR-G
  D9 = Schottky Diode [part_number=1S4 breakdown_voltage=3.6V package="300 mil [THT]"]
  R3 = Resistor [tolerance=±5% resistance=3k package=THT]
  R4 = Resistor [tolerance=±5% resistance=3k package=THT]
  2SC1816 = NPN-Transistor [package="TO92 [THT]"]
  Relay1 = RELAY-G6L [package=1P]
  ICSP1 = Arduino R3 6pin male header [package=THT]  # not connected
  Signal_OUT2 = Grove Header 4pin 90 degree direct mount [package="90 degree"]
  Power_OUT2 = Grove Header 4pin 90 degree direct mount [package="90 degree"]
  IOH7 = female pin header, 10 pins [form="♀ (female)"]
  Rx4 = male pin header, 15 pins [form="♂ (male)"]
  Reset4 = male pin header, 13 pins [form="♂ (male)"]
  J112 = male pin header, 13 pins [form="♂ (male)"]
  Shutdown3 = male pin header, 15 pins [form="♂ (male)"]
  J113 = male pin header, 15 pins [form="♂ (male)"]
  J114 = male pin header, 13 pins [form="♂ (male)"]
  RelayControl2 = male pin header, 13 pins [form="♂ (male)"]
  J115 = male pin header, 15 pins [form="♂ (male)"]
  Tx4 = male pin header, 15 pins [form="♂ (male)"]
  J116 = male pin header, 15 pins [form="♂ (male)"]
  IOL7 = female pin header, 8 pins [form="♀ (female)"]
  Power7 = female pin header, 8 pins [form="♀ (female)"]
  AD7 = female pin header, 6 pins [form="♀ (female)"]  # not connected
  パーツ3 = Arduino Mega 2560 (Rev3)  # not connected
  パーツ4 = Arduino Uno (Rev3)  # not connected
  microSD3 = MicroSD Breakout
  IO21 = female pin header, 8 pins [form="♀ (female)"]
  SCL5 = male pin header, 3 pins [form="♂ (male)"]
  AD18 = female pin header, 8 pins [form="♀ (female)"]  # not connected
  J146 = male pin header, 3 pins [form="♂ (male)"]
  SCL6 = male pin header, 3 pins [form="♂ (male)"]
  IO22 = female pin header, 18 pins [form="♀ (female)"]  # not connected
  J147 = male pin header, 3 pins [form="♂ (male)"]
  SDA5 = male pin header, 3 pins [form="♂ (male)"]
  IO23 = female pin header, 18 pins [form="♀ (female)"]  # not connected
  J148 = male pin header, 3 pins [form="♂ (male)"]
  SDA6 = male pin header, 3 pins [form="♂ (male)"]
  ICSP10 = Arduino R3 6pin male header [package=THT]  # not connected
  Power_IN4 = Grove Header 4pin 90 degree direct mount [package="90 degree"]
  Signal_IN4 = Grove Header 4pin 90 degree direct mount [package="90 degree"]
  LevelConverter4 = Bi-Directional Logic Level Converter [part_number=BOB-12009]
  IOH14 = female pin header, 10 pins [form="♀ (female)"]
  Shutdown6 = male pin header, 15 pins [form="♂ (male)"]
  J149 = male pin header, 15 pins [form="♂ (male)"]
  J150 = male pin header, 22 pins [form="♂ (male)"]
  INT8 = male pin header, 22 pins [form="♂ (male)"]
  Rx9 = male pin header, 15 pins [form="♂ (male)"]
  AD19 = female pin header, 8 pins [form="♀ (female)"]  # not connected
  J151 = male pin header, 15 pins [form="♂ (male)"]
  S6 = Akizuki slide switch IS-2235
  S7 = Akizuki slide switch IS-2235
  Tx9 = male pin header, 15 pins [form="♂ (male)"]
  J152 = male pin header, 15 pins [form="♂ (male)"]
  IOL14 = female pin header, 8 pins [form="♀ (female)"]
  Power15 = female pin header, 8 pins [form="♀ (female)"]
  AD20 = female pin header, 6 pins [form="♀ (female)"]  # not connected
  RTC8 = RTC-8564NB [package="Module(DIP 8P)"]
  SW4 = Akizuki slide switch IS-1250
  RTC9 = RTC-8564NB [package="Module(DIP 8P)"]
  ICSP11 = Arduino R3 6pin male header [package=THT]  # not connected
  ICSP12 = Arduino R3 6pin male header [package=THT]  # not connected
  D17 = Schottky Diode [part_number=1N5817 package="300 mil [THT]"]
  SW5 = Akizuki slide switch IS-1250
  D18 = Schottky Diode [part_number=1N5817 package="300 mil [THT]"]
  Power_IN5 = Grove Header 4pin 90 degree direct mount [package="90 degree"]
  IO24 = female pin header, 10 pins [form="♀ (female)"]
  ICSP13 = Arduino R3 6pin male header [package=THT]  # not connected
  Signal_IN5 = Grove Header 4pin 90 degree direct mount [package="90 degree"]
  IO25 = female pin header, 8 pins [form="♀ (female)"]
  LevelConverter5 = Bi-Directional Logic Level Converter [part_number=BOB-12009]
  Power16 = female pin header, 8 pins [form="♀ (female)"]
  IO26 = female pin header, 10 pins [form="♀ (female)"]
  BAT8 = Battery Holders [package=battcom_20mm_pth]
  Shutdown7 = male pin header, 24 pins [form="♂ (male)"]
  J153 = male pin header, 24 pins [form="♂ (male)"]
  IO27 = female pin header, 8 pins [form="♀ (female)"]
  Rx10 = male pin header, 24 pins [form="♂ (male)"]
  J154 = male pin header, 24 pins [form="♂ (male)"]
  AD21 = female pin header, 8 pins [form="♀ (female)"]  # not connected
  Tx10 = male pin header, 24 pins [form="♂ (male)"]
  J155 = male pin header, 24 pins [form="♂ (male)"]
  IO28 = female pin header, 8 pins [form="♀ (female)"]
  Power17 = female pin header, 8 pins [form="♀ (female)"]
  Card_detect3 = male pin header, 12 pins [form="♂ (male)"]
  J156 = male pin header, 12 pins [form="♂ (male)"]
  Chip_select3 = male pin header, 12 pins [form="♂ (male)"]
  J157 = male pin header, 12 pins [form="♂ (male)"]
  S8 = Akizuki slide switch IS-2235
  Grove7 = Grove 3 Axis Digital Accelerometer 16g  # not connected
  Grove8 = Grove 3 Axis Digital Accelerometer 16g  # not connected
  IO29 = female pin header, 18 pins [form="♀ (female)"]  # not connected
  IO30 = female pin header, 18 pins [form="♀ (female)"]  # not connected
  D19 = Schottky Diode [part_number=1N5817 package="300 mil [THT]"]
  D20 = Schottky Diode [part_number=1N5817 package="300 mil [THT]"]
  IOH15 = female pin header, 10 pins [form="♀ (female)"]
  INT9 = male pin header, 15 pins [form="♂ (male)"]
  J158 = male pin header, 15 pins [form="♂ (male)"]
  IOL15 = female pin header, 8 pins [form="♀ (female)"]
  Power18 = female pin header, 8 pins [form="♀ (female)"]
  AD22 = female pin header, 6 pins [form="♀ (female)"]
  BAT9 = Battery Holders [package=battcom_20mm_pth]
  microSD4 = MicroSD Breakout
  ICSP14 = Arduino R3 6pin male header [package=THT]
  Card_detect4 = male pin header, 24 pins [form="♂ (male)"]
  J159 = male pin header, 24 pins [form="♂ (male)"]
  Chip_select4 = male pin header, 24 pins [form="♂ (male)"]
  J160 = male pin header, 24 pins [form="♂ (male)"]
  IOH16 = female pin header, 10 pins [form="♀ (female)"]
  IOL16 = female pin header, 8 pins [form="♀ (female)"]
  POWER3 = female pin header, 8 pins [form="♀ (female)"]
  AD23 = female pin header, 6 pins [form="♀ (female)"]  # not connected
  ICSP15 = Arduino R3 6pin male header [package=THT]
  IO31 = female pin header, 10 pins [form="♀ (female)"]
  IO32 = female pin header, 8 pins [form="♀ (female)"]
  POWER4 = female pin header, 8 pins [form="♀ (female)"]
  AD24 = female pin header, 8 pins [form="♀ (female)"]  # not connected
  IO33 = female pin header, 18 pins [form="♀ (female)"]  # not connected
  IO34 = female pin header, 18 pins [form="♀ (female)"]  # not connected
  IO35 = female pin header, 8 pins [form="♀ (female)"]
  ADL2 = female pin header, 8 pins [form="♀ (female)"]  # not connected
  ADH2 = female pin header, 8 pins [form="♀ (female)"]  # not connected
  Grove9 = Grove Infrared Emitter  # not connected
  Grove10 = Grove Infrared Emitter  # not connected
  Grove11 = Grove 3 Axis Digital Accelerometer 16g  # not connected
  Grove12 = Grove 3 Axis Digital Accelerometer 16g  # not connected

nets:
  N1: U9.IN, Power3.pin8
  N2: U9.CIN, RelayControl1.pin1, RelayControl1.pin2, RelayControl1.pin3, RelayControl1.pin4, RelayControl1.pin5, RelayControl1.pin6, RelayControl1.pin7, RelayControl1.pin8, RelayControl1.pin9, RelayControl1.pin10, RelayControl1.pin11, RelayControl1.pin12, RelayControl1.pin13, RelayControl1.pin14, RelayControl1.pin15
  N3: U9.COUT, Power_OUT1.4, IOH3.pin4, Power3.pin6, Power3.pin7
  N4: U9.OUT, Power_OUT1.3
  N5: Signal_OUT1.1, Reset2.pin1, Reset2.pin2, Reset2.pin3, Reset2.pin4, Reset2.pin5, Reset2.pin6, Reset2.pin7, Reset2.pin8, Reset2.pin9, Reset2.pin10, Reset2.pin11, Reset2.pin12, Reset2.pin13, Reset2.pin14, Reset2.pin15
  N6: Signal_OUT1.2, Shutdown1.pin1, Shutdown1.pin2, Shutdown1.pin3, Shutdown1.pin4, Shutdown1.pin5, Shutdown1.pin6, Shutdown1.pin7, Shutdown1.pin8, Shutdown1.pin9, Shutdown1.pin10, Shutdown1.pin11, Shutdown1.pin12, Shutdown1.pin13, Shutdown1.pin14, Shutdown1.pin15
  N7: Signal_OUT1.3, Rx2.pin1, Rx2.pin2, Rx2.pin3, Rx2.pin4, Rx2.pin5, Rx2.pin6, Rx2.pin7, Rx2.pin8, Rx2.pin9, Rx2.pin10, Rx2.pin11, Rx2.pin12, Rx2.pin13, Rx2.pin14, Rx2.pin15
  N8: Signal_OUT1.4, Tx2.pin1, Tx2.pin2, Tx2.pin3, Tx2.pin4, Tx2.pin5, Tx2.pin6, Tx2.pin7, Tx2.pin8, Tx2.pin9, Tx2.pin10, Tx2.pin11, Tx2.pin12, Tx2.pin13, Tx2.pin14, Tx2.pin15
  N9: Power_OUT1.2, Power3.pin4
  N10: IOH3.pin5, J99.pin1, J100.pin1, J101.pin1, J102.pin1, J103.pin1
  N11: IOH3.pin6, J99.pin2, J100.pin2, J101.pin2, J102.pin2, J103.pin2
  N12: IOH3.pin7, J99.pin3, J100.pin3, J101.pin3, J102.pin3, J103.pin3
  N13: IOH3.pin8, J99.pin4, J100.pin4, J101.pin4, J102.pin4, J103.pin4
  N14: IOH3.pin9, J99.pin5, J100.pin5, J101.pin5, J102.pin5, J103.pin5
  N15: IOH3.pin10, J99.pin6, J100.pin6, J101.pin6, J102.pin6, J103.pin6
  N16: J99.pin8, J100.pin8, J101.pin8, J102.pin8, J103.pin8, IOL3.pin1
  N17: J99.pin9, J100.pin9, J101.pin9, J102.pin9, J103.pin9, IOL3.pin2
  N18: J99.pin10, J100.pin10, J101.pin10, J102.pin10, J103.pin10, IOL3.pin3
  N19: J99.pin11, J100.pin11, J101.pin11, J102.pin11, J103.pin11, IOL3.pin4
  N20: J99.pin12, J100.pin12, J101.pin12, J102.pin12, J103.pin12, IOL3.pin5
  N21: J99.pin13, J100.pin13, J101.pin13, J102.pin13, J103.pin13, IOL3.pin6
  N22: J99.pin14, J100.pin14, J101.pin14, J102.pin14, J103.pin14, IOL3.pin7
  N23: J99.pin15, J100.pin15, J101.pin15, J102.pin15, J103.pin15, IOL3.pin8
  GND: Power_plug7.GND, Xbee3.GND, Vol1.leg2, Reset3.3, IOH6.pin4, Power6.pin6, Power6.pin7, J111.pin3, AE-MOD2.VSS
  N24: Power_plug7.VCC, Power6.pin8, AE-MOD2.Vbat, AE-MOD2.CE
  N25: Xbee3.VCC, Vol1.leg1, Power6.pin4, R2.Pin_1, AE-MOD2.Vout
  N26: Xbee3.pin2, IOL6.pin7
  N27: Xbee3.pin3, IOL6.pin8
  N28: Xbee3.pin4, IOH6.pin6
  N29: Xbee3.pin5, Reset3.2, Power6.pin3
  N30: Xbee3.pin6, IOH6.pin8
  N31: Xbee3.pin7, IOH6.pin7
  N32: Xbee3.pin9, IOH6.pin10
  N33: Xbee3.pin11, IOL6.pin4
  N34: Xbee3.pin12, IOL6.pin1
  N35: Xbee3.pin13, IOL6.pin5
  N36: Xbee3.pin14, J111.pin2
  N37: Xbee3.pin15, IOL6.pin3
  N38: Xbee3.pin16, IOL6.pin2
  N39: Xbee3.pin17, AD6.pin4
  N40: Xbee3.pin18, AD6.pin3
  N41: Xbee3.pin19, AD6.pin2
  N42: Xbee3.pin20, AD6.pin1
  N43: Vol1.wiper, J111.pin1
  N44: Reset3.1, R2.Pin_0
  N45: D9.cathode, Relay1.CIO#1, Power_OUT2.2, Power7.pin4
  N46: D9.anode, 2SC1816.C, Relay1.CIO#2
  N47: R3.Pin_0, RelayControl2.pin1, RelayControl2.pin2, RelayControl2.pin3, RelayControl2.pin4, RelayControl2.pin5, RelayControl2.pin6, RelayControl2.pin7, RelayControl2.pin8, RelayControl2.pin9, RelayControl2.pin10, RelayControl2.pin11, RelayControl2.pin12, RelayControl2.pin13
  N48: R3.Pin_1, R4.Pin_1, 2SC1816.B
  N49: R4.Pin_0, 2SC1816.E, Power_OUT2.4, IOH7.pin4, Power7.pin6, Power7.pin7
  N50: Relay1.SIO#0, Power7.pin8
  N51: Relay1.SIO#3, Power_OUT2.3
  N52: Signal_OUT2.1, Reset4.pin1, Reset4.pin2, Reset4.pin3, Reset4.pin4, Reset4.pin5, Reset4.pin6, Reset4.pin7, Reset4.pin8, Reset4.pin9, Reset4.pin10, Reset4.pin11, Reset4.pin12, Reset4.pin13
  N53: Signal_OUT2.2, Shutdown3.pin1, Shutdown3.pin2, Shutdown3.pin3, Shutdown3.pin4, Shutdown3.pin5, Shutdown3.pin6, Shutdown3.pin7, Shutdown3.pin8, Shutdown3.pin9, Shutdown3.pin10, Shutdown3.pin11, Shutdown3.pin12, Shutdown3.pin13, Shutdown3.pin14, Shutdown3.pin15
  N54: Signal_OUT2.3, Rx4.pin1, Rx4.pin2, Rx4.pin3, Rx4.pin4, Rx4.pin5, Rx4.pin6, Rx4.pin7, Rx4.pin8, Rx4.pin9, Rx4.pin10, Rx4.pin11, Rx4.pin12, Rx4.pin13, Rx4.pin14, Rx4.pin15
  N55: Signal_OUT2.4, Tx4.pin1, Tx4.pin2, Tx4.pin3, Tx4.pin4, Tx4.pin5, Tx4.pin6, Tx4.pin7, Tx4.pin8, Tx4.pin9, Tx4.pin10, Tx4.pin11, Tx4.pin12, Tx4.pin13, Tx4.pin14, Tx4.pin15
  N56: IOH7.pin5, J112.pin1, J113.pin1, J114.pin1, J115.pin1, J116.pin1
  N57: IOH7.pin6, J112.pin2, J113.pin2, J114.pin2, J115.pin2, J116.pin2
  N58: IOH7.pin7, J112.pin3, J113.pin3, J114.pin3, J115.pin3, J116.pin3
  N59: IOH7.pin8, J112.pin4, J113.pin4, J114.pin4, J115.pin4, J116.pin4
  N60: IOH7.pin9, J112.pin5, J113.pin5, J114.pin5, J115.pin5, J116.pin5
  N61: IOH7.pin10, J112.pin6, J113.pin6, J114.pin6, J115.pin6, J116.pin6
  N62: J112.pin8, J113.pin8, J114.pin8, J115.pin8, J116.pin8, IOL7.pin1
  N63: J112.pin9, J113.pin9, J114.pin9, J115.pin9, J116.pin9, IOL7.pin2
  N64: J112.pin10, J113.pin10, J114.pin10, J115.pin10, J116.pin10, IOL7.pin3
  N65: J112.pin11, J113.pin11, J114.pin11, J115.pin11, J116.pin11, IOL7.pin4
  N66: J112.pin12, J113.pin12, J114.pin12, J115.pin12, J116.pin12, IOL7.pin5
  N67: J112.pin13, J113.pin13, J114.pin13, J115.pin13, J116.pin13, IOL7.pin6
  N68: J113.pin14, J115.pin14, J116.pin14, IOL7.pin7
  N69: J113.pin15, J115.pin15, J116.pin15, IOL7.pin8
  N70: microSD3.CD, Card_detect3.pin1, Card_detect3.pin2, Card_detect3.pin3, Card_detect3.pin4, Card_detect3.pin5, Card_detect3.pin6, Card_detect3.pin7, Card_detect3.pin8, Card_detect3.pin9, Card_detect3.pin10, Card_detect3.pin11, Card_detect3.pin12
  N71: microSD3.CS, Chip_select3.pin1, Chip_select3.pin2, Chip_select3.pin3, Chip_select3.pin4, Chip_select3.pin5, Chip_select3.pin6, Chip_select3.pin7, Chip_select3.pin8, Chip_select3.pin9, Chip_select3.pin10, Chip_select3.pin11, Chip_select3.pin12
  N72: microSD3.DI, J147.pin1
  N73: microSD3.DO, J147.pin2
  N74: microSD3.CLK, J147.pin3
  N75: microSD3.GND, IOH16.pin4, POWER3.pin6, POWER3.pin7
  N76: microSD3.3v, S7.pin4
  N77: microSD3.5V, S7.pin1
  N78: IO21.pin1, J159.pin17, J160.pin17
  N79: IO21.pin2, J159.pin18, J160.pin18
  N80: IO21.pin3, J159.pin19, J160.pin19
  N81: IO21.pin4, J159.pin20, J160.pin20
  N82: IO21.pin5, J159.pin21, J160.pin21
  N83: IO21.pin6, J159.pin22, J160.pin22
  N84: IO21.pin7, J159.pin23, J160.pin23
  N85: IO21.pin8, J159.pin24, J160.pin24
  N86: SCL5.pin1, IOH15.pin1
  N87: SCL5.pin2, J158.pin8, IOL15.pin1
  N88: SCL5.pin3, AD22.pin6
  N89: J146.pin1, IOH16.pin7
  N90: J146.pin2, IOH16.pin6
  N91: J146.pin3, IOH16.pin5
  N92: SCL6.pin1, SCL6.pin2, SCL6.pin3, RTC9.SCL
  N93: SDA5.pin1, IOH15.pin2
  N94: SDA5.pin2, IOH15.pin10, J158.pin6
  N95: SDA5.pin3, AD22.pin5
  N96: J148.pin1, ICSP14.pin5
  N97: J148.pin2, ICSP14.pin1
  N98: J148.pin3, ICSP14.pin2
  N99: SDA6.pin1, SDA6.pin2, SDA6.pin3, RTC9.SDA
  N100: Power_IN4.2, LevelConverter4.LV
  N101: Power_IN4.3, Power15.pin8
  N102: Power_IN4.4, LevelConverter4.GND, IOH14.pin4, Power15.pin6, Power15.pin7
  N103: Signal_IN4.1, LevelConverter4.LV4
  N104: Signal_IN4.2, LevelConverter4.LV3
  N105: Signal_IN4.3, LevelConverter4.LV2
  N106: Signal_IN4.4, LevelConverter4.LV1
  N107: LevelConverter4.HV4, Power15.pin3
  N108: LevelConverter4.HV3, Shutdown6.pin1, Shutdown6.pin2, Shutdown6.pin3, Shutdown6.pin4, Shutdown6.pin5, Shutdown6.pin6, Shutdown6.pin7, Shutdown6.pin8, Shutdown6.pin9, Shutdown6.pin10, Shutdown6.pin11, Shutdown6.pin12, Shutdown6.pin13, Shutdown6.pin14, Shutdown6.pin15
  N109: LevelConverter4.HV, Power15.pin5
  N110: LevelConverter4.HV2, Rx9.pin1, Rx9.pin2, Rx9.pin3, Rx9.pin4, Rx9.pin5, Rx9.pin6, Rx9.pin7, Rx9.pin8, Rx9.pin9, Rx9.pin10, Rx9.pin11, Rx9.pin12, Rx9.pin13, Rx9.pin14, Rx9.pin15
  N111: LevelConverter4.HV1, Tx9.pin1, Tx9.pin2, Tx9.pin3, Tx9.pin4, Tx9.pin5, Tx9.pin6, Tx9.pin7, Tx9.pin8, Tx9.pin9, Tx9.pin10, Tx9.pin11, Tx9.pin12, Tx9.pin13, Tx9.pin14, Tx9.pin15
  N112: IOH14.pin5, J149.pin1, J151.pin1, J152.pin1
  N113: IOH14.pin6, J149.pin2, J151.pin2, J152.pin2
  N114: IOH14.pin7, J149.pin3, J151.pin3, J152.pin3
  N115: IOH14.pin8, J149.pin4, J151.pin4, J152.pin4
  N116: IOH14.pin9, J149.pin5, J151.pin5, J152.pin5
  N117: IOH14.pin10, J149.pin6, J151.pin6, J152.pin6
  N118: J149.pin8, J151.pin8, J152.pin8, IOL14.pin1
  N119: J149.pin9, J151.pin9, J152.pin9, IOL14.pin2
  N120: J149.pin10, J151.pin10, J152.pin10, IOL14.pin3
  N121: J149.pin11, J151.pin11, J152.pin11, IOL14.pin4
  N122: J149.pin12, J151.pin12, J152.pin12, IOL14.pin5
  N123: J149.pin13, J151.pin13, J152.pin13, IOL14.pin6
  N124: J149.pin14, J151.pin14, J152.pin14, IOL14.pin7
  N125: J149.pin15, J151.pin15, J152.pin15, IOL14.pin8
  N126: J150.pin1, IO24.pin5
  N127: J150.pin2, IO24.pin6
  N128: J150.pin3, IO24.pin7
  N129: J150.pin4, IO24.pin8
  N130: J150.pin5, IO24.pin9
  N131: J150.pin6, IO24.pin10
  N132: J150.pin8, IO25.pin1
  N133: J150.pin9, IO25.pin2
  N134: J150.pin10, IO25.pin3
  N135: J150.pin11, IO25.pin4
  N136: J150.pin12, IO25.pin5
  N137: J150.pin13, IO25.pin6
  N138: J150.pin14, IO25.pin7
  N139: J150.pin15, IO25.pin8
  N140: J150.pin17, IO27.pin1
  N141: J150.pin18, IO27.pin2
  N142: J150.pin19, IO27.pin3
  N143: J150.pin20, IO27.pin4
  N144: J150.pin21, IO27.pin5
  N145: J150.pin22, IO27.pin6
  N146: INT8.pin1, INT8.pin2, INT8.pin3, INT8.pin4, INT8.pin5, INT8.pin6, INT8.pin7, INT8.pin8, INT8.pin9, INT8.pin10, INT8.pin11, INT8.pin12, INT8.pin13, INT8.pin14, INT8.pin15, INT8.pin16, INT8.pin17, INT8.pin18, INT8.pin19, INT8.pin20, INT8.pin21, INT8.pin22, RTC8.INT
  N147: S6.pin0, IO27.pin8
  N148: S6.pin1, RTC8.SCL
  N149: S6.pin2, IO24.pin1
  N150: S6.pin3, IO27.pin7
  N151: S6.pin4, RTC8.SDA
  N152: S6.pin5, IO24.pin2
  N153: S7.pin0, POWER3.pin5
  N154: S7.pin5, POWER3.pin4
  N155: RTC8.GND, IO24.pin4, Power16.pin6, Power16.pin7, BAT8.-
  N156: RTC8.VDD, D17.cathode, D18.cathode
  N157: SW4.pin0, SW4.pin3, Power16.pin5
  N158: SW4.pin1, SW4.pin4, D18.anode
  N159: SW4.pin2, SW4.pin5, Power16.pin4
  N160: RTC9.INT, INT9.pin1, INT9.pin2, INT9.pin3, INT9.pin4, INT9.pin5, INT9.pin6, INT9.pin7, INT9.pin8, INT9.pin9, INT9.pin10, INT9.pin11, INT9.pin12, INT9.pin13, INT9.pin14, INT9.pin15
  N161: RTC9.GND, IOH15.pin4, Power18.pin6, Power18.pin7, BAT9.-
  N162: RTC9.VDD, D19.cathode, D20.cathode
  N163: D17.anode, BAT8.+
  N164: SW5.pin0, SW5.pin3, Power18.pin5
  N165: SW5.pin1, SW5.pin4, D20.anode
  N166: SW5.pin2, SW5.pin5, Power18.pin4
  N167: Power_IN5.2, LevelConverter5.LV
  N168: Power_IN5.3, Power17.pin8
  N169: Power_IN5.4, LevelConverter5.GND, IO26.pin4, Power17.pin6, Power17.pin7
  N170: Signal_IN5.1, LevelConverter5.LV4
  N171: Signal_IN5.2, LevelConverter5.LV3
  N172: Signal_IN5.3, LevelConverter5.LV2
  N173: Signal_IN5.4, LevelConverter5.LV1
  N174: LevelConverter5.HV4, Power17.pin3
  N175: LevelConverter5.HV3, Shutdown7.pin1, Shutdown7.pin2, Shutdown7.pin3, Shutdown7.pin4, Shutdown7.pin5, Shutdown7.pin6, Shutdown7.pin7, Shutdown7.pin8, Shutdown7.pin9, Shutdown7.pin10, Shutdown7.pin11, Shutdown7.pin12, Shutdown7.pin13, Shutdown7.pin14, Shutdown7.pin15, Shutdown7.pin16, Shutdown7.pin17, Shutdown7.pin18, Shutdown7.pin19, Shutdown7.pin20, Shutdown7.pin21, Shutdown7.pin22, Shutdown7.pin23, Shutdown7.pin24
  N176: LevelConverter5.HV, Power17.pin5
  N177: LevelConverter5.HV2, Rx10.pin1, Rx10.pin2, Rx10.pin3, Rx10.pin4, Rx10.pin5, Rx10.pin6, Rx10.pin7, Rx10.pin8, Rx10.pin9, Rx10.pin10, Rx10.pin11, Rx10.pin12, Rx10.pin13, Rx10.pin14, Rx10.pin15, Rx10.pin16, Rx10.pin17, Rx10.pin18, Rx10.pin19, Rx10.pin20, Rx10.pin21, Rx10.pin22, Rx10.pin23, Rx10.pin24
  N178: LevelConverter5.HV1, Tx10.pin1, Tx10.pin2, Tx10.pin3, Tx10.pin4, Tx10.pin5, Tx10.pin6, Tx10.pin7, Tx10.pin8, Tx10.pin9, Tx10.pin10, Tx10.pin11, Tx10.pin12, Tx10.pin13, Tx10.pin14, Tx10.pin15, Tx10.pin16, Tx10.pin17, Tx10.pin18, Tx10.pin19, Tx10.pin20, Tx10.pin21, Tx10.pin22, Tx10.pin23, Tx10.pin24
  N179: IO26.pin5, J153.pin1, J154.pin1, J155.pin1
  N180: IO26.pin6, J153.pin2, J154.pin2, J155.pin2
  N181: IO26.pin7, J153.pin3, J154.pin3, J155.pin3
  N182: IO26.pin8, J153.pin4, J154.pin4, J155.pin4
  N183: IO26.pin9, J153.pin5, J154.pin5, J155.pin5
  N184: IO26.pin10, J153.pin6, J154.pin6, J155.pin6
  N185: J153.pin8, J154.pin8, J155.pin8, IO28.pin1
  N186: J153.pin9, J154.pin9, J155.pin9, IO28.pin2
  N187: J153.pin10, J154.pin10, J155.pin10, IO28.pin3
  N188: J153.pin11, J154.pin11, J155.pin11, IO28.pin4
  N189: J153.pin12, J154.pin12, J155.pin12, IO28.pin5
  N190: J153.pin13, J154.pin13, J155.pin13, IO28.pin6
  N191: J153.pin14, J154.pin14, J155.pin14, IO28.pin7
  N192: J153.pin15, J154.pin15, J155.pin15, IO28.pin8
  N193: J153.pin17, J154.pin17, J155.pin17, IO35.pin1
  N194: J153.pin18, J154.pin18, J155.pin18, IO35.pin2
  N195: J153.pin19, J154.pin19, J155.pin19, IO35.pin3
  N196: J153.pin20, J154.pin20, J155.pin20, IO35.pin4
  N197: J153.pin21, J154.pin21, J155.pin21, IO35.pin5
  N198: J153.pin22, J154.pin22, J155.pin22, IO35.pin6
  N199: J153.pin23, J154.pin23, J155.pin23, IO35.pin7
  N200: J153.pin24, J154.pin24, J155.pin24, IO35.pin8
  N201: J156.pin1, J157.pin1, IOH16.pin8
  N202: J156.pin2, J157.pin2, IOH16.pin9
  N203: J156.pin3, J157.pin3, IOH16.pin10
  N204: J156.pin5, J157.pin5, IOL16.pin1
  N205: J156.pin6, J157.pin6, IOL16.pin2
  N206: J156.pin7, J157.pin7, IOL16.pin3
  N207: J156.pin8, J157.pin8, IOL16.pin4
  N208: J156.pin9, J157.pin9, IOL16.pin5
  N209: J156.pin10, J157.pin10, IOL16.pin6
  N210: J156.pin11, J157.pin11, IOL16.pin7
  N211: J156.pin12, J157.pin12, IOL16.pin8
  N212: S8.pin0, POWER4.pin5
  N213: S8.pin1, S8.pin2, microSD4.5V
  N214: S8.pin3, S8.pin4, microSD4.3v
  N215: S8.pin5, POWER4.pin4
  N216: D19.anode, BAT9.+
  N217: IOH15.pin5, J158.pin1
  N218: IOH15.pin6, J158.pin2
  N219: IOH15.pin7, J158.pin3
  N220: IOH15.pin8, J158.pin4
  N221: IOH15.pin9, J158.pin5
  N222: J158.pin9, IOL15.pin2
  N223: J158.pin10, IOL15.pin3
  N224: J158.pin11, IOL15.pin4
  N225: J158.pin12, IOL15.pin5
  N226: J158.pin13, IOL15.pin6
  N227: J158.pin14, IOL15.pin7
  N228: J158.pin15, IOL15.pin8
  N229: microSD4.CD, Card_detect4.pin1, Card_detect4.pin2, Card_detect4.pin3, Card_detect4.pin4, Card_detect4.pin5, Card_detect4.pin6, Card_detect4.pin7, Card_detect4.pin8, Card_detect4.pin9, Card_detect4.pin10, Card_detect4.pin11, Card_detect4.pin12, Card_detect4.pin13, Card_detect4.pin14, Card_detect4.pin15, Card_detect4.pin16, Card_detect4.pin17, Card_detect4.pin18, Card_detect4.pin19, Card_detect4.pin20, Card_detect4.pin21, Card_detect4.pin22, Card_detect4.pin23, Card_detect4.pin24
  N230: microSD4.CS, Chip_select4.pin1, Chip_select4.pin2, Chip_select4.pin3, Chip_select4.pin4, Chip_select4.pin5, Chip_select4.pin6, Chip_select4.pin7, Chip_select4.pin8, Chip_select4.pin9, Chip_select4.pin10, Chip_select4.pin11, Chip_select4.pin12, Chip_select4.pin13, Chip_select4.pin14, Chip_select4.pin15, Chip_select4.pin16, Chip_select4.pin17, Chip_select4.pin18, Chip_select4.pin19, Chip_select4.pin20, Chip_select4.pin21, Chip_select4.pin22, Chip_select4.pin23, Chip_select4.pin24
  N231: microSD4.DI, ICSP15.pin5
  N232: microSD4.DO, ICSP15.pin1
  N233: microSD4.CLK, ICSP15.pin2
  N234: microSD4.GND, IO31.pin4, POWER4.pin6, POWER4.pin7
  N235: J159.pin1, J160.pin1, IO31.pin5
  N236: J159.pin2, J160.pin2, IO31.pin6
  N237: J159.pin3, J160.pin3, IO31.pin7
  N238: J159.pin4, J160.pin4, IO31.pin8
  N239: J159.pin5, J160.pin5, IO31.pin9
  N240: J159.pin6, J160.pin6, IO31.pin10
  N241: J159.pin8, J160.pin8, IO32.pin1
  N242: J159.pin9, J160.pin9, IO32.pin2
  N243: J159.pin10, J160.pin10, IO32.pin3
  N244: J159.pin11, J160.pin11, IO32.pin4
  N245: J159.pin12, J160.pin12, IO32.pin5
  N246: J159.pin13, J160.pin13, IO32.pin6
  N247: J159.pin14, J160.pin14, IO32.pin7
  N248: J159.pin15, J160.pin15, IO32.pin8

notes:
  アプリケーションプロセッサ
  MEGA版
  UNO版
  電源制御回路から，電源を供給され，センサ処理を時刻情報付きで，マイクロSDに保存すると共に，電源制御回路に送る．
  電源制御回路
  通常眠っているXbeeが内蔵タイマで一定周期でケーションプロセッサに電源を供給する．
  一定時間以内にシリアルでアプリケーションプロセッサの処理結果が送られた場合，それを受け取り，外部に送信する．
  一定時間が経過すると，処理結果が帰ってきたか否かに関係なく，リレーをOFFして，アプリプロセッサの電源を落とし，自分も眠る．
  Arduino単独の場合と同様に，5V駆動のArduinoからロジックレベル変換でXbeeに接続すると，データの抜け落ちが多発し，本当にデータを読み取るには，SDを読むしか無い状況となる．

custom parts:
  RELAY-SIL05-1A72-71D: MEDER SIL05-1A72-71D RSコンポーネンツ 349-2884
  Arduino R3 6pin male header: Pin header for arduino R3
  Grove Header 4pin 90 degree direct mount: Header
  Power plug: 秋月電子通商 AE-DCJACK-DIPKIT-2.1mm-10A(通販コードK-06998)とその互換品(K06999,K-08415,K-08416)
  SSCI-KIT-XBSOCKET: Xbee pin conversion
  RELAY-G6L: OMRON G6L
  MicroSD Breakout: 5V-ready microSD Breakout with Level Shifter
  Bi-Directional Logic Level Converter: Description: If you've ever tried to connect a 3.3V device to a 5V system, you know what a challenge it can be. The SparkFun bi-directional logic level converter is a small device that safely steps down 5V signals to 3.3V AND steps up 3.3V to 5V at the same time. This level converter also works with 2.8V and 1.8V devices. What really separates this Logic level converter from our previous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
  Akizuki slide switch IS-2235: Akizuki slide switch is-2235 (P-02627)
  RTC-8564NB: Real Time Clock Module and I2C-BUS interface method. This product is a module of the SON 8-pin DIP package. Supply voltage 1.8-5.5V original version by KimuShige
  Akizuki slide switch IS-1250: Akizuki slide switch is-1250 (P-01665)
