# Fritzing sketch 全体構成図 (saved by Fritzing 0.9.2b)
perfboards: 4

parts:
  パーツ1 = Arduino Uno (Rev3)  # not connected
  J5 = female pin header, 6 pins [form="♀ (female)"]  # not connected
  J3 = female pin header, 8 pins [form="♀ (female)"]
  J2 = female pin header, 10 pins [form="♀ (female)"]
  J8 = male pin header, 15 pins [form="♂ (male)"]
  J13 = female pin header, 8 pins [form="♀ (female)"]
  J50 = female pin header, 10 pins [form="♀ (female)"]
  J52 = male pin header, 15 pins [form="♂ (male)"]
  J53 = female pin header, 8 pins [form="♀ (female)"]
  J54 = female pin header, 8 pins [form="♀ (female)"]
  J55 = female pin header, 6 pins [form="♀ (female)"]  # not connected
  J60 = male pin header, 15 pins [form="♂ (male)"]
  U7 = RELAY-2 [package=relay-g5v]
  J64 = male pin header, 15 pins [form="♂ (male)"]
  J65 = male pin header, 15 pins [form="♂ (male)"]
  J75 = female pin header, 4 pins [form="♀ (female)"]
  J76 = female pin header, 4 pins [form="♀ (female)"]
  J77 = male pin header, 15 pins [form="♂ (male)"]
  J78 = male pin header, 15 pins [form="♂ (male)"]
  J79 = male pin header, 15 pins [form="♂ (male)"]
  J14 = female pin header, 4 pins [form="♀ (female)"]
  J15 = female pin header, 4 pins [form="♀ (female)"]
  パーツ8 = Bi-Directional Logic Level Converter [part_number=BOB-12009]
  S1 = Momentary Switch [package=ksa_sealed_tac_switch]
  Power_plug5 = AE-DC-POWER-JACK-DIP [part_number=AE-DC-POWER-JACK-DIP]
  J66 = male pin header, 15 pins [form="♂ (male)"]
  J67 = male pin header, 15 pins [form="♂ (male)"]
  J68 = male pin header, 15 pins [form="♂ (male)"]
  J69 = male pin header, 15 pins [form="♂ (male)"]
  J80 = male pin header, 15 pins [form="♂ (male)"]
  J81 = male pin header, 15 pins [form="♂ (male)"]
  J82 = male pin header, 15 pins [form="♂ (male)"]
  J83 = male pin header, 15 pins [form="♂ (male)"]
  U9 = XBEE-1 [package=xbee-1]
  J89 = female pin header, 8 pins [form="♀ (female)"]
  J90 = female pin header, 10 pins [form="♀ (female)"]
  J91 = female pin header, 6 pins [form="♀ (female)"]
  J92 = female pin header, 8 pins [form="♀ (female)"]
  U10 = XCL101 [package=sc70-6]
  J93 = male pin header, 3 pins [form="♂ (male)"]
  R3 = Resistor StandUp [package=THT]
  R4 = Resistor StandUp [package=THT]
  S2 = Momentary Switch [package=ksa_sealed_tac_switch]
  U14 = XBEE-1 [package=xbee-1]
  Power_plug6 = AE-DC-POWER-JACK-DIP [part_number=AE-DC-POWER-JACK-DIP]
  J94 = female pin header, 10 pins [form="♀ (female)"]
  J95 = female pin header, 8 pins [form="♀ (female)"]
  J96 = female pin header, 8 pins [form="♀ (female)"]
  J97 = male pin header, 3 pins [form="♂ (male)"]
  J98 = female pin header, 6 pins [form="♀ (female)"]
  U16 = AE-LXDC55 [package=AE]

nets:
  N1: J3.pin1, J8.pin8, J80.pin8, J82.pin8
  N2: J3.pin2, J8.pin9, J80.pin9, J82.pin9
  N3: J3.pin3, J8.pin10, J80.pin10, J82.pin10
  N4: J3.pin4, J8.pin11, J80.pin11, J82.pin11
  N5: J3.pin5, J8.pin12, J80.pin12, J82.pin12
  N6: J3.pin6, J8.pin13, J80.pin13, J82.pin13
  N7: J3.pin7, J8.pin14, J80.pin14, J82.pin14
  N8: J3.pin8, J8.pin15, J80.pin15, J82.pin15
  N9: J2.pin5, J8.pin1, J80.pin1, J82.pin1
  N10: J2.pin6, J8.pin2, J80.pin2, J82.pin2
  N11: J2.pin7, J8.pin3, J80.pin3, J82.pin3
  N12: J2.pin8, J8.pin4, J80.pin4, J82.pin4
  N13: J2.pin9, J8.pin5, J80.pin5, J82.pin5
  N14: J2.pin10, J8.pin6, J80.pin6, J82.pin6
  N15: J13.pin3, パーツ8.HV4
  N16: J13.pin5, パーツ8.HV
  N17: J13.pin6, J13.pin7, パーツ8.GND
  N18: J13.pin8, J15.pin3
  N19: J50.pin5, J52.pin1, J64.pin1, J78.pin1, J66.pin1, J68.pin1
  N20: J50.pin6, J52.pin2, J64.pin2, J78.pin2, J66.pin2, J68.pin2
  N21: J50.pin7, J52.pin3, J64.pin3, J78.pin3, J66.pin3, J68.pin3
  N22: J50.pin8, J52.pin4, J64.pin4, J78.pin4, J66.pin4, J68.pin4
  N23: J50.pin9, J52.pin5, J64.pin5, J78.pin5, J66.pin5, J68.pin5
  N24: J50.pin10, J52.pin6, J64.pin6, J78.pin6, J66.pin6, J68.pin6
  N25: J52.pin8, J53.pin1, J64.pin8, J78.pin8, J66.pin8, J68.pin8
  N26: J52.pin9, J53.pin2, J64.pin9, J78.pin9, J66.pin9, J68.pin9
  N27: J52.pin10, J53.pin3, J64.pin10, J78.pin10, J66.pin10, J68.pin10
  N28: J52.pin11, J53.pin4, J64.pin11, J78.pin11, J66.pin11, J68.pin11
  N29: J52.pin12, J53.pin5, J64.pin12, J78.pin12, J66.pin12, J68.pin12
  N30: J52.pin13, J53.pin6, J64.pin13, J78.pin13, J66.pin13, J68.pin13
  N31: J52.pin14, J53.pin7, J64.pin14, J78.pin14, J66.pin14, J68.pin14
  N32: J52.pin15, J53.pin8, J64.pin15, J78.pin15, J66.pin15, J68.pin15
  N33: J54.pin4, J75.pin2
  N34: J54.pin6, U7.2
  N35: J54.pin7, J75.pin4
  N36: J54.pin8, U7.5
  N37: J60.pin1, J60.pin2, J60.pin3, J60.pin4, J60.pin5, J60.pin6, J60.pin7, J60.pin8, J60.pin9, J60.pin10, J60.pin11, J60.pin12, J60.pin13, J60.pin14, J60.pin15, U7.9
  N38: U7.6, J75.pin3
  N39: J65.pin1, J65.pin2, J65.pin3, J65.pin4, J65.pin5, J65.pin6, J65.pin7, J65.pin8, J65.pin9, J65.pin10, J65.pin11, J65.pin12, J65.pin13, J65.pin14, J65.pin15, J76.pin4
  N40: J76.pin1, J67.pin1, J67.pin2, J67.pin3, J67.pin4, J67.pin5, J67.pin6, J67.pin7, J67.pin8, J67.pin9, J67.pin10, J67.pin11, J67.pin12, J67.pin13, J67.pin14, J67.pin15
  N41: J76.pin2, J69.pin1, J69.pin2, J69.pin3, J69.pin4, J69.pin5, J69.pin6, J69.pin7, J69.pin8, J69.pin9, J69.pin10, J69.pin11, J69.pin12, J69.pin13, J69.pin14, J69.pin15
  N42: J76.pin3, J77.pin1, J77.pin2, J77.pin3, J77.pin4, J77.pin5, J77.pin6, J77.pin7, J77.pin8, J77.pin9, J77.pin10, J77.pin11, J77.pin12, J77.pin13, J77.pin14, J77.pin15
  N43: J79.pin1, J79.pin2, J79.pin3, J79.pin4, J79.pin5, J79.pin6, J79.pin7, J79.pin8, J79.pin9, J79.pin10, J79.pin11, J79.pin12, J79.pin13, J79.pin14, J79.pin15, パーツ8.HV3
  N44: J14.pin1, パーツ8.LV1
  N45: J14.pin2, パーツ8.LV2
  N46: J14.pin3, パーツ8.LV3
  N47: J14.pin4, パーツ8.LV4
  N48: J15.pin2, パーツ8.LV
  N49: パーツ8.HV2, J83.pin1, J83.pin2, J83.pin3, J83.pin4, J83.pin5, J83.pin6, J83.pin7, J83.pin8, J83.pin9, J83.pin10, J83.pin11, J83.pin12, J83.pin13, J83.pin14, J83.pin15
  N50: パーツ8.HV1, J81.pin1, J81.pin2, J81.pin3, J81.pin4, J81.pin5, J81.pin6, J81.pin7, J81.pin8, J81.pin9, J81.pin10, J81.pin11, J81.pin12, J81.pin13, J81.pin14, J81.pin15
  N51: S1.1, R3.Pin_0
  N52: S1.2, U9.RESET, J92.pin3
  N53: S1.3, Power_plug5.GND#0, Power_plug5.GND#2, J92.pin6, U10.VSS
  N54: Power_plug5.VCC#5, J92.pin8, U10.Vbat, U10.CE
  N55: U9.VDD, J92.pin4, U10.Vout, J93.pin1, R3.Pin_1
  N56: U9.DOUT, J89.pin7
  N57: U9.DIN, J89.pin8
  N58: U9.DIO12, J90.pin6
  N59: U9.RSSI, J90.pin8
  N60: U9.DIO11, J90.pin7
  N61: U9.RES, J93.pin2
  N62: U9.DTR, J90.pin10
  N63: U9.GND, J92.pin7, J93.pin3
  N64: U9.DIO4, J89.pin4
  N65: U9.CTS, J89.pin1
  N66: U9.DIO9, J89.pin5
  N67: U9.DIO5, J89.pin3
  N68: U9.RTS, J89.pin2
  N69: U9.DIO3, J91.pin4
  N70: U9.DIO2, J91.pin3
  N71: U9.DIO1, J91.pin2
  N72: U9.DIO0, J91.pin1
  N73: R4.Pin_0, S2.1
  N74: R4.Pin_1, U14.VDD, J96.pin4, J97.pin1, U16.OUT
  N75: S2.2, U14.RESET, J96.pin3
  N76: S2.3, Power_plug6.GND#0, Power_plug6.GND#2, J94.pin4, J96.pin6, U16.GND
  N77: U14.DOUT, J95.pin7
  N78: U14.DIN, J95.pin8
  N79: U14.DIO12, J94.pin6
  N80: U14.RSSI, J94.pin8
  N81: U14.DIO11, J94.pin7
  N82: U14.RES, J97.pin2
  N83: U14.DTR, J94.pin10
  N84: U14.GND, J96.pin7, J97.pin3
  N85: U14.DIO4, J95.pin4
  N86: U14.CTS, J95.pin1
  N87: U14.DIO9, J95.pin5
  N88: U14.DIO5, J95.pin3
  N89: U14.RTS, J95.pin2
  N90: U14.DIO3, J98.pin4
  N91: U14.DIO2, J98.pin3
  N92: U14.DIO1, J98.pin2
  N93: U14.DIO0, J98.pin1
  N94: Power_plug6.VCC#5, J96.pin8, U16.IN

custom parts:
  Bi-Directional Logic Level Converter: Description: If you've ever tried to connect a 3.3V device to a 5V system, you know what a challenge it can be. The SparkFun bi-directional logic level converter is a small device that safely steps down 5V signals to 3.3V AND steps up 3.3V to 5V at the same time. This level converter also works with 2.8V and 1.8V devices. What really separates this Logic level converter from our previous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
  AE-DC-POWER-JACK-DIP: 秋月電子通商 K-05148
  XCL101: AE-XCL101C331BR
  Resistor StandUp: A generic resistor (100mil stand-up)
  AE-LXDC55: AE-LXDC55-3.3V
