# Fritzing sketch Xbeeシステム例 (saved by Fritzing 0.9.2b)
perfboards: 3

parts:
  Grove1 = Grove 3 Axis Digital Accelerometer 16g  # not connected
  Grove3 = Grove 3 Axis Digital Accelerometer 16g  # not connected
  Power_plug7 = Power plug
  Xbee3 = SSCI-KIT-XBSOCKET
  J110 = Arduino R3 6pin male header [package=THT]  # not connected
  Vol1 = Trimmer Potentiometer [maximum_resistance=0.1MΩ package=THT]
  Reset3 = Momentary Switch [package=ksa_sealed_tac_switch]
  IOH6 = female pin header, 10 pins [form="♀ (female)"]
  IOL6 = female pin header, 8 pins [form="♀ (female)"]
  Power6 = female pin header, 8 pins [form="♀ (female)"]
  J111 = male pin header, 3 pins [form="♂ (male)"]
  AD6 = female pin header, 6 pins [form="♀ (female)"]
  R2 = Resistor [tolerance=±5% resistance=10k package=THT]
  AE-MOD2 = AE-XCL101C331BR-G
  VCC2 = Battery  # not connected
  R3 = Resistor [tolerance=±5% resistance=220 package=THT]  # not connected
  R4 = Resistor [tolerance=±5% resistance=220 package=THT]
  IC1 = IC, DIP package, 8 pins [chip_label=IC]  # not connected
  JP1 = Grove Header 4pin Straight direct mount [package=straight]  # not connected
  JP2 = Grove Header 4pin Straight direct mount [package=straight]
  C1 = Ceramic Capacitor [capacitance=100nF package="100 mil [THT, multilayer]"]  # not connected
  R5 = Resistor [tolerance=±5% resistance=220 package=THT]  # not connected
  R6 = Resistor [tolerance=±5% resistance=220 package=THT]
  IC2 = IC, DIP package, 8 pins [chip_label=IC]  # not connected
  JP3 = Grove Header 4pin Straight direct mount [package=straight]  # not connected
  JP4 = Grove Header 4pin Straight direct mount [package=straight]
  C2 = Ceramic Capacitor [capacitance=100nF package="100 mil [THT, multilayer]"]  # not connected

nets:
  GND: Power_plug7.GND, Xbee3.GND, Vol1.leg2, Reset3.3, IOH6.pin4, Power6.pin6, Power6.pin7, J111.pin3, AE-MOD2.VSS
  N1: Power_plug7.VCC, Power6.pin8, AE-MOD2.Vbat, AE-MOD2.CE
  N2: Xbee3.VCC, Vol1.leg1, Power6.pin4, R2.Pin_1, AE-MOD2.Vout
  N3: Xbee3.pin2, IOL6.pin7
  N4: Xbee3.pin3, IOL6.pin8
  N5: Xbee3.pin4, IOH6.pin6
  N6: Xbee3.pin5, Reset3.2, Power6.pin3
  N7: Xbee3.pin6, IOH6.pin8
  N8: Xbee3.pin7, IOH6.pin7
  N9: Xbee3.pin9, IOH6.pin10
  N10: Xbee3.pin11, IOL6.pin4
  N11: Xbee3.pin12, IOL6.pin1
  N12: Xbee3.pin13, IOL6.pin5
  N13: Xbee3.pin14, J111.pin2
  N14: Xbee3.pin15, IOL6.pin3
  N15: Xbee3.pin16, IOL6.pin2
  N16: Xbee3.pin17, AD6.pin4
  N17: Xbee3.pin18, AD6.pin3
  N18: Xbee3.pin19, AD6.pin2
  N19: Xbee3.pin20, AD6.pin1
  N20: Vol1.wiper, J111.pin1
  N21: Reset3.1, R2.Pin_0
  N22: R4.Pin_1, JP2.1
  N23: R6.Pin_1, JP4.1

custom parts:
  Power plug: 秋月電子通商 AE-DCJACK-DIPKIT-2.1mm-10A(通販コードK-06998)とその互換品(K06999,K-08415,K-08416)
  SSCI-KIT-XBSOCKET: Xbee pin conversion
  Arduino R3 6pin male header: Pin header for arduino R3
  Grove Header 4pin Straight direct mount: Header
