# Fritzing sketch AusExDHT_Ether_WebServer (saved by Fritzing 0.9.3b)
breadboards: 1

parts:
  DHT1 = DHT22 Humidity and Temperature Sensor
  パーツ1 = Arduino Mega 2560 (Rev3)  # not connected
  パーツ2 = Arduino Ethernet Shield (Rev3)

nets:
  VDD: DHT1.VDD, パーツ2.5V
  N1: DHT1.DATA, パーツ2.D2
  GND: DHT1.GND, パーツ2.GND
