# Fritzing sketch 3V3昇圧DCDCシールド (saved by Fritzing 0.9.2b)
perfboards: 1

parts:
  IOL = female pin header, 8 pins [form="♀ (female)"]  # not connected
  IOH = female pin header, 10 pins [form="♀ (female)"]
  AD = female pin header, 6 pins [form="♀ (female)"]  # not connected
  POWER = female pin header, 8 pins [form="♀ (female)"]
  ICSP = Arduino R3 6pin male header [package=THT]  # not connected
  AE-XCL101C331BR-G = AE-XCL101C331BR-G

nets:
  GND: IOH.pin4, POWER.pin6, POWER.pin7, AE-XCL101C331BR-G.VSS
  N1: POWER.pin4, AE-XCL101C331BR-G.Vout
  VIN: POWER.pin8, AE-XCL101C331BR-G.Vbat, AE-XCL101C331BR-G.CE

custom parts:
  Arduino R3 6pin male header: Pin header for arduino R3
