# Fritzing sketch 3V3降圧DCDCシールド (saved by Fritzing 0.9.2b)
perfboards: 1

parts:
  IOL = female pin header, 8 pins [form="♀ (female)"]  # not connected
  IOH = female pin header, 10 pins [form="♀ (female)"]
  AD = female pin header, 6 pins [form="♀ (female)"]  # not connected
  POWER = female pin header, 8 pins [form="♀ (female)"]
  ICSP = Arduino R3 6pin male header [package=THT]  # not connected
  AE-LXDC55-3_3V = AE-LXDC55-3.3V-Down

nets:
  GND: IOH.pin4, POWER.pin6, POWER.pin7, AE-LXDC55-3_3V.GND
  N1: POWER.pin4, AE-LXDC55-3_3V.OUT
  VIN: POWER.pin8, AE-LXDC55-3_3V.IN

custom parts:
  Arduino R3 6pin male header: Pin header for arduino R3
  AE-LXDC55-3.3V-Down: AE-LXDC55-3.3V upside down
