# Fritzing sketch Arduino相互接続インターフェース (saved by Fritzing 0.9.2b)
perfboards: 1

parts:
  AD = female pin header, 6 pins [form="♀ (female)"]  # not connected
  IOL = female pin header, 8 pins [form="♀ (female)"]
  IOH = female pin header, 10 pins [form="♀ (female)"]
  J1 = male pin header, 15 pins [form="♂ (male)"]
  Power = female pin header, 8 pins [form="♀ (female)"]
  Tx = male pin header, 15 pins [form="♂ (male)"]
  LevelConverter = Bi-Directional Logic Level Converter [part_number=BOB-12009]
  J2 = male pin header, 15 pins [form="♂ (male)"]
  Rx = male pin header, 15 pins [form="♂ (male)"]
  J3 = male pin header, 15 pins [form="♂ (male)"]
  Shutdown = male pin header, 15 pins [form="♂ (male)"]
  Signal_IN = Grove Header 4pin 90 degree direct mount [package="90 degree"]
  Power_IN = Grove Header 4pin 90 degree direct mount [package="90 degree"]
  ICSP = Arduino R3 6pin male header [package=THT]  # not connected

nets:
  N1: IOL.pin1, J1.pin8, J2.pin8, J3.pin8
  N2: IOL.pin2, J1.pin9, J2.pin9, J3.pin9
  N3: IOL.pin3, J1.pin10, J2.pin10, J3.pin10
  N4: IOL.pin4, J1.pin11, J2.pin11, J3.pin11
  N5: IOL.pin5, J1.pin12, J2.pin12, J3.pin12
  N6: IOL.pin6, J1.pin13, J2.pin13, J3.pin13
  N7: IOL.pin7, J1.pin14, J2.pin14, J3.pin14
  N8: IOL.pin8, J1.pin15, J2.pin15, J3.pin15
  GND: IOH.pin4, Power.pin6, Power.pin7, LevelConverter.GND, Power_IN.4
  N9: IOH.pin5, J1.pin1, J2.pin1, J3.pin1
  N10: IOH.pin6, J1.pin2, J2.pin2, J3.pin2
  N11: IOH.pin7, J1.pin3, J2.pin3, J3.pin3
  N12: IOH.pin8, J1.pin4, J2.pin4, J3.pin4
  N13: IOH.pin9, J1.pin5, J2.pin5, J3.pin5
  N14: IOH.pin10, J1.pin6, J2.pin6, J3.pin6
  N15: Power.pin3, LevelConverter.HV4
  N16: Power.pin5, LevelConverter.HV
  N17: Power.pin8, Power_IN.3
  N18: Tx.pin1, Tx.pin2, Tx.pin3, Tx.pin4, Tx.pin5, Tx.pin6, Tx.pin7, Tx.pin8, Tx.pin9, Tx.pin10, Tx.pin11, Tx.pin12, Tx.pin13, Tx.pin14, Tx.pin15, LevelConverter.HV1
  N19: LevelConverter.LV1, Signal_IN.4
  N20: LevelConverter.LV2, Signal_IN.3
  3V3: LevelConverter.LV, Power_IN.2
  N21: LevelConverter.LV3, Signal_IN.2
  N22: LevelConverter.LV4, Signal_IN.1
  N23: LevelConverter.HV3, Shutdown.pin1, Shutdown.pin2, Shutdown.pin3, Shutdown.pin4, Shutdown.pin5, Shutdown.pin6, Shutdown.pin7, Shutdown.pin8, Shutdown.pin9, Shutdown.pin10, Shutdown.pin11, Shutdown.pin12, Shutdown.pin13, Shutdown.pin14, Shutdown.pin15
  N24: LevelConverter.HV2, Rx.pin1, Rx.pin2, Rx.pin3, Rx.pin4, Rx.pin5, Rx.pin6, Rx.pin7, Rx.pin8, Rx.pin9, Rx.pin10, Rx.pin11, Rx.pin12, Rx.pin13, Rx.pin14, Rx.pin15

custom parts:
  Bi-Directional Logic Level Converter: Description: If you've ever tried to connect a 3.3V device to a 5V system, you know what a challenge it can be. The SparkFun bi-directional logic level converter is a small device that safely steps down 5V signals to 3.3V AND steps up 3.3V to 5V at the same time. This level converter also works with 2.8V and 1.8V devices. What really separates this Logic level converter from our previous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
  Grove Header 4pin 90 degree direct mount: Header
  Arduino R3 6pin male header: Pin header for arduino R3
