# Fritzing sketch DeadOnRTCシールド (saved by Fritzing 0.9.2b)
perfboards: 1

parts:
  IOH = female pin header, 10 pins [form="♀ (female)"]
  IOL = female pin header, 8 pins [form="♀ (female)"]
  AD = female pin header, 6 pins [form="♀ (female)"]  # not connected
  Power = female pin header, 8 pins [form="♀ (female)"]
  S1 = Akizuki slide switch IS-1250
  ICSP = Arduino R3 6pin male header [package=THT]
  BOB-1 = DeadOn RTC - DS3234 Breakout (for upside down) [part_number=BOB-10160]
  chip_select = male pin header, 12 pins [form="♂ (male)"]
  J1 = male pin header, 12 pins [form="♂ (male)"]
  SQW = male pin header, 12 pins [form="♂ (male)"]
  J2 = male pin header, 12 pins [form="♂ (male)"]
  J3 = male pin header, 3 pins [form="♂ (male)"]
  J4 = male pin header, 3 pins [form="♂ (male)"]
  J5 = male pin header, 3 pins [form="♂ (male)"]

nets:
  GND: IOH.pin4, Power.pin6, Power.pin7, BOB-1.GND
  SCLK: IOH.pin5, J3.pin3
  MISO: IOH.pin6, J3.pin2
  MOSI: IOH.pin7, J3.pin1
  N1: IOH.pin8, J1.pin1, J2.pin1
  N2: IOH.pin9, J1.pin2, J2.pin2
  N3: IOH.pin10, J1.pin3, J2.pin3
  N4: IOL.pin1, J1.pin5, J2.pin5
  N5: IOL.pin2, J1.pin6, J2.pin6
  N6: IOL.pin3, J1.pin7, J2.pin7
  N7: IOL.pin4, J1.pin8, J2.pin8
  N8: IOL.pin5, J1.pin9, J2.pin9
  N9: IOL.pin6, J1.pin10, J2.pin10
  N10: IOL.pin7, J1.pin11, J2.pin11
  N11: IOL.pin8, J1.pin12, J2.pin12
  N12: Power.pin4, S1.pin2, S1.pin5
  N13: Power.pin5, S1.pin0, S1.pin3
  N14: S1.pin1, S1.pin4, BOB-1.VCC
  N15: ICSP.pin1, J5.pin2
  N16: ICSP.pin2, J5.pin3
  N17: ICSP.pin5, J5.pin1
  chip select: BOB-1.SS, chip_select.pin1, chip_select.pin2, chip_select.pin3, chip_select.pin4, chip_select.pin5, chip_select.pin6, chip_select.pin7, chip_select.pin8, chip_select.pin9, chip_select.pin10, chip_select.pin11, chip_select.pin12
  N18: BOB-1.MOSI, J4.pin1
  N19: BOB-1.MISO, J4.pin2
  N20: BOB-1.SCLK, J4.pin3
  N21: BOB-1.INT/SQW, SQW.pin1, SQW.pin2, SQW.pin3, SQW.pin4, SQW.pin5, SQW.pin6, SQW.pin7, SQW.pin8, SQW.pin9, SQW.pin10, SQW.pin11, SQW.pin12

custom parts:
  Akizuki slide switch IS-1250: Akizuki slide switch is-1250 (P-01665)
  Arduino R3 6pin male header: Pin header for arduino R3
  DeadOn RTC - DS3234 Breakout (for upside down): Description: Here is a real time clock based on the DS3234 Real Time Clock IC. The DS3234 is a low-cost, extremely accurate SPI bus real-time clock with an integrated temperature-compensated crystal oscillator and crystal. The RTC maintains seconds, minutes, hours, day, date, month, and year information. The date at the end of the month is automatically adjusted for months with fewer than 31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
