# Fritzing sketch GR-kurumi基板変換(降圧直結両用) (saved by Fritzing 0.9.2b)
perfboards: 1

parts:
  IOH = female pin header, 10 pins [form="♀ (female)"]
  IOL = female pin header, 8 pins [form="♀ (female)"]
  AD = female pin header, 6 pins [form="♀ (female)"]
  Power = female pin header, 8 pins [form="♀ (female)"]
  Reset = Momentary Switch [package=ksa_sealed_tac_switch]
  Power_plug = Power plug
  ICSP = Arduino R3 6pin male header [package=THT]  # not connected
  R1 = Resistor [tolerance=±5% resistance=10k package=THT]
  D1 = Rectifier Diode [part_number=1N4001 package="300 mil [THT]"]
  GR-kurumi = GR kurumi (Renesas Gadget) no serial
  AE-LXDC55-3_3V = AE-LXDC55-3.3V-Down
  J2 = male pin header, 2 pins [form="♂ (male)"]
  J3 = male pin header, 2 pins [form="♂ (male)"]

nets:
  GND: IOH.pin4, Power.pin6, Power.pin7, Reset.4, Power_plug.GND, GR-kurumi.GND, AE-LXDC55-3_3V.GND
  SCLK: IOH.pin5, GR-kurumi.D13/SCLK
  MISO: IOH.pin6, GR-kurumi.D12/MISO
  MOSI: IOH.pin7, GR-kurumi.D11/Soft_PWM/MOSI
  SS: IOH.pin8, GR-kurumi.D10/RX2/SS
  N1: IOH.pin9, GR-kurumi.D9/TX2/PWM
  N2: IOH.pin10, GR-kurumi.D8/RX1/SDA
  N3: IOL.pin1, GR-kurumi.D7/TX1/SCL
  N4: IOL.pin2, GR-kurumi.D6/PWM
  N5: IOL.pin3, GR-kurumi.D5/PWM
  N6: IOL.pin4, GR-kurumi.D4
  N7: IOL.pin5, GR-kurumi.D3/INT1/PWM
  D2/VIN: IOL.pin6, GR-kurumi.D2/INT0, GR-kurumi.RAW, J2.pin2
  D1: IOL.pin7, GR-kurumi.D1/TX0
  D0: IOL.pin8, GR-kurumi.D0/RX0
  N8: AD.pin1, GR-kurumi.A0
  N9: AD.pin2, GR-kurumi.A1
  N10: AD.pin3, GR-kurumi.A2
  N11: AD.pin4, GR-kurumi.A3
  N12: AD.pin5, GR-kurumi.A4
  N13: AD.pin6, GR-kurumi.A5
  RST: Power.pin3, Reset.2, GR-kurumi.RST
  3.3V: Power.pin4, R1.Pin_1, D1.cathode, GR-kurumi.VCC, J3.pin2
  RAW: Power.pin8, Power_plug.VCC, AE-LXDC55-3_3V.IN, J2.pin1
  N14: Reset.1, R1.Pin_0, D1.anode
  N15: AE-LXDC55-3_3V.OUT, J3.pin1

custom parts:
  Power plug: 秋月電子通商 AE-DCJACK-DIPKIT-2.1mm-10A(通販コードK-06998)とその互換品(K06999,K-08415,K-08416)
  Arduino R3 6pin male header: Pin header for arduino R3
  GR kurumi (Renesas Gadget) no serial: RL78/G13
  AE-LXDC55-3.3V-Down: AE-LXDC55-3.3V upside down
