# Fritzing sketch GR-kurumi基板変換 (saved by Fritzing 0.9.2b)
perfboards: 1

parts:
  IOH = female pin header, 10 pins [form="♀ (female)"]
  IOL = female pin header, 8 pins [form="♀ (female)"]
  AD = female pin header, 6 pins [form="♀ (female)"]
  Power = female pin header, 8 pins [form="♀ (female)"]
  Reset = Momentary Switch [package=ksa_sealed_tac_switch]
  Power_plug1 = Power plug
  J1 = Arduino R3 6pin male header [package=THT]  # not connected
  R1 = Resistor [tolerance=±5% resistance=10k package=THT]
  D1 = Rectifier Diode [part_number=1N4001 package="300 mil [THT]"]
  Pro_Mini_5V_16MHz = GR kurumi (Renesas Gadget) no serial

nets:
  GND: IOH.pin4, Power.pin6, Power.pin7, Reset.4, Power_plug1.GND, Pro_Mini_5V_16MHz.GND
  SCLK: IOH.pin5, Pro_Mini_5V_16MHz.D13/SCLK
  MISO: IOH.pin6, Pro_Mini_5V_16MHz.D12/MISO
  MOSI: IOH.pin7, Pro_Mini_5V_16MHz.D11/Soft_PWM/MOSI
  SS: IOH.pin8, Pro_Mini_5V_16MHz.D10/RX2/SS
  N1: IOH.pin9, Pro_Mini_5V_16MHz.D9/TX2/PWM
  N2: IOH.pin10, Pro_Mini_5V_16MHz.D8/RX1/SDA
  N3: IOL.pin1, Pro_Mini_5V_16MHz.D7/TX1/SCL
  N4: IOL.pin2, Pro_Mini_5V_16MHz.D6/PWM
  N5: IOL.pin3, Pro_Mini_5V_16MHz.D5/PWM
  N6: IOL.pin4, Pro_Mini_5V_16MHz.D4
  N7: IOL.pin5, Pro_Mini_5V_16MHz.D3/INT1/PWM
  D2/RAW: IOL.pin6, Power.pin8, Power_plug1.VCC, Pro_Mini_5V_16MHz.D2/INT0, Pro_Mini_5V_16MHz.RAW
  D1: IOL.pin7, Pro_Mini_5V_16MHz.D1/TX0
  D0: IOL.pin8, Pro_Mini_5V_16MHz.D0/RX0
  N8: AD.pin1, Pro_Mini_5V_16MHz.A0
  N9: AD.pin2, Pro_Mini_5V_16MHz.A1
  N10: AD.pin3, Pro_Mini_5V_16MHz.A2
  N11: AD.pin4, Pro_Mini_5V_16MHz.A3
  N12: AD.pin5, Pro_Mini_5V_16MHz.A4
  N13: AD.pin6, Pro_Mini_5V_16MHz.A5
  RST: Power.pin3, Reset.2, Pro_Mini_5V_16MHz.RST
  VCC: Power.pin4, R1.Pin_1, D1.cathode, Pro_Mini_5V_16MHz.VCC
  5V: Power.pin5
  N14: Reset.1, R1.Pin_0, D1.anode

custom parts:
  Power plug: 秋月電子通商 AE-DCJACK-DIPKIT-2.1mm-10A(通販コードK-06998)とその互換品(K06999,K-08415,K-08416)
  Arduino R3 6pin male header: Pin header for arduino R3
  GR kurumi (Renesas Gadget) no serial: RL78/G13
