# Fritzing sketch RTC8564NB-Megaシールド (saved by Fritzing 0.9.2b)
perfboards: 1

parts:
  IO1 = female pin header, 10 pins [form="♀ (female)"]
  IO2 = female pin header, 8 pins [form="♀ (female)"]
  BAT = Battery Holders [package=battcom_20mm_pth]
  D1 = Schottky Diode [part_number=1N5817 package="300 mil [THT]"]
  D2 = Schottky Diode [part_number=1N5817 package="300 mil [THT]"]
  Power = female pin header, 8 pins [form="♀ (female)"]
  SW = Akizuki slide switch IS-1250
  ICSP = Arduino R3 6pin male header [package=THT]  # not connected
  RTC = RTC-8564NB [package="Module(DIP 8P)"]
  IO3 = female pin header, 8 pins [form="♀ (female)"]
  AD2 = female pin header, 8 pins [form="♀ (female)"]  # not connected
  S2 = Akizuki slide switch IS-2235
  AD1 = female pin header, 8 pins [form="♀ (female)"]  # not connected
  INT = male pin header, 22 pins [form="♂ (male)"]
  J1 = male pin header, 22 pins [form="♂ (male)"]
  IO4 = female pin header, 18 pins [form="♀ (female)"]  # not connected
  IO5 = female pin header, 18 pins [form="♀ (female)"]  # not connected

nets:
  SCL3: IO1.pin1, S2.pin2
  SDA3: IO1.pin2, S2.pin5
  GND: IO1.pin4, BAT.-, Power.pin6, Power.pin7, RTC.GND
  N1: IO1.pin5, J1.pin1
  N2: IO1.pin6, J1.pin2
  N3: IO1.pin7, J1.pin3
  N4: IO1.pin8, J1.pin4
  N5: IO1.pin9, J1.pin5
  N6: IO1.pin10, J1.pin6
  N7: IO2.pin1, J1.pin8
  N8: IO2.pin2, J1.pin9
  N9: IO2.pin3, J1.pin10
  N10: IO2.pin4, J1.pin11
  N11: IO2.pin5, J1.pin12
  N12: IO2.pin6, J1.pin13
  N13: IO2.pin7, J1.pin14
  N14: IO2.pin8, J1.pin15
  N15: BAT.+, D2.anode
  N16: D1.cathode, D2.cathode, RTC.VDD
  N17: D1.anode, SW.pin1, SW.pin4
  N18: Power.pin4, SW.pin2, SW.pin5
  N19: Power.pin5, SW.pin0, SW.pin3
  N20: RTC.INT, INT.pin1, INT.pin2, INT.pin3, INT.pin4, INT.pin5, INT.pin6, INT.pin7, INT.pin8, INT.pin9, INT.pin10, INT.pin11, INT.pin12, INT.pin13, INT.pin14, INT.pin15, INT.pin16, INT.pin17, INT.pin18, INT.pin19, INT.pin20, INT.pin21, INT.pin22
  SDA: RTC.SDA, S2.pin4
  SCL: RTC.SCL, S2.pin1
  N21: IO3.pin1, J1.pin17
  N22: IO3.pin2, J1.pin18
  N23: IO3.pin3, J1.pin19
  N24: IO3.pin4, J1.pin20
  N25: IO3.pin5, J1.pin21
  N26: IO3.pin6, J1.pin22
  N27: IO3.pin7, S2.pin3
  N28: IO3.pin8, S2.pin0

custom parts:
  Akizuki slide switch IS-1250: Akizuki slide switch is-1250 (P-01665)
  Arduino R3 6pin male header: Pin header for arduino R3
  RTC-8564NB: Real Time Clock Module and I2C-BUS interface method. This product is a module of the SON 8-pin DIP package. Supply voltage 1.8-5.5V original version by KimuShige
  Akizuki slide switch IS-2235: Akizuki slide switch is-2235 (P-02627)
