# Fritzing sketch Xbee-Megaシンプルシールド (saved by Fritzing 0.9.2b)
perfboards: 1

parts:
  IO1 = female pin header, 10 pins [form="♀ (female)"]
  IO2 = female pin header, 8 pins [form="♀ (female)"]
  Power = female pin header, 8 pins [form="♀ (female)"]
  Xbee = SSCI-KIT-XBSOCKET
  AD1 = female pin header, 8 pins [form="♀ (female)"]  # not connected
  AD2 = female pin header, 8 pins [form="♀ (female)"]  # not connected
  IO5 = female pin header, 18 pins [form="♀ (female)"]  # not connected
  IO4 = female pin header, 18 pins [form="♀ (female)"]  # not connected
  J1 = male pin header, 24 pins [form="♂ (male)"]
  IO3 = female pin header, 8 pins [form="♀ (female)"]
  J2 = male pin header, 24 pins [form="♂ (male)"]
  J4 = male pin header, 21 pins [form="♂ (male)"]
  J5 = male pin header, 21 pins [form="♂ (male)"]
  J6 = male pin header, 21 pins [form="♂ (male)"]
  J7 = male pin header, 21 pins [form="♂ (male)"]
  Tx = male pin header, 24 pins [form="♂ (male)"]
  Reset = male pin header, 21 pins [form="♂ (male)"]
  RSSI = male pin header, 21 pins [form="♂ (male)"]
  Associate = male pin header, 21 pins [form="♂ (male)"]
  ON/Sleep = male pin header, 21 pins [form="♂ (male)"]
  Rx = male pin header, 24 pins [form="♂ (male)"]
  DTR/Sleep = male pin header, 21 pins [form="♂ (male)"]
  J3 = male pin header, 21 pins [form="♂ (male)"]
  LC = M-04522
  S1 = Akizuki slide switch IS-1250

nets:
  GND: IO1.pin4, Power.pin6, Power.pin7, Xbee.GND, LC.GND, LC.OE
  N1: IO1.pin5, J1.pin1, J2.pin1
  N2: IO1.pin6, J1.pin2, J2.pin2
  N3: IO1.pin7, J1.pin3, J2.pin3
  N4: IO1.pin8, J1.pin4, J2.pin4, J4.pin1, J5.pin1, J6.pin1, J7.pin1, J3.pin1
  N5: IO1.pin9, J1.pin5, J2.pin5, J4.pin2, J5.pin2, J6.pin2, J7.pin2, J3.pin2
  N6: IO1.pin10, J1.pin6, J2.pin6, J4.pin3, J5.pin3, J6.pin3, J7.pin3, J3.pin3
  N7: IO2.pin1, J1.pin8, J2.pin8, J4.pin5, J5.pin5, J6.pin5, J7.pin5, J3.pin5
  N8: IO2.pin2, J1.pin9, J2.pin9, J4.pin6, J5.pin6, J6.pin6, J7.pin6, J3.pin6
  N9: IO2.pin3, J1.pin10, J2.pin10, J4.pin7, J5.pin7, J6.pin7, J7.pin7, J3.pin7
  N10: IO2.pin4, J1.pin11, J2.pin11, J4.pin8, J5.pin8, J6.pin8, J7.pin8, J3.pin8
  N11: IO2.pin5, J1.pin12, J2.pin12, J4.pin9, J5.pin9, J6.pin9, J7.pin9, J3.pin9
  N12: IO2.pin6, J1.pin13, J2.pin13, J4.pin10, J5.pin10, J6.pin10, J7.pin10, J3.pin10
  N13: IO2.pin7, J1.pin14, J2.pin14, J4.pin11, J5.pin11, J6.pin11, J7.pin11, J3.pin11
  N14: IO2.pin8, J1.pin15, J2.pin15, J4.pin12, J5.pin12, J6.pin12, J7.pin12, J3.pin12
  3.3V: Power.pin4, Xbee.VCC, LC.VCCA, S1.pin0, S1.pin3
  5V: Power.pin5, S1.pin2, S1.pin5
  N15: Xbee.pin2, LC.A0
  N16: Xbee.pin3, LC.A1
  N17: Xbee.pin5, LC.A2
  N18: Xbee.pin6, LC.A3
  N19: Xbee.pin9, LC.A4
  ON3V: Xbee.pin13, LC.A6
  ASSOC3V: Xbee.pin15, LC.A5
  N20: J1.pin17, IO3.pin1, J2.pin17, J4.pin14, J5.pin14, J6.pin14, J7.pin14, J3.pin14
  N21: J1.pin18, IO3.pin2, J2.pin18, J4.pin15, J5.pin15, J6.pin15, J7.pin15, J3.pin15
  N22: J1.pin19, IO3.pin3, J2.pin19, J4.pin16, J5.pin16, J6.pin16, J7.pin16, J3.pin16
  N23: J1.pin20, IO3.pin4, J2.pin20, J4.pin17, J5.pin17, J6.pin17, J7.pin17, J3.pin17
  N24: J1.pin21, IO3.pin5, J2.pin21, J4.pin18, J5.pin18, J6.pin18, J7.pin18, J3.pin18
  N25: J1.pin22, IO3.pin6, J2.pin22, J4.pin19, J5.pin19, J6.pin19, J7.pin19, J3.pin19
  N26: J1.pin23, IO3.pin7, J2.pin23, J4.pin20, J5.pin20, J6.pin20, J7.pin20, J3.pin20
  N27: J1.pin24, IO3.pin8, J2.pin24, J4.pin21, J5.pin21, J6.pin21, J7.pin21, J3.pin21
  Tx: Tx.pin1, Tx.pin2, Tx.pin3, Tx.pin4, Tx.pin5, Tx.pin6, Tx.pin7, Tx.pin8, Tx.pin9, Tx.pin10, Tx.pin11, Tx.pin12, Tx.pin13, Tx.pin14, Tx.pin15, Tx.pin16, Tx.pin17, Tx.pin18, Tx.pin19, Tx.pin20, Tx.pin21, Tx.pin22, Tx.pin23, Tx.pin24, LC.B0
  RST: Reset.pin1, Reset.pin2, Reset.pin3, Reset.pin4, Reset.pin5, Reset.pin6, Reset.pin7, Reset.pin8, Reset.pin9, Reset.pin10, Reset.pin11, Reset.pin12, Reset.pin13, Reset.pin14, Reset.pin15, Reset.pin16, Reset.pin17, Reset.pin18, Reset.pin19, Reset.pin20, Reset.pin21, LC.B2
  RSSI: RSSI.pin1, RSSI.pin2, RSSI.pin3, RSSI.pin4, RSSI.pin5, RSSI.pin6, RSSI.pin7, RSSI.pin8, RSSI.pin9, RSSI.pin10, RSSI.pin11, RSSI.pin12, RSSI.pin13, RSSI.pin14, RSSI.pin15, RSSI.pin16, RSSI.pin17, RSSI.pin18, RSSI.pin19, RSSI.pin20, RSSI.pin21, LC.B3
  ASSOC: Associate.pin1, Associate.pin2, Associate.pin3, Associate.pin4, Associate.pin5, Associate.pin6, Associate.pin7, Associate.pin8, Associate.pin9, Associate.pin10, Associate.pin11, Associate.pin12, Associate.pin13, Associate.pin14, Associate.pin15, Associate.pin16, Associate.pin17, Associate.pin18, Associate.pin19, Associate.pin20, Associate.pin21, LC.B5
  ON: ON/Sleep.pin1, ON/Sleep.pin2, ON/Sleep.pin3, ON/Sleep.pin4, ON/Sleep.pin5, ON/Sleep.pin6, ON/Sleep.pin7, ON/Sleep.pin8, ON/Sleep.pin9, ON/Sleep.pin10, ON/Sleep.pin11, ON/Sleep.pin12, ON/Sleep.pin13, ON/Sleep.pin14, ON/Sleep.pin15, ON/Sleep.pin16, ON/Sleep.pin17, ON/Sleep.pin18, ON/Sleep.pin19, ON/Sleep.pin20, ON/Sleep.pin21, LC.B6
  Rx: Rx.pin1, Rx.pin2, Rx.pin3, Rx.pin4, Rx.pin5, Rx.pin6, Rx.pin7, Rx.pin8, Rx.pin9, Rx.pin10, Rx.pin11, Rx.pin12, Rx.pin13, Rx.pin14, Rx.pin15, Rx.pin16, Rx.pin17, Rx.pin18, Rx.pin19, Rx.pin20, Rx.pin21, Rx.pin22, Rx.pin23, Rx.pin24, LC.B1
  DTR/Sleep: DTR/Sleep.pin1, DTR/Sleep.pin2, DTR/Sleep.pin3, DTR/Sleep.pin4, DTR/Sleep.pin5, DTR/Sleep.pin6, DTR/Sleep.pin7, DTR/Sleep.pin8, DTR/Sleep.pin9, DTR/Sleep.pin10, DTR/Sleep.pin11, DTR/Sleep.pin12, DTR/Sleep.pin13, DTR/Sleep.pin14, DTR/Sleep.pin15, DTR/Sleep.pin16, DTR/Sleep.pin17, DTR/Sleep.pin18, DTR/Sleep.pin19, DTR/Sleep.pin20, DTR/Sleep.pin21, LC.B4
  N28: LC.VCCB, S1.pin1, S1.pin4

custom parts:
  SSCI-KIT-XBSOCKET: Xbee pin conversion
  M-04522: Akizuki 8bit bi-directional logic level converter M-04522
  Akizuki slide switch IS-1250: Akizuki slide switch is-1250 (P-01665)
