# Fritzing sketch Xbeeシールド (saved by Fritzing 0.9.2b)
perfboards: 1

parts:
  IOH = female pin header, 10 pins [form="♀ (female)"]
  J1 = male pin header, 15 pins [form="♂ (male)"]
  IOL = female pin header, 8 pins [form="♀ (female)"]
  Power = female pin header, 8 pins [form="♀ (female)"]
  AD = female pin header, 6 pins [form="♀ (female)"]
  INT = male pin header, 15 pins [form="♂ (male)"]
  J2 = male pin header, 15 pins [form="♂ (male)"]
  Tx = male pin header, 15 pins [form="♂ (male)"]
  J3 = male pin header, 15 pins [form="♂ (male)"]
  Rx = male pin header, 15 pins [form="♂ (male)"]
  Xbee = SSCI-KIT-XBSOCKET
  ICSP = Arduino R3 6pin male header [package=THT]  # not connected
  J9 = male pin header, 6 pins [form="♂ (male)"]
  J4 = male pin header, 13 pins [form="♂ (male)"]
  J5 = male pin header, 13 pins [form="♂ (male)"]
  J6 = male pin header, 13 pins [form="♂ (male)"]
  J7 = male pin header, 13 pins [form="♂ (male)"]
  J8 = male pin header, 13 pins [form="♂ (male)"]
  Reset = male pin header, 13 pins [form="♂ (male)"]
  RSSI = male pin header, 13 pins [form="♂ (male)"]
  Sleep_RQ = male pin header, 13 pins [form="♂ (male)"]
  Associate = male pin header, 13 pins [form="♂ (male)"]
  ON/Sleep = male pin header, 15 pins [form="♂ (male)"]

nets:
  GND: IOH.pin4, IOH.pin5, J1.pin1, Power.pin6, Power.pin7, J2.pin1, J3.pin1, Xbee.GND, J4.pin1, J5.pin1, J6.pin1, J7.pin1, J8.pin1
  N1: IOH.pin6, J1.pin2, J2.pin2, J3.pin2, J4.pin2, J5.pin2, J6.pin2, J7.pin2, J8.pin2
  N2: IOH.pin7, J1.pin3, J2.pin3, J3.pin3, J4.pin3, J5.pin3, J6.pin3, J7.pin3, J8.pin3
  N3: IOH.pin8, J1.pin4, J2.pin4, J3.pin4, J4.pin4, J5.pin4, J6.pin4, J7.pin4, J8.pin4
  N4: IOH.pin9, J1.pin5, J2.pin5, J3.pin5, J4.pin5, J5.pin5, J6.pin5, J7.pin5, J8.pin5
  N5: IOH.pin10, J1.pin6, J2.pin6, J3.pin6, J4.pin6, J5.pin6, J6.pin6, J7.pin6, J8.pin6
  N6: J1.pin8, IOL.pin1, J2.pin8, J3.pin8, J4.pin8, J5.pin8, J6.pin8, J7.pin8, J8.pin8
  N7: J1.pin9, IOL.pin2, J2.pin9, J3.pin9, J4.pin9, J5.pin9, J6.pin9, J7.pin9, J8.pin9
  N8: J1.pin10, IOL.pin3, J2.pin10, J3.pin10, J4.pin10, J5.pin10, J6.pin10, J7.pin10, J8.pin10
  N9: J1.pin11, IOL.pin4, J2.pin11, J3.pin11, J4.pin11, J5.pin11, J6.pin11, J7.pin11, J8.pin11
  N10: J1.pin12, IOL.pin5, J2.pin12, J3.pin12, J4.pin12, J5.pin12, J6.pin12, J7.pin12, J8.pin12
  N11: J1.pin13, IOL.pin6, J2.pin13, J3.pin13, J4.pin13, J5.pin13, J6.pin13, J7.pin13, J8.pin13
  N12: J1.pin14, IOL.pin7, J2.pin14, J3.pin14
  N13: J1.pin15, IOL.pin8, J2.pin15, J3.pin15
  3.3V: Power.pin4, Xbee.VCC
  N14: AD.pin1, J9.pin1
  N15: AD.pin2, J9.pin2
  N16: AD.pin3, J9.pin3
  N17: AD.pin4, J9.pin4
  N18: AD.pin5, J9.pin5
  N19: AD.pin6, J9.pin6
  INT: INT.pin1, INT.pin2, INT.pin3, INT.pin4, INT.pin5, INT.pin6, INT.pin7, INT.pin8, INT.pin9, INT.pin10, INT.pin11, INT.pin12, INT.pin13, INT.pin14, INT.pin15, Xbee.pin4
  Tx: Tx.pin1, Tx.pin2, Tx.pin3, Tx.pin4, Tx.pin5, Tx.pin6, Tx.pin7, Tx.pin8, Tx.pin9, Tx.pin10, Tx.pin11, Tx.pin12, Tx.pin13, Tx.pin14, Tx.pin15, Xbee.pin2
  Rx: Rx.pin1, Rx.pin2, Rx.pin3, Rx.pin4, Rx.pin5, Rx.pin6, Rx.pin7, Rx.pin8, Rx.pin9, Rx.pin10, Rx.pin11, Rx.pin12, Rx.pin13, Rx.pin14, Rx.pin15, Xbee.pin3
  RST: Xbee.pin5, Reset.pin1, Reset.pin2, Reset.pin3, Reset.pin4, Reset.pin5, Reset.pin6, Reset.pin7, Reset.pin8, Reset.pin9, Reset.pin10, Reset.pin11, Reset.pin12, Reset.pin13
  RSSI: Xbee.pin6, Xbee.pin11, RSSI.pin1, RSSI.pin2, RSSI.pin3, RSSI.pin4, RSSI.pin5, RSSI.pin6, RSSI.pin7, RSSI.pin8, RSSI.pin9, RSSI.pin10, RSSI.pin11, RSSI.pin12, RSSI.pin13
  DTR/Sleep: Xbee.pin9, Sleep_RQ.pin1, Sleep_RQ.pin2, Sleep_RQ.pin3, Sleep_RQ.pin4, Sleep_RQ.pin5, Sleep_RQ.pin6, Sleep_RQ.pin7, Sleep_RQ.pin8, Sleep_RQ.pin9, Sleep_RQ.pin10, Sleep_RQ.pin11, Sleep_RQ.pin12, Sleep_RQ.pin13
  ON: Xbee.pin13, ON/Sleep.pin1, ON/Sleep.pin2, ON/Sleep.pin3, ON/Sleep.pin4, ON/Sleep.pin5, ON/Sleep.pin6, ON/Sleep.pin7, ON/Sleep.pin8, ON/Sleep.pin9, ON/Sleep.pin10, ON/Sleep.pin11, ON/Sleep.pin12, ON/Sleep.pin13, ON/Sleep.pin14, ON/Sleep.pin15
  ASSOC: Xbee.pin15, Associate.pin1, Associate.pin2, Associate.pin3, Associate.pin4, Associate.pin5, Associate.pin6, Associate.pin7, Associate.pin8, Associate.pin9, Associate.pin10, Associate.pin11, Associate.pin12, Associate.pin13

custom parts:
  SSCI-KIT-XBSOCKET: Xbee pin conversion
  Arduino R3 6pin male header: Pin header for arduino R3
