# Fritzing sketch grove-Xbeeシールド (saved by Fritzing 0.9.2b)
perfboards: 2

parts:
  IOL = female pin header, 8 pins [form="♀ (female)"]
  IOH = female pin header, 10 pins [form="♀ (female)"]
  AD = female pin header, 6 pins [form="♀ (female)"]
  Power = female pin header, 8 pins [form="♀ (female)"]
  J2 = male pin header, 2 pins [form="♂ (male)"]
  M-04522 = M-04522
  ICSP = Arduino R3 6pin male header [package=THT]  # not connected
  S1 = Akizuki slide switch IS-1250
  AD1 = Grove Header 4pin Straight direct mount [package=straight]
  AD2 = Grove Header 4pin Straight direct mount [package=straight]
  AD3 = Grove Header 4pin Straight direct mount [package=straight]
  AD4 = Grove Header 4pin Straight direct mount [package=straight]
  D1 = Grove Header 4pin Straight direct mount [package=straight]
  D2 = Grove Header 4pin Straight direct mount [package=straight]
  D3 = Grove Header 4pin Straight direct mount [package=straight]
  D4 = Grove Header 4pin Straight direct mount [package=straight]
  S2 = Akizuki slide switch IS-2235
  S3 = Akizuki slide switch IS-2235
  S4 = Akizuki slide switch IS-2235
  S5 = Akizuki slide switch IS-2235

nets:
  A5: IOL.pin2, M-04522.A5
  A4: IOL.pin5, M-04522.A4
  A7: IOH.pin6, M-04522.A7
  A6: IOH.pin7, M-04522.A6
  N1: AD.pin1, S5.pin1, S5.pin5
  N2: AD.pin2, S4.pin1, S4.pin5
  N3: AD.pin3, S3.pin1, S3.pin5
  N4: AD.pin4, S2.pin1, S2.pin5
  3.3V: Power.pin4, M-04522.VCCA, S1.pin0, S1.pin3
  5V: Power.pin5, M-04522.VCCB, S1.pin2, S1.pin5
  GND: Power.pin6, Power.pin7, J2.pin1, M-04522.GND, AD1.1, AD2.1, AD3.1, AD4.1, D1.1, D2.1, D3.1, D4.1
  N5: J2.pin2, M-04522.OE
  A0: M-04522.A0, S5.pin0
  A1: M-04522.A1, S4.pin0
  A2: M-04522.A2, S3.pin0
  A3: M-04522.A3, S2.pin0
  B0: M-04522.B0, S5.pin3
  B1: M-04522.B1, S4.pin3
  B2: M-04522.B2, S3.pin3
  B3: M-04522.B3, S2.pin3
  B4: M-04522.B4, AD4.3, D1.4
  B5: M-04522.B5, D1.3, D2.4
  B6: M-04522.B6, D2.3, D3.4
  B7: M-04522.B7, D3.3, D4.4
  VDD: S1.pin1, S1.pin4, AD1.2, AD2.2, AD3.2, AD4.2, D1.2, D2.2, D3.2, D4.2
  N6: AD1.3, AD2.4
  N7: AD1.4, S5.pin4
  N8: AD2.3, AD3.4, S3.pin4
  N9: AD3.3, AD4.4, S2.pin4

custom parts:
  M-04522: Akizuki 8bit bi-directional logic level converter M-04522
  Arduino R3 6pin male header: Pin header for arduino R3
  Akizuki slide switch IS-1250: Akizuki slide switch is-1250 (P-01665)
  Grove Header 4pin Straight direct mount: Header
  Akizuki slide switch IS-2235: Akizuki slide switch is-2235 (P-02627)
