# Fritzing sketch grove3v3シールド (saved by Fritzing 0.9.2b)
perfboards: 1

parts:
  IOL = female pin header, 8 pins [form="♀ (female)"]
  IOH = female pin header, 10 pins [form="♀ (female)"]
  AD = female pin header, 6 pins [form="♀ (female)"]
  Power = female pin header, 8 pins [form="♀ (female)"]
  D_IF_3 = double row male pin header, 4 pins [form="♂ (male)"]
  D_IF_4 = double row male pin header, 4 pins [form="♂ (male)"]
  D_IF_2 = double row male pin header, 4 pins [form="♂ (male)"]
  AD_IF_1 = double row male pin header, 4 pins [form="♂ (male)"]
  AD_IF_4 = double row male pin header, 4 pins [form="♂ (male)"]
  AD_IF_3 = double row male pin header, 4 pins [form="♂ (male)"]
  D_IF_1 = double row male pin header, 4 pins [form="♂ (male)"]
  AD_switch1 = Akizuki slide switch IS-2235
  AD_switch2 = Akizuki slide switch IS-2235
  AD_switch4 = Akizuki slide switch IS-2235
  D_switch1 = Akizuki slide switch IS-2235
  D_switch2 = Akizuki slide switch IS-2235
  D_switch3 = Akizuki slide switch IS-2235
  D_switch4 = Akizuki slide switch IS-2235
  AD_IF_2 = double row male pin header, 4 pins [form="♂ (male)"]
  J1 = male pin header, 2 pins [form="♂ (male)"]
  AD_switch3 = Akizuki slide switch IS-2235
  LC = M-04522 [part_number=M-04522]
  AE-MOD1 = M-04522 [part_number=M-04522]  # not connected
  S1 = Akizuki slide switch IS-2235  # not connected
  S2 = Akizuki slide switch IS-2235  # not connected
  U1 = DS3234 [package=ds3234]  # not connected
  パーツ2 = DeadOn RTC - DS3234 Breakout  # not connected
  パーツ3 = DeadOn RTC - DS3234 Breakout (for upside down)  # not connected
  パーツ4 = Bluetooth Mate Silver  # not connected
  microSD_Transflash1 = SparkFun - microSD Transflash  # not connected
  I2C/SPI_to_Serial1 = SparkFun - I2C/SPI-to-UART Breakout - SC16IS750 [part_number=BOB-09981]  # not connected

nets:
  N1: IOL.pin2, D_switch2.pin1, D_switch2.pin5
  N2: IOL.pin5, D_switch1.pin1, D_switch1.pin5
  N3: IOH.pin6, D_switch4.pin1, D_switch4.pin5
  N4: IOH.pin7, D_switch3.pin1, D_switch3.pin5
  N5: AD.pin1, AD_switch1.pin1, AD_switch1.pin5
  N6: AD.pin2, AD_switch2.pin1, AD_switch2.pin5
  N7: AD.pin3, AD_switch3.pin1, AD_switch3.pin5
  N8: AD.pin4, AD_switch4.pin1, AD_switch4.pin5
  N9: Power.pin4, LC.VCCA
  N10: Power.pin5, D_IF_3.pin3, D_IF_4.pin3, D_IF_2.pin3, AD_IF_1.pin2, AD_IF_4.pin2, AD_IF_3.pin2, D_IF_1.pin2, AD_IF_2.pin2, LC.VCCB
  N11: Power.pin6, D_IF_3.pin4, D_IF_4.pin4, D_IF_2.pin4, AD_IF_1.pin1, AD_IF_4.pin1, AD_IF_3.pin1, D_IF_1.pin1, AD_IF_2.pin1
  N12: Power.pin7, J1.pin1, LC.GND
  N13: D_IF_3.pin1, D_IF_2.pin2, D_switch3.pin4
  N14: D_IF_3.pin2, D_IF_4.pin1, D_switch4.pin4
  N15: D_IF_2.pin1, D_IF_1.pin3, D_switch2.pin4
  N16: AD_IF_1.pin3, AD_switch2.pin4, AD_IF_2.pin4
  N17: AD_IF_1.pin4, AD_switch1.pin4
  N18: AD_IF_4.pin3, D_IF_1.pin4, D_switch1.pin4
  N19: AD_IF_4.pin4, AD_IF_3.pin3, AD_switch4.pin4
  N20: AD_IF_3.pin4, AD_IF_2.pin3, AD_switch3.pin4
  N21: AD_switch1.pin0, LC.A0
  N22: AD_switch1.pin3, LC.B0
  N23: AD_switch2.pin0, LC.A1
  N24: AD_switch2.pin3, LC.B1
  N25: AD_switch4.pin0, LC.A3
  N26: AD_switch4.pin3, LC.B3
  N27: D_switch1.pin0, LC.A4
  N28: D_switch1.pin3, LC.B4
  N29: D_switch2.pin0, LC.A5
  N30: D_switch2.pin3, LC.B5
  N31: D_switch3.pin0, LC.A6
  N32: D_switch3.pin3, LC.B6
  N33: D_switch4.pin0, LC.A7
  N34: D_switch4.pin3, LC.B7
  N35: J1.pin2, LC.OE
  N36: AD_switch3.pin0, LC.A2
  N37: AD_switch3.pin3, LC.B2

custom parts:
  Akizuki slide switch IS-2235: Akizuki slide switch is-2235 (P-02627)
  M-04522: Akizuki 8bit bi-directional logic level converter M-04522
  M-04522: Akizuki 8bit bi-directional logic level converter M-04522
  Akizuki slide switch IS-2235: Akizuki slide switch is-2235 (P-02627)
  DeadOn RTC - DS3234 Breakout (for upside down): Description: Here is a real time clock based on the DS3234 Real Time Clock IC. The DS3234 is a low-cost, extremely accurate SPI bus real-time clock with an integrated temperature-compensated crystal oscillator and crystal. The RTC maintains seconds, minutes, hours, day, date, month, and year information. The date at the end of the month is automatically adjusted for months with fewer than 31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
  SparkFun - I2C/SPI-to-UART Breakout - SC16IS750: https://www.sparkfun.com/products/retired/9981
