# Fritzing sketch マイクロSD3V3シールド (saved by Fritzing 0.9.2b)
perfboards: 1

parts:
  IOL = female pin header, 8 pins [form="♀ (female)"]
  IOH = female pin header, 10 pins [form="♀ (female)"]
  AD = female pin header, 6 pins [form="♀ (female)"]  # not connected
  POWER = female pin header, 8 pins [form="♀ (female)"]
  ICSP = Arduino R3 6pin male header [package=THT]  # not connected
  SD1 = AE-MICRO-SD-DIP
  J1 = male pin header, 12 pins [form="♂ (male)"]
  Chip_select = male pin header, 12 pins [form="♂ (male)"]

nets:
  N1: IOL.pin1, J1.pin5
  N2: IOL.pin2, J1.pin6
  N3: IOL.pin3, J1.pin7
  N4: IOL.pin4, J1.pin8
  N5: IOL.pin5, J1.pin9
  N6: IOL.pin6, J1.pin10
  N7: IOL.pin7, J1.pin11
  N8: IOL.pin8, J1.pin12
  GND: IOH.pin4, POWER.pin6, POWER.pin7, SD1.GND
  SCLK: IOH.pin5, SD1.SCK
  MISO: IOH.pin6, SD1.MISO
  MOSI: IOH.pin7, SD1.MOSI
  N9: IOH.pin8, J1.pin1
  N10: IOH.pin9, J1.pin2
  N11: IOH.pin10, J1.pin3
  3.3V: POWER.pin4, SD1.VCC
  N12: SD1.CDA, SD1.NC0
  Chip Select: SD1.SS, Chip_select.pin1, Chip_select.pin2, Chip_select.pin3, Chip_select.pin4, Chip_select.pin5, Chip_select.pin6, Chip_select.pin7, Chip_select.pin8, Chip_select.pin9, Chip_select.pin10, Chip_select.pin11, Chip_select.pin12

custom parts:
  Arduino R3 6pin male header: Pin header for arduino R3
  AE-MICRO-SD-DIP: 秋月電子通商 K-05488
