# Fritzing sketch マイクロSD両用シールドMega (saved by Fritzing 0.9.2b)
perfboards: 1

parts:
  IO2 = female pin header, 8 pins [form="♀ (female)"]
  IO1 = female pin header, 10 pins [form="♀ (female)"]
  POWER = female pin header, 8 pins [form="♀ (female)"]
  microSD1 = MicroSD Breakout
  S2 = Akizuki slide switch IS-2235
  IO3 = female pin header, 8 pins [form="♀ (female)"]
  AD1 = female pin header, 8 pins [form="♀ (female)"]  # not connected
  AD2 = female pin header, 8 pins [form="♀ (female)"]  # not connected
  IO5 = female pin header, 18 pins [form="♀ (female)"]  # not connected
  IO4 = female pin header, 18 pins [form="♀ (female)"]  # not connected
  ICSP = Arduino R3 6pin male header [package=THT]
  J2 = male pin header, 24 pins [form="♂ (male)"]
  J3 = male pin header, 24 pins [form="♂ (male)"]
  Chip_select = male pin header, 24 pins [form="♂ (male)"]
  Card_detect = male pin header, 24 pins [form="♂ (male)"]

nets:
  N1: IO2.pin1, J2.pin8, J3.pin8
  N2: IO2.pin2, J2.pin9, J3.pin9
  N3: IO2.pin3, J2.pin10, J3.pin10
  N4: IO2.pin4, J2.pin11, J3.pin11
  N5: IO2.pin5, J2.pin12, J3.pin12
  N6: IO2.pin6, J2.pin13, J3.pin13
  N7: IO2.pin7, J2.pin14, J3.pin14
  N8: IO2.pin8, J2.pin15, J3.pin15
  GND: IO1.pin4, POWER.pin6, POWER.pin7, microSD1.GND
  N9: IO1.pin5, J2.pin1, J3.pin1
  N10: IO1.pin6, J2.pin2, J3.pin2
  N11: IO1.pin7, J2.pin3, J3.pin3
  N12: IO1.pin8, J2.pin4, J3.pin4
  N13: IO1.pin9, J2.pin5, J3.pin5
  N14: IO1.pin10, J2.pin6, J3.pin6
  N15: POWER.pin4, S2.pin5
  N16: POWER.pin5, S2.pin0
  Card detect: microSD1.CD, Card_detect.pin1, Card_detect.pin2, Card_detect.pin3, Card_detect.pin4, Card_detect.pin5, Card_detect.pin6, Card_detect.pin7, Card_detect.pin8, Card_detect.pin9, Card_detect.pin10, Card_detect.pin11, Card_detect.pin12, Card_detect.pin13, Card_detect.pin14, Card_detect.pin15, Card_detect.pin16, Card_detect.pin17, Card_detect.pin18, Card_detect.pin19, Card_detect.pin20, Card_detect.pin21, Card_detect.pin22, Card_detect.pin23, Card_detect.pin24
  Chip Select: microSD1.CS, Chip_select.pin1, Chip_select.pin2, Chip_select.pin3, Chip_select.pin4, Chip_select.pin5, Chip_select.pin6, Chip_select.pin7, Chip_select.pin8, Chip_select.pin9, Chip_select.pin10, Chip_select.pin11, Chip_select.pin12, Chip_select.pin13, Chip_select.pin14, Chip_select.pin15, Chip_select.pin16, Chip_select.pin17, Chip_select.pin18, Chip_select.pin19, Chip_select.pin20, Chip_select.pin21, Chip_select.pin22, Chip_select.pin23, Chip_select.pin24
  MOSI: microSD1.DI, ICSP.pin5
  MISO: microSD1.DO, ICSP.pin1
  SCLK: microSD1.CLK, ICSP.pin2
  N17: microSD1.3v, S2.pin4
  N18: microSD1.5V, S2.pin1
  N19: IO3.pin1, J2.pin17, J3.pin17
  N20: IO3.pin2, J2.pin18, J3.pin18
  N21: IO3.pin3, J2.pin19, J3.pin19
  N22: IO3.pin4, J2.pin20, J3.pin20
  N23: IO3.pin5, J2.pin21, J3.pin21
  N24: IO3.pin6, J2.pin22, J3.pin22
  N25: IO3.pin7, J2.pin23, J3.pin23
  N26: IO3.pin8, J2.pin24, J3.pin24

custom parts:
  MicroSD Breakout: 5V-ready microSD Breakout with Level Shifter
  Akizuki slide switch IS-2235: Akizuki slide switch is-2235 (P-02627)
  Arduino R3 6pin male header: Pin header for arduino R3
