# Fritzing sketch 相互接続Megaインターフェース (saved by Fritzing 0.9.2b)
perfboards: 1

parts:
  IO2 = female pin header, 8 pins [form="♀ (female)"]
  IO1 = female pin header, 10 pins [form="♀ (female)"]
  Power = female pin header, 8 pins [form="♀ (female)"]
  LevelConverter = Bi-Directional Logic Level Converter [part_number=BOB-12009]
  Signal_IN = Grove Header 4pin 90 degree direct mount [package="90 degree"]
  Power_IN = Grove Header 4pin 90 degree direct mount [package="90 degree"]
  ICSP = Arduino R3 6pin male header [package=THT]  # not connected
  IO5 = female pin header, 18 pins [form="♀ (female)"]  # not connected
  IO4 = female pin header, 18 pins [form="♀ (female)"]  # not connected
  ADH = female pin header, 8 pins [form="♀ (female)"]  # not connected
  ADL = female pin header, 8 pins [form="♀ (female)"]  # not connected
  J1 = male pin header, 24 pins [form="♂ (male)"]
  J2 = male pin header, 24 pins [form="♂ (male)"]
  J3 = male pin header, 24 pins [form="♂ (male)"]
  IO3 = female pin header, 8 pins [form="♀ (female)"]
  Tx = male pin header, 24 pins [form="♂ (male)"]
  Rx = male pin header, 24 pins [form="♂ (male)"]
  Shutdown = male pin header, 24 pins [form="♂ (male)"]

nets:
  N1: IO2.pin1, J1.pin8, J2.pin8, J3.pin8
  N2: IO2.pin2, J1.pin9, J2.pin9, J3.pin9
  N3: IO2.pin3, J1.pin10, J2.pin10, J3.pin10
  N4: IO2.pin4, J1.pin11, J2.pin11, J3.pin11
  N5: IO2.pin5, J1.pin12, J2.pin12, J3.pin12
  N6: IO2.pin6, J1.pin13, J2.pin13, J3.pin13
  N7: IO2.pin7, J1.pin14, J2.pin14, J3.pin14
  N8: IO2.pin8, J1.pin15, J2.pin15, J3.pin15
  GND: IO1.pin4, Power.pin6, Power.pin7, LevelConverter.GND, Power_IN.4
  N9: IO1.pin5, J1.pin1, J2.pin1, J3.pin1
  N10: IO1.pin6, J1.pin2, J2.pin2, J3.pin2
  N11: IO1.pin7, J1.pin3, J2.pin3, J3.pin3
  N12: IO1.pin8, J1.pin4, J2.pin4, J3.pin4
  N13: IO1.pin9, J1.pin5, J2.pin5, J3.pin5
  N14: IO1.pin10, J1.pin6, J2.pin6, J3.pin6
  N15: Power.pin3, LevelConverter.HV4
  N16: Power.pin5, LevelConverter.HV
  N17: Power.pin8, Power_IN.3
  N18: LevelConverter.LV1, Signal_IN.4
  N19: LevelConverter.LV2, Signal_IN.3
  3V3: LevelConverter.LV, Power_IN.2
  N20: LevelConverter.LV3, Signal_IN.2
  N21: LevelConverter.LV4, Signal_IN.1
  N22: LevelConverter.HV3, Shutdown.pin1, Shutdown.pin2, Shutdown.pin3, Shutdown.pin4, Shutdown.pin5, Shutdown.pin6, Shutdown.pin7, Shutdown.pin8, Shutdown.pin9, Shutdown.pin10, Shutdown.pin11, Shutdown.pin12, Shutdown.pin13, Shutdown.pin14, Shutdown.pin15, Shutdown.pin16, Shutdown.pin17, Shutdown.pin18, Shutdown.pin19, Shutdown.pin20, Shutdown.pin21, Shutdown.pin22, Shutdown.pin23, Shutdown.pin24
  N23: LevelConverter.HV2, Rx.pin1, Rx.pin2, Rx.pin3, Rx.pin4, Rx.pin5, Rx.pin6, Rx.pin7, Rx.pin8, Rx.pin9, Rx.pin10, Rx.pin11, Rx.pin12, Rx.pin13, Rx.pin14, Rx.pin15, Rx.pin16, Rx.pin17, Rx.pin18, Rx.pin19, Rx.pin20, Rx.pin21, Rx.pin22, Rx.pin23, Rx.pin24
  N24: LevelConverter.HV1, Tx.pin1, Tx.pin2, Tx.pin3, Tx.pin4, Tx.pin5, Tx.pin6, Tx.pin7, Tx.pin8, Tx.pin9, Tx.pin10, Tx.pin11, Tx.pin12, Tx.pin13, Tx.pin14, Tx.pin15, Tx.pin16, Tx.pin17, Tx.pin18, Tx.pin19, Tx.pin20, Tx.pin21, Tx.pin22, Tx.pin23, Tx.pin24
  N25: J1.pin17, J2.pin17, J3.pin17, IO3.pin1
  N26: J1.pin18, J2.pin18, J3.pin18, IO3.pin2
  N27: J1.pin19, J2.pin19, J3.pin19, IO3.pin3
  N28: J1.pin20, J2.pin20, J3.pin20, IO3.pin4
  N29: J1.pin21, J2.pin21, J3.pin21, IO3.pin5
  N30: J1.pin22, J2.pin22, J3.pin22, IO3.pin6
  N31: J1.pin23, J2.pin23, J3.pin23, IO3.pin7
  N32: J1.pin24, J2.pin24, J3.pin24, IO3.pin8

custom parts:
  Bi-Directional Logic Level Converter: Description: If you've ever tried to connect a 3.3V device to a 5V system, you know what a challenge it can be. The SparkFun bi-directional logic level converter is a small device that safely steps down 5V signals to 3.3V AND steps up 3.3V to 5V at the same time. This level converter also works with 2.8V and 1.8V devices. What really separates this Logic level converter from our previous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
  Grove Header 4pin 90 degree direct mount: Header
  Arduino R3 6pin male header: Pin header for arduino R3
