# Fritzing sketch 相互接続スイッチングリレーシールド (saved by Fritzing 0.9.2b)
perfboards: 1

parts:
  IOH = female pin header, 10 pins [form="♀ (female)"]
  J1 = male pin header, 15 pins [form="♂ (male)"]
  IOL = female pin header, 8 pins [form="♀ (female)"]
  Power = female pin header, 8 pins [form="♀ (female)"]
  AD = female pin header, 6 pins [form="♀ (female)"]  # not connected
  Tx = male pin header, 15 pins [form="♂ (male)"]
  J2 = male pin header, 15 pins [form="♂ (male)"]
  Rx = male pin header, 15 pins [form="♂ (male)"]
  RelayControl = male pin header, 15 pins [form="♂ (male)"]
  J5 = male pin header, 15 pins [form="♂ (male)"]
  J3 = male pin header, 15 pins [form="♂ (male)"]
  Shutdown = male pin header, 15 pins [form="♂ (male)"]
  J4 = male pin header, 15 pins [form="♂ (male)"]
  Reset = male pin header, 15 pins [form="♂ (male)"]
  Power_OUT = Grove Header 4pin 90 degree direct mount [package="90 degree"]
  Signal_OUT = Grove Header 4pin 90 degree direct mount [package="90 degree"]
  J6 = Arduino R3 6pin male header [package=THT]  # not connected
  Relay = RELAY-G6L [package=1P]
  R1 = Resistor [tolerance=±5% resistance=3k package=THT]
  R2 = Resistor [tolerance=±5% resistance=3k package=THT]
  2SC1815 = NPN-Transistor [package="TO92 [THT]"]
  D1 = Schottky Diode [part_number=1S4 breakdown_voltage=3.6V package="300 mil [THT]"]

nets:
  GND: IOH.pin4, Power.pin6, Power.pin7, Power_OUT.4, R2.Pin_0, 2SC1815.E
  N1: IOH.pin5, J1.pin1, J2.pin1, J5.pin1, J3.pin1, J4.pin1
  N2: IOH.pin6, J1.pin2, J2.pin2, J5.pin2, J3.pin2, J4.pin2
  N3: IOH.pin7, J1.pin3, J2.pin3, J5.pin3, J3.pin3, J4.pin3
  N4: IOH.pin8, J1.pin4, J2.pin4, J5.pin4, J3.pin4, J4.pin4
  N5: IOH.pin9, J1.pin5, J2.pin5, J5.pin5, J3.pin5, J4.pin5
  N6: IOH.pin10, J1.pin6, J2.pin6, J5.pin6, J3.pin6, J4.pin6
  N7: J1.pin8, IOL.pin1, J2.pin8, J5.pin8, J3.pin8, J4.pin8
  N8: J1.pin9, IOL.pin2, J2.pin9, J5.pin9, J3.pin9, J4.pin9
  N9: J1.pin10, IOL.pin3, J2.pin10, J5.pin10, J3.pin10, J4.pin10
  N10: J1.pin11, IOL.pin4, J2.pin11, J5.pin11, J3.pin11, J4.pin11
  N11: J1.pin12, IOL.pin5, J2.pin12, J5.pin12, J3.pin12, J4.pin12
  N12: J1.pin13, IOL.pin6, J2.pin13, J5.pin13, J3.pin13, J4.pin13
  N13: J1.pin14, IOL.pin7, J2.pin14, J5.pin14, J3.pin14, J4.pin14
  N14: J1.pin15, IOL.pin8, J2.pin15, J5.pin15, J3.pin15, J4.pin15
  3.3V: Power.pin4, Power_OUT.2, Relay.CIO#1, D1.cathode
  N15: Power.pin8, Relay.SIO#3
  N16: Tx.pin1, Tx.pin2, Tx.pin3, Tx.pin4, Tx.pin5, Tx.pin6, Tx.pin7, Tx.pin8, Tx.pin9, Tx.pin10, Tx.pin11, Tx.pin12, Tx.pin13, Tx.pin14, Tx.pin15, Signal_OUT.4
  N17: Rx.pin1, Rx.pin2, Rx.pin3, Rx.pin4, Rx.pin5, Rx.pin6, Rx.pin7, Rx.pin8, Rx.pin9, Rx.pin10, Rx.pin11, Rx.pin12, Rx.pin13, Rx.pin14, Rx.pin15, Signal_OUT.3
  RC: RelayControl.pin1, RelayControl.pin2, RelayControl.pin3, RelayControl.pin4, RelayControl.pin5, RelayControl.pin6, RelayControl.pin7, RelayControl.pin8, RelayControl.pin9, RelayControl.pin10, RelayControl.pin11, RelayControl.pin12, RelayControl.pin13, RelayControl.pin14, RelayControl.pin15, R1.Pin_0
  N18: Shutdown.pin1, Shutdown.pin2, Shutdown.pin3, Shutdown.pin4, Shutdown.pin5, Shutdown.pin6, Shutdown.pin7, Shutdown.pin8, Shutdown.pin9, Shutdown.pin10, Shutdown.pin11, Shutdown.pin12, Shutdown.pin13, Shutdown.pin14, Shutdown.pin15, Signal_OUT.2
  N19: Reset.pin1, Reset.pin2, Reset.pin3, Reset.pin4, Reset.pin5, Reset.pin6, Reset.pin7, Reset.pin8, Reset.pin9, Reset.pin10, Reset.pin11, Reset.pin12, Reset.pin13, Reset.pin14, Reset.pin15, Signal_OUT.1
  RAW: Power_OUT.3, Relay.SIO#0
  N20: Relay.CIO#2, 2SC1815.C, D1.anode
  N21: R1.Pin_1, R2.Pin_1, 2SC1815.B

custom parts:
  Grove Header 4pin 90 degree direct mount: Header
  Arduino R3 6pin male header: Pin header for arduino R3
  RELAY-G6L: OMRON G6L
