# Fritzing sketch Xbeeホスト基板(昇圧電源) (saved by Fritzing 0.9.2b)
perfboards: 1

parts:
  Reset = Momentary Switch [package=ksa_sealed_tac_switch]
  IOL = female pin header, 8 pins [form="♀ (female)"]
  IOH = female pin header, 10 pins [form="♀ (female)"]
  AD = female pin header, 6 pins [form="♀ (female)"]
  Power = female pin header, 8 pins [form="♀ (female)"]
  J1 = male pin header, 3 pins [form="♂ (male)"]
  Vol = Trimmer Potentiometer [maximum_resistance=0.1MΩ package=THT]
  J2 = Arduino R3 6pin male header [package=THT]  # not connected
  AE-MOD1 = AE-XCL101C331BR-G
  Xbee1 = SSCI-KIT-XBSOCKET
  Power_plug2 = Power plug
  D1 = Rectifier Diode [part_number=1N4001 package="300 mil [THT]"]
  R2 = Resistor [tolerance=±5% resistance=10k package=THT]

nets:
  N1: Reset.1, D1.anode, R2.Pin_0
  RST: Reset.2, Power.pin3, Xbee1.pin5
  GND: Reset.3, IOH.pin4, Power.pin6, Power.pin7, J1.pin3, Vol.leg2, AE-MOD1.VSS, Xbee1.GND, Power_plug2.GND
  CTS: IOL.pin1, Xbee1.pin12
  N2: IOL.pin2, Xbee1.pin16
  N3: IOL.pin3, Xbee1.pin15
  DIO4: IOL.pin4, Xbee1.pin11
  N4: IOL.pin5, Xbee1.pin13
  Tx: IOL.pin7, Xbee1.pin2
  Rx: IOL.pin8, Xbee1.pin3
  N5: IOH.pin6, Xbee1.pin4
  DIO11: IOH.pin7, Xbee1.pin7
  N6: IOH.pin8, Xbee1.pin6
  N7: IOH.pin10, Xbee1.pin9
  N8: AD.pin1, Xbee1.pin20
  N9: AD.pin2, Xbee1.pin19
  N10: AD.pin3, Xbee1.pin18
  N11: AD.pin4, Xbee1.pin17
  3.3V: Power.pin4, Vol.leg1, AE-MOD1.Vout, Xbee1.VCC, D1.cathode, R2.Pin_1
  VIN: Power.pin8, AE-MOD1.Vbat, AE-MOD1.CE, Power_plug2.VCC
  N12: J1.pin1, Vol.wiper
  VREF: J1.pin2, Xbee1.pin14

custom parts:
  Arduino R3 6pin male header: Pin header for arduino R3
  SSCI-KIT-XBSOCKET: Xbee pin conversion
  Power plug: 秋月電子通商 AE-DCJACK-DIPKIT-2.1mm-10A(通販コードK-06998)とその互換品(K06999,K-08415,K-08416)
