# Fritzing sketch Xbeeホスト基板(降圧電源) (saved by Fritzing 0.9.2b)
perfboards: 1

parts:
  Reset = Momentary Switch [package=ksa_sealed_tac_switch]
  IOL = female pin header, 8 pins [form="♀ (female)"]
  IOH = female pin header, 10 pins [form="♀ (female)"]
  AD = female pin header, 6 pins [form="♀ (female)"]
  Power = female pin header, 8 pins [form="♀ (female)"]
  J1 = male pin header, 3 pins [form="♂ (male)"]
  Vol = Trimmer Potentiometer [maximum_resistance=0.1MΩ package=THT]
  J6 = Arduino R3 6pin male header [package=THT]  # not connected
  AE-MOD1 = AE-LXDC55-3.3V-Down
  Power_plug1 = Power plug
  Xbee1 = SSCI-KIT-XBSOCKET
  D1 = Rectifier Diode [part_number=1N4001 package="300 mil [THT]"]
  R2 = Resistor [tolerance=±5% resistance=10k package=THT]

nets:
  N1: Reset.1, D1.anode, R2.Pin_0
  RST: Reset.2, Power.pin3, Xbee1.pin5
  GND: Reset.3, IOH.pin4, Power.pin6, Power.pin7, J1.pin3, Vol.leg2, AE-MOD1.GND, Power_plug1.GND, Xbee1.GND
  N2: IOL.pin1, Xbee1.pin12
  N3: IOL.pin2, Xbee1.pin16
  N4: IOL.pin3, Xbee1.pin15
  N5: IOL.pin4, Xbee1.pin11
  N6: IOL.pin5, Xbee1.pin13
  Tx: IOL.pin7, Xbee1.pin2
  Rx: IOL.pin8, Xbee1.pin3
  N7: IOH.pin6, Xbee1.pin4
  N8: IOH.pin7, Xbee1.pin7
  N9: IOH.pin8, Xbee1.pin6
  N10: IOH.pin10, Xbee1.pin9
  N11: AD.pin1, Xbee1.pin20
  N12: AD.pin2, Xbee1.pin19
  N13: AD.pin3, Xbee1.pin18
  N14: AD.pin4, Xbee1.pin17
  3.3V: Power.pin4, Vol.leg1, AE-MOD1.OUT, Xbee1.VCC, D1.cathode, R2.Pin_1
  VIN: Power.pin8, AE-MOD1.IN, Power_plug1.VCC
  N15: J1.pin1, Vol.wiper
  VREF: J1.pin2, Xbee1.pin14

custom parts:
  Arduino R3 6pin male header: Pin header for arduino R3
  AE-LXDC55-3.3V-Down: AE-LXDC55-3.3V upside down
  Power plug: 秋月電子通商 AE-DCJACK-DIPKIT-2.1mm-10A(通販コードK-06998)とその互換品(K06999,K-08415,K-08416)
  SSCI-KIT-XBSOCKET: Xbee pin conversion
