# Fritzing sketch DHTシールド (saved by Fritzing 0.9.2b)
perfboards: 1

parts:
  AD = female pin header, 6 pins [form="♀ (female)"]  # not connected
  Power = female pin header, 8 pins [form="♀ (female)"]
  IOL = female pin header, 8 pins [form="♀ (female)"]
  IOH = female pin header, 10 pins [form="♀ (female)"]
  DHT1 = DHT11 Humitidy and Temperature Sensor
  R1 = Resistor [tolerance=±5% resistance=10k package=THT]
  J1 = male pin header, 15 pins [form="♂ (male)"]
  J2 = male pin header, 15 pins [form="♂ (male)"]

nets:
  3.3V: Power.pin4, DHT1.VDD, R1.Pin_1
  GND: Power.pin6, Power.pin7, IOH.pin4, DHT1.GND
  N1: IOL.pin1, J2.pin8
  N2: IOL.pin2, J2.pin9
  N3: IOL.pin3, J2.pin10
  N4: IOL.pin4, J2.pin11
  N5: IOL.pin5, J2.pin12
  N6: IOL.pin6, J2.pin13
  N7: IOL.pin7, J2.pin14
  N8: IOL.pin8, J2.pin15
  N9: IOH.pin5, J2.pin1
  MISO: IOH.pin6, J2.pin2
  N10: IOH.pin7, J2.pin3
  N11: IOH.pin8, J2.pin4
  Chip select: IOH.pin9, J2.pin5
  N12: IOH.pin10, J2.pin6
  N13: DHT1.DATA, R1.Pin_0, J1.pin1, J1.pin2, J1.pin3, J1.pin4, J1.pin5, J1.pin6, J1.pin7, J1.pin8, J1.pin9, J1.pin10, J1.pin11, J1.pin12, J1.pin13, J1.pin14, J1.pin15

custom parts:
  DHT11 Humitidy and Temperature Sensor: DHT11 Humidity and Temperature Sensor
