# Fritzing sketch grove DHTシールド (saved by Fritzing 0.9.3b)
stripboards: 1

parts:
  JP3 = Grove Header 4pin Straight direct mount [package=straight]
  DHT1 = DHT11 Humitidy and Temperature Sensor
  R1 = Resistor [tolerance=±5% resistance=10k package=THT]

nets:
  N1: JP3.1, DHT1.GND
  N2: JP3.2, DHT1.VDD, R1.Pin_0
  N3: JP3.3, DHT1.NULL
  N4: JP3.4, DHT1.DATA, R1.Pin_1

custom parts:
  Grove Header 4pin Straight direct mount: Header
  DHT11 Humitidy and Temperature Sensor: DHT11 Humidity and Temperature Sensor
