# Fritzing sketch grove RGB LEDシールド (saved by Fritzing 0.9.3b)
stripboards: 1

parts:
  JP3 = Grove Header 4pin Straight direct mount [package=straight]
  LED2 = RGB LED PL9823 F5 [package="5 mm [THT]"]
  C1 = Ceramic Capacitor [capacitance=0.1nF voltage=50V package="100 mil [THT, multilayer]"]
  R1 = Resistor [tolerance=±5% resistance=100 package=THT]

nets:
  N1: JP3.1, LED2.GND, C1.1
  N2: JP3.2, R1.Pin_0
  N3: JP3.4, LED2.DIN
  N4: LED2.VDD, C1.0, R1.Pin_1

custom parts:
  Grove Header 4pin Straight direct mount: Header
  RGB LED PL9823 F5: A 5mm tri-color LED with red, green and blue inside. this led includes WS2811 controller.
