# Fritzing sketch アナログ抵抗分圧(半固定抵抗) (saved by Fritzing 0.9.2b)
stripboards: 1

parts:
  Host = Grove Header 4pin Straight direct mount [package=straight]
  Sensor = Grove Header 4pin Straight direct mount [package=straight]
  R1 = Trimmer Potentiometer [maximum_resistance=10kΩ package=THT]

nets:
  GND: Host.1, Sensor.1, R1.leg1
  VDD: Host.2, Sensor.2
  N1: Host.4, R1.wiper
  N2: Sensor.4, R1.leg2

custom parts:
  Grove Header 4pin Straight direct mount: Header
