# Fritzing sketch アナログ抵抗分圧5V (saved by Fritzing 0.9.2b)
stripboards: 1

parts:
  Host = Grove Header 4pin Straight direct mount [package=straight]
  R3 = Resistor [tolerance=±5% resistance=15k package=THT]
  R4 = Resistor [tolerance=±5% resistance=47k package=THT]
  Sensor = Grove Header 4pin Straight direct mount [package=straight]
  R5 = Resistor [tolerance=±5% resistance=15k package=THT]
  R6 = Resistor [tolerance=±5% resistance=47k package=THT]

nets:
  GND: Host.1, R3.Pin_1, Sensor.1, R5.Pin_1
  VDD: Host.2, Sensor.2
  N1: Host.3, R5.Pin_0, R6.Pin_0
  N2: Host.4, R3.Pin_0, R4.Pin_0
  N3: R4.Pin_1, Sensor.4
  N4: Sensor.3, R6.Pin_1

custom parts:
  Grove Header 4pin Straight direct mount: Header
