# Fritzing sketch リードスイッチシールド (saved by Fritzing 0.9.3b)
stripboards: 1

parts:
  JP3 = Grove Header 4pin Straight direct mount [package=straight]
  リードスイッチ = Reed switch [package=THT]
  R1 = Resistor [tolerance=±5% resistance=10k package=THT]

nets:
  N1: JP3.1, R1.Pin_1
  N2: JP3.2, リードスイッチ.pin_2
  N3: JP3.4, リードスイッチ.pin_1, R1.Pin_0

custom parts:
  Grove Header 4pin Straight direct mount: Header
